// Logisim project cpu24.circ as structural Verilog: 26 circuits, main circuit ◇单周期MIPS
module \单周期MIPS  (
  output RegWrite,
  output MemWrite,
  output [31:0] PC,
  output [31:0] IR,
  output [31:0] RDin,
  output [31:0] MDin,
  output [31:0] LedData
);

  wire and_2_out, and_3_out, Beq, beq_bne_suc, BGTZ, bgtz_suc, Bne, CLK, comparator_2_eq, equal, Go, IR1,
       IR2, IR3, isI, isJ, isRTYPE, JAL, JMP, JR, LB, not_1_out, not_2_out, or_1_out, or_3_out, or_4_out,
       or_5_out, pause, SignedExt, stop, Syscall, W1, W2, W3, \单周期硬布线控制器_1_alu_src , \单周期硬布线控制器_1_memtoreg ,
       \单周期硬布线控制器_1_regdst ;
  wire [1:0] index, \确定pc_1_out_7 ;
  wire [3:0] \单周期硬布线控制器_1_alu_op ;
  wire [4:0] multiplexer_3_out, multiplexer_4_out, multiplexer_5_out, multiplexer_6_out, multiplexer_10_out;
  wire [7:0] LBans;
  wire [15:0] \总周期数 , \无条件分支数 , \条件分支成功数 ;
  wire [27:0] nextpc;
  wire [31:0] bit_extender_1_out, bit_extender_2_out, multiplexer_1_out, multiplexer_2_out,
       multiplexer_8_out, multiplexer_9_out, multiplexer_12_out, pcbranch, R1data, ram_1_data, shifter_1_out;
  wire [31:2] mips_alu_1_result;
  wire [31:28] jmppc;

  Clock #(.highDuration(1), .lowDuration(1)) clock_1 (.out(CLK));
  Button _1 (.out(IR1));
  Button _2 (.out(IR2));
  Button _3 (.out(IR3));
  Button \u_继续运行  (.out(Go));
  LED #(.active("true")) led_1 (.in(W1));
  LED #(.active("true")) led_2 (.in(W2));
  LED #(.active("true")) led_3 (.in(W3));
  or or_1 (or_1_out, JMP, JAL);
  Hex_Digit_Display hex_digit_display_1 (.value(LedData[31:28]));  // open: dp
  \确定pc  \u_确定pc_1  (
    .equal(equal), .Beq(Beq), .Bne(Bne), .JR(JR), .j(or_1_out), .out_7(\确定pc_1_out_7 ),
    .beq_bne_suc(beq_bne_suc));
  and and_1 (bgtz_suc, BGTZ, not_1_out);
  Multiplexer #(.select(2), .width(32), .disabled("Z"), .enable("false")) multiplexer_1 (
    .in0(pcbranch), .in1({jmppc, nextpc}), .in2(R1data), .in3({jmppc, IR[25:0], 2'b00}),
    .out(multiplexer_1_out), .sel(\确定pc_1_out_7 ));
  D_Flip_Flop #(.trigger("falling"), .Pre_Clr_Positions("ABOVE_BELOW"), .NegatePresetClear("false"), .enable("false"), .NewFFLayout("true")) d_ff_1 (
    .clk(CLK), .D(pause), .Qn(stop), .reset(Go));  // open: Q, preset
  Hex_Digit_Display hex_digit_display_2 (.value(LedData[23:20]));  // open: dp
  Hex_Digit_Display hex_digit_display_3 (.value(LedData[27:24]));  // open: dp
  not not_1 (not_1_out, RDin[0]);
  Multiplexer #(.select(1), .width(32), .disabled("Z"), .enable("false")) multiplexer_2 (
    .in0(multiplexer_1_out), .in1(pcbranch), .out(multiplexer_2_out), .sel(bgtz_suc));
  Register #(.width(32), .trigger("rising"), .Select("low")) u_PC (
    .D(multiplexer_2_out), .en(stop), .Q(PC), .clk(CLK));  // open: clr
  Hex_Digit_Display hex_digit_display_4 (.value(LedData[15:12]));  // open: dp
  Hex_Digit_Display hex_digit_display_5 (.value(LedData[19:16]));  // open: dp
  Hex_Digit_Display hex_digit_display_6 (.value(LedData[11:8]));  // open: dp
  Hex_Digit_Display hex_digit_display_7 (.value(LedData[7:4]));  // open: dp
  // Probe on \总周期数 
  Adder #(.width(32)) adder_1 (.a(PC), .b(32'h4), .out({jmppc, nextpc}));  // open: cin, cout
  Hex_Digit_Display hex_digit_display_8 (.value(LedData[3:0]));  // open: dp
  Counter #(.width(16), .max('hffff), .ongoal("wrap"), .trigger("rising"), .behavior("new")) counter_1 (
    .count(stop), .Q(\总周期数 ), .clk(CLK));  // open: load, D, carry, clr, preset, down
  Comparator #(.width(6), .mode("unsigned")) comparator_1 (.a({6{1'b0}}), .b(IR[31:26]), .eq(isRTYPE));  // open: gt, lt
  ROM #(.addrWidth(10), .dataWidth(32), .Select("high")) rom_1 (.addr(PC[11:2]), .data(IR));
  \单周期硬布线控制器  \u_单周期硬布线控制器_1  (
    .Func(IR[5:0]), .OP(IR[31:26]), .ALU_OP(\单周期硬布线控制器_1_alu_op ), .MemToReg(\单周期硬布线控制器_1_memtoreg ),
    .MemWrite(MemWrite), .ALU_SRC(\单周期硬布线控制器_1_alu_src ), .RegWrite(RegWrite), .SysCALL(Syscall),
    .SignedExt(SignedExt), .RegDst(\单周期硬布线控制器_1_regdst ), .JR(JR), .JMP(JMP), .Beq(Beq), .JAL(JAL),
    .Bne(Bne), .BGTZ(BGTZ), .LB(LB));
  Multiplexer #(.select(1), .width(5), .disabled("Z"), .enable("false")) multiplexer_3 (
    .in0(IR[20:16]), .in1(IR[15:11]), .out(multiplexer_3_out), .sel(\单周期硬布线控制器_1_regdst ));
  Multiplexer #(.select(1), .width(5), .disabled("Z"), .enable("false")) multiplexer_4 (
    .in0(multiplexer_3_out), .in1({5{1'b1}}), .out(multiplexer_4_out), .sel(JAL));
  and and_2 (and_2_out, SignedExt, IR[15]);
  Comparator #(.width(32), .mode("unsigned")) comparator_2 (
    .a(MDin), .b(32'h22), .eq(comparator_2_eq));  // open: gt, lt
  Multiplexer #(.select(1), .width(5), .disabled("Z"), .enable("false")) multiplexer_5 (
    .in0(IR[25:21]), .in1(5'b00100), .out(multiplexer_5_out), .sel(Syscall));
  Multiplexer #(.select(1), .width(5), .disabled("Z"), .enable("false")) multiplexer_6 (
    .in0(IR[20:16]), .in1(5'b00010), .out(multiplexer_6_out), .sel(Syscall));
  assign bit_extender_1_out = {{16{and_2_out}}, IR[15:0]};  // Bit_Extender bit_extender_1
  Multiplexer #(.select(1), .width(32), .disabled("Z"), .enable("false")) multiplexer_7 (
    .in0(multiplexer_9_out), .in1({jmppc, nextpc}), .out(RDin), .sel(JAL));
  not not_2 (not_2_out, comparator_2_eq);
  // Mips_Probe mips_probe_1: pin names not known; wires that end beside it: IR
  MIPS_Regifile mips_regifile_1 (
    .Din(RDin), .Clk(CLK), .R1(R1data), .R2(MDin), .WE(RegWrite), .W_num(multiplexer_4_out),
    .R1_num(multiplexer_5_out), .R2_num(multiplexer_6_out));
  Shifter #(.width(32), .shift("ll")) shifter_1 (.in(bit_extender_1_out), .\dist (5'b00010), .out(shifter_1_out));
  and and_3 (and_3_out, Syscall, comparator_2_eq);
  and and_4 (pause, Syscall, not_2_out);
  Multiplexer #(.select(1), .width(32), .disabled("Z"), .enable("false")) multiplexer_8 (
    .in0(MDin), .in1(bit_extender_1_out), .out(multiplexer_8_out), .sel(\单周期硬布线控制器_1_alu_src ));
  Multiplexer #(.select(1), .width(32), .disabled("Z"), .enable("false")) multiplexer_9 (
    .in0(multiplexer_12_out), .in1(bit_extender_2_out), .out(multiplexer_9_out), .sel(LB));
  or or_2 (isJ, JMP, JAL);
  or or_3 (or_3_out, isJ, isRTYPE, Syscall);
  Multiplexer #(.select(1), .width(5), .disabled("Z"), .enable("false")) multiplexer_10 (
    .in0({5{1'b0}}), .in1(IR[10:6]), .out(multiplexer_10_out), .sel(isRTYPE));
  Adder #(.width(32)) adder_2 (.a(shifter_1_out), .b({jmppc, nextpc}), .out(pcbranch));  // open: cin, cout
  Register #(.width(32), .trigger("rising"), .Select("low")) register_1 (
    .D(R1data), .en(and_3_out), .Q(LedData), .clk(CLK));  // open: clr
  not not_3 (isI, or_3_out);
  MIPS_ALU mips_alu_1 (
    .X(R1data), .Y(multiplexer_8_out), .AluOP(\单周期硬布线控制器_1_alu_op ), .Equal(equal),
    .Result({mips_alu_1_result, index}), .shamt(multiplexer_10_out));  // open: Result_2
  assign bit_extender_2_out = {{24{multiplexer_12_out[31]}}, LBans};  // Bit_Extender bit_extender_2
  RAM #(.addrWidth(10), .dataWidth(32), .bus("separate"), .Select("high")) ram_1 (
    .addr(mips_alu_1_result[11:2]), .din(MDin), .data(ram_1_data), .str(MemWrite), .clk(CLK));  // open: sel, ld, clr
  Multiplexer #(.select(2), .width(8), .disabled("Z"), .enable("false")) multiplexer_11 (
    .in0(multiplexer_12_out[7:0]), .in1(multiplexer_12_out[15:8]), .in2(multiplexer_12_out[23:16]),
    .in3(multiplexer_12_out[31:24]), .out(LBans), .sel(index));
  Counter #(.width(16), .max('hffff), .ongoal("wrap"), .trigger("rising"), .behavior("old")) counter_2 (
    .count(or_4_out), .Q(\条件分支成功数 ), .clk(CLK));  // open: load, D, carry, clr, preset
  or or_4 (or_4_out, beq_bne_suc, bgtz_suc);
  Counter #(.width(16), .max('hffff), .ongoal("wrap"), .trigger("rising"), .behavior("old")) counter_3 (
    .count(or_5_out), .Q(\无条件分支数 ), .clk(CLK));  // open: load, D, carry, clr, preset
  or or_5 (or_5_out, JMP, JR, JAL);
  Multiplexer #(.select(1), .width(32), .disabled("Z"), .enable("false")) multiplexer_12 (
    .in0({mips_alu_1_result, index}), .in1(ram_1_data), .out(multiplexer_12_out), .sel(\单周期硬布线控制器_1_memtoreg ));

  // Other names for the same wires on the sheet: address[25:0] = IR[25:0]; jmppc[27:2] = IR[25:0];
  //   shamt[4:0] = IR[10:6]; nextpc[31:28] = jmppc; R2data[31:0] = MDin

  // Notes on the sheet:
  //   中断源
  //   中断等待指示
  //   总复位信号应将除ROM以外所有存储组件全部清零
  //   数码管输出
  //   数码管输出应该用寄存器锁存，否则显示数据只能一闪而过
  //   指令存储器
  //   指令字
  //   contents of rom_1 (hex, n*v repeats v):
  //   20110005 8100006 20110001 20120002 20130003 20140004 810000b 20110001 20120002 20130003 20140004
  //   8100010 20110001 20120002 20130003 20140004 8100015 20110001 20120002 20130003 20140004 810001a
  //   20110001 20120002 20130003 20140004 810001f 20110001 20120002 20130003 20140004 8100024 20110001
  //   20120002 20130003 20140004 8100029 20110001 20120002 20130003 20140004 2231ffff 1620ffe0 20100001
  //   201200ff 20110001 20130003 12120005 12100004 20110001 20120002 20130003 20140004 16310004 16320003
  //   20110001 20120002 20130003 c10003d 2002000a c 20100000 22100001 102020 20020022 c 3e00008
  //   rd
  //   JMP
  //   JR
  //   OP
  //   OP
  //   Func
  //   Func
  //   rs
  //   rt
  //   rd
  //   Beq
  //   Bne
  //   MemToReg
  //   MemWrite
  //   AluOP
  //   AluSrcB
  //   RegWrite
  //   JAL
  //   RegDst
  //   Syscall
  //   为方便自动评测，需要输出PC，IR，寄存器文件写入端口RDin，内存写入端口MDin等信号
  //   j型指令
  //   I型指令
endmodule

// 单周期硬布线控制器
module \单周期硬布线控制器  (
  input  [5:0] OP,
  input  [5:0] Func,
  output [3:0] ALU_OP,
  output MemToReg,
  output MemWrite,
  output ALU_SRC,
  output RegWrite,
  output SysCALL,
  output SignedExt,
  output RegDst,
  output Beq,
  output Bne,
  output JR,
  output JMP,
  output JAL,
  output BGTZ,
  output LB
);

  \运算控制器自动生成  \u_运算控制器自动生成_1  (
    .OP0(OP[0]), .OP1(OP[1]), .OP2(OP[2]), .OP3(OP[3]), .OP4(OP[4]), .OP5(OP[5]), .F0(Func[0]), .F1(Func[1]),
    .F2(Func[2]), .F3(Func[3]), .F4(Func[4]), .F5(Func[5]), .S0(ALU_OP[0]), .S1(ALU_OP[1]), .S2(ALU_OP[2]),
    .S3(ALU_OP[3]));
  \控制信号自动生成  \u_控制信号自动生成_1  (
    .OP0(OP[0]), .OP1(OP[1]), .OP2(OP[2]), .OP3(OP[3]), .OP4(OP[4]), .OP5(OP[5]), .F0(Func[0]), .F1(Func[1]),
    .F2(Func[2]), .F3(Func[3]), .F4(Func[4]), .F5(Func[5]), .MemToReg(MemToReg), .MemWrite(MemWrite),
    .ALU_SRC(ALU_SRC), .RegWrite(RegWrite), .SysCALL(SysCALL), .SignedExt(SignedExt), .RegDst(RegDst),
    .BEQ(Beq), .BNE(Bne), .JR(JR), .JUMP(JMP), .JAL(JAL), .BGTZ(BGTZ), .LB(LB));

  // Other names for the same wires on the sheet: OP_CODE[5:0] = OP

  // Notes on the sheet:
  //   运算器控制器，根据指令生成运算器功能选择信号
  //   控制信号生成，产生数据通路需要的其他控制信号
endmodule

// 运算器控制器
module \运算控制器自动生成  (
  input  OP0,
  input  OP1,
  input  OP2,
  input  OP3,
  input  OP4,
  input  OP5,
  input  F0,
  input  F1,
  input  F2,
  input  F3,
  input  F4,
  input  F5,
  output S0,
  output S1,
  output S2,
  output S3
);

  wire and_1_out, and_2_out, and_3_out, and_4_out, and_5_out, and_6_out, and_7_out, and_8_out, and_9_out,
       and_10_out, and_11_out, and_12_out, and_13_out, and_14_out, and_15_out, and_16_out, and_17_out,
       and_18_out, and_19_out, and_20_out, and_21_out, and_22_out, and_23_out, and_24_out, and_25_out,
       and_26_out, and_27_out, and_28_out, and_29_out, and_30_out, and_31_out, and_32_out, and_33_out,
       and_34_out, and_35_out, and_36_out, and_37_out, and_38_out, and_39_out, and_40_out, and_41_out,
       and_42_out, and_43_out, and_44_out, and_45_out, and_46_out, and_47_out, and_48_out, and_49_out,
       not_1_out, not_2_out, not_3_out, not_4_out, not_5_out, not_6_out, not_7_out, not_8_out, not_9_out,
       not_10_out, not_11_out, not_12_out, not_13_out, not_14_out, not_15_out, not_16_out, not_17_out,
       not_18_out, not_19_out, not_20_out, not_21_out, not_22_out, not_23_out, not_24_out, not_25_out,
       not_26_out, not_27_out, not_28_out, not_29_out, not_30_out, not_31_out, not_32_out, not_33_out,
       not_34_out, not_35_out, not_36_out, not_37_out, not_38_out, not_39_out, not_40_out, not_41_out,
       not_42_out, not_43_out, not_44_out, not_45_out, not_46_out, not_47_out, not_48_out, not_49_out,
       not_50_out, not_51_out, not_52_out, not_53_out, not_54_out, not_55_out, not_56_out, not_57_out,
       not_58_out, not_59_out, not_60_out, not_61_out, not_62_out, not_63_out, not_64_out, not_65_out,
       not_66_out, not_67_out, not_68_out, not_69_out, not_70_out, not_71_out, not_72_out, not_73_out,
       not_74_out, not_75_out, not_76_out, not_77_out, not_78_out, not_79_out, not_80_out, not_81_out,
       not_82_out, not_83_out, not_84_out, not_85_out, not_86_out, not_87_out, not_88_out, not_89_out,
       not_90_out, not_91_out, not_92_out, not_93_out, not_94_out, not_95_out, not_96_out, not_97_out,
       not_98_out, not_99_out, not_100_out, not_101_out, not_102_out, not_103_out, not_104_out, not_105_out,
       not_106_out, not_107_out, not_108_out, not_109_out, not_110_out, not_111_out, not_112_out,
       not_113_out, not_114_out, not_115_out, not_116_out, not_117_out, not_118_out, not_119_out,
       not_120_out, not_121_out, not_122_out, not_123_out, not_124_out, not_125_out, not_126_out,
       not_127_out, not_128_out, not_129_out, not_130_out, not_131_out, not_132_out, not_133_out,
       not_134_out, not_135_out, not_136_out, not_137_out, not_138_out, not_139_out, not_140_out,
       not_141_out, not_142_out, not_143_out, not_144_out, not_145_out, not_146_out, not_147_out,
       not_148_out, not_149_out, not_150_out, not_151_out, not_152_out, not_153_out, not_154_out,
       not_155_out, not_156_out, not_157_out, not_158_out, not_159_out, not_160_out, not_161_out,
       not_162_out, not_163_out, not_164_out, not_165_out, not_166_out, not_167_out, not_168_out,
       not_169_out, not_170_out, not_171_out, not_172_out, not_173_out, not_174_out, not_175_out,
       not_176_out, not_177_out, not_178_out, not_179_out, not_180_out, not_181_out, not_182_out,
       not_183_out, not_184_out, not_185_out, not_186_out, not_187_out, not_188_out, not_189_out,
       not_190_out, not_191_out, not_192_out, not_193_out, not_194_out, not_195_out, not_196_out,
       not_197_out, not_198_out, not_199_out, not_200_out, not_201_out, not_202_out, not_203_out,
       not_204_out, not_205_out, not_206_out, not_207_out, not_208_out, not_209_out, not_210_out,
       not_211_out, not_212_out, not_213_out, not_214_out, not_215_out, not_216_out, not_217_out,
       not_218_out, not_219_out, not_220_out, not_221_out, not_222_out, not_223_out, not_224_out,
       not_225_out, not_226_out, not_227_out, not_228_out, not_229_out, not_230_out, not_231_out,
       not_232_out, not_233_out, not_234_out, not_235_out, not_236_out, not_237_out, not_238_out,
       not_239_out, not_240_out, not_241_out, not_242_out, not_243_out, not_244_out, not_245_out,
       not_246_out, not_247_out, not_248_out, not_249_out, not_250_out, not_251_out, not_252_out,
       not_253_out, not_254_out, not_255_out, not_256_out, not_257_out, not_258_out, not_259_out,
       not_260_out, not_261_out, not_262_out, not_263_out, not_264_out, not_265_out, not_266_out,
       not_267_out, not_268_out, not_269_out, not_270_out, not_271_out, not_272_out, not_273_out,
       not_274_out, not_275_out, not_276_out, not_277_out, not_278_out, not_279_out, not_280_out,
       not_281_out, not_282_out, not_283_out, not_284_out, not_285_out, not_286_out, not_287_out,
       not_288_out, not_289_out, not_290_out, not_291_out, not_292_out, not_293_out, not_294_out,
       not_295_out, not_296_out, not_297_out, not_298_out, not_299_out, not_300_out, not_301_out,
       not_302_out, not_303_out, not_304_out, not_305_out, not_306_out;

  not not_1 (not_1_out, OP5);
  not not_2 (not_2_out, OP4);
  not not_3 (not_3_out, OP3);
  not not_4 (not_4_out, OP2);
  not not_5 (not_5_out, OP1);
  not not_6 (not_6_out, OP0);
  not not_7 (not_7_out, F5);
  not not_8 (not_8_out, F4);
  not not_9 (not_9_out, F3);
  not not_10 (not_10_out, F2);
  not not_11 (not_11_out, OP5);
  not not_12 (not_12_out, OP4);
  not not_13 (not_13_out, OP3);
  not not_14 (not_14_out, OP2);
  not not_15 (not_15_out, OP1);
  not not_16 (not_16_out, OP0);
  not not_17 (not_17_out, F4);
  not not_18 (not_18_out, F3);
  not not_19 (not_19_out, F2);
  not not_20 (not_20_out, F1);
  not not_21 (not_21_out, F0);
  not not_22 (not_22_out, OP5);
  not not_23 (not_23_out, OP4);
  not not_24 (not_24_out, OP3);
  not not_25 (not_25_out, OP2);
  not not_26 (not_26_out, OP1);
  not not_27 (not_27_out, OP0);
  not not_28 (not_28_out, F4);
  not not_29 (not_29_out, F3);
  not not_30 (not_30_out, F2);
  not not_31 (not_31_out, F1);
  not not_32 (not_32_out, OP5);
  not not_33 (not_33_out, OP4);
  not not_34 (not_34_out, OP3);
  not not_35 (not_35_out, OP2);
  not not_36 (not_36_out, OP1);
  not not_37 (not_37_out, OP0);
  not not_38 (not_38_out, F4);
  not not_39 (not_39_out, F3);
  not not_40 (not_40_out, F1);
  not not_41 (not_41_out, F0);
  not not_42 (not_42_out, OP5);
  not not_43 (not_43_out, OP4);
  not not_44 (not_44_out, OP3);
  not not_45 (not_45_out, OP2);
  not not_46 (not_46_out, OP1);
  not not_47 (not_47_out, OP0);
  not not_48 (not_48_out, F4);
  not not_49 (not_49_out, F2);
  not not_50 (not_50_out, F0);
  not not_51 (not_51_out, OP5);
  not not_52 (not_52_out, OP4);
  not not_53 (not_53_out, OP3);
  not not_54 (not_54_out, OP1);
  not not_55 (not_55_out, OP0);
  not not_56 (not_56_out, OP5);
  not not_57 (not_57_out, OP4);
  not not_58 (not_58_out, OP3);
  not not_59 (not_59_out, OP1);
  not not_60 (not_60_out, OP5);
  not not_61 (not_61_out, OP4);
  not not_62 (not_62_out, OP2);
  not not_63 (not_63_out, OP1);
  not not_64 (not_64_out, OP0);
  not not_65 (not_65_out, OP5);
  not not_66 (not_66_out, OP4);
  not not_67 (not_67_out, OP1);
  not not_68 (not_68_out, OP0);
  not not_69 (not_69_out, OP5);
  not not_70 (not_70_out, OP4);
  not not_71 (not_71_out, OP2);
  not not_72 (not_72_out, OP1);
  not not_73 (not_73_out, OP5);
  not not_74 (not_74_out, OP4);
  not not_75 (not_75_out, OP2);
  not not_76 (not_76_out, OP0);
  not not_77 (not_77_out, OP4);
  not not_78 (not_78_out, OP3);
  not not_79 (not_79_out, OP2);
  not not_80 (not_80_out, OP4);
  not not_81 (not_81_out, OP2);
  not not_82 (not_82_out, OP5);
  not not_83 (not_83_out, OP4);
  not not_84 (not_84_out, OP3);
  not not_85 (not_85_out, OP2);
  not not_86 (not_86_out, OP1);
  not not_87 (not_87_out, OP0);
  not not_88 (not_88_out, F4);
  not not_89 (not_89_out, F3);
  not not_90 (not_90_out, F0);
  not not_91 (not_91_out, OP4);
  not not_92 (not_92_out, OP3);
  not not_93 (not_93_out, OP2);
  not not_94 (not_94_out, OP1);
  not not_95 (not_95_out, OP0);
  not not_96 (not_96_out, OP5);
  not not_97 (not_97_out, OP4);
  not not_98 (not_98_out, OP3);
  not not_99 (not_99_out, OP5);
  not not_100 (not_100_out, OP4);
  not not_101 (not_101_out, OP3);
  not not_102 (not_102_out, OP2);
  not not_103 (not_103_out, OP1);
  not not_104 (not_104_out, OP0);
  not not_105 (not_105_out, F5);
  not not_106 (not_106_out, F4);
  not not_107 (not_107_out, F3);
  not not_108 (not_108_out, F2);
  not not_109 (not_109_out, F0);
  not not_110 (not_110_out, OP5);
  not not_111 (not_111_out, OP4);
  not not_112 (not_112_out, OP3);
  not not_113 (not_113_out, OP2);
  not not_114 (not_114_out, OP1);
  not not_115 (not_115_out, OP0);
  not not_116 (not_116_out, F4);
  not not_117 (not_117_out, F3);
  not not_118 (not_118_out, F2);
  not not_119 (not_119_out, F0);
  not not_120 (not_120_out, OP5);
  not not_121 (not_121_out, OP4);
  not not_122 (not_122_out, OP3);
  not not_123 (not_123_out, OP2);
  not not_124 (not_124_out, OP1);
  not not_125 (not_125_out, OP0);
  not not_126 (not_126_out, F4);
  not not_127 (not_127_out, F3);
  not not_128 (not_128_out, F1);
  not not_129 (not_129_out, F0);
  not not_130 (not_130_out, OP5);
  not not_131 (not_131_out, OP4);
  not not_132 (not_132_out, OP3);
  not not_133 (not_133_out, OP2);
  not not_134 (not_134_out, OP1);
  not not_135 (not_135_out, OP0);
  not not_136 (not_136_out, F4);
  not not_137 (not_137_out, F3);
  not not_138 (not_138_out, OP5);
  not not_139 (not_139_out, OP4);
  not not_140 (not_140_out, OP3);
  not not_141 (not_141_out, OP2);
  not not_142 (not_142_out, OP1);
  not not_143 (not_143_out, OP0);
  not not_144 (not_144_out, F4);
  not not_145 (not_145_out, F2);
  not not_146 (not_146_out, F0);
  not not_147 (not_147_out, OP5);
  not not_148 (not_148_out, OP4);
  not not_149 (not_149_out, OP3);
  not not_150 (not_150_out, OP1);
  not not_151 (not_151_out, OP0);
  not not_152 (not_152_out, OP5);
  not not_153 (not_153_out, OP4);
  not not_154 (not_154_out, OP3);
  not not_155 (not_155_out, OP1);
  not not_156 (not_156_out, OP5);
  not not_157 (not_157_out, OP4);
  not not_158 (not_158_out, OP1);
  not not_159 (not_159_out, OP0);
  not not_160 (not_160_out, OP5);
  not not_161 (not_161_out, OP4);
  not not_162 (not_162_out, OP2);
  not not_163 (not_163_out, OP0);
  not not_164 (not_164_out, OP5);
  not not_165 (not_165_out, OP4);
  not not_166 (not_166_out, OP3);
  not not_167 (not_167_out, OP5);
  not not_168 (not_168_out, OP4);
  not not_169 (not_169_out, OP3);
  not not_170 (not_170_out, OP2);
  not not_171 (not_171_out, OP1);
  not not_172 (not_172_out, OP0);
  not not_173 (not_173_out, F4);
  not not_174 (not_174_out, F3);
  not not_175 (not_175_out, F2);
  not not_176 (not_176_out, F1);
  not not_177 (not_177_out, F0);
  not not_178 (not_178_out, OP5);
  not not_179 (not_179_out, OP4);
  not not_180 (not_180_out, OP3);
  not not_181 (not_181_out, OP2);
  not not_182 (not_182_out, OP1);
  not not_183 (not_183_out, OP0);
  not not_184 (not_184_out, F4);
  not not_185 (not_185_out, F3);
  not not_186 (not_186_out, F2);
  not not_187 (not_187_out, F1);
  not not_188 (not_188_out, OP5);
  not not_189 (not_189_out, OP4);
  not not_190 (not_190_out, OP3);
  not not_191 (not_191_out, OP2);
  not not_192 (not_192_out, OP1);
  not not_193 (not_193_out, OP0);
  not not_194 (not_194_out, F4);
  not not_195 (not_195_out, F3);
  not not_196 (not_196_out, F2);
  not not_197 (not_197_out, F0);
  not not_198 (not_198_out, OP5);
  not not_199 (not_199_out, OP4);
  not not_200 (not_200_out, OP3);
  not not_201 (not_201_out, OP2);
  not not_202 (not_202_out, OP1);
  not not_203 (not_203_out, OP0);
  not not_204 (not_204_out, F4);
  not not_205 (not_205_out, F3);
  not not_206 (not_206_out, F1);
  not not_207 (not_207_out, F0);
  not not_208 (not_208_out, OP5);
  not not_209 (not_209_out, OP4);
  not not_210 (not_210_out, OP3);
  not not_211 (not_211_out, OP2);
  not not_212 (not_212_out, OP1);
  not not_213 (not_213_out, OP0);
  not not_214 (not_214_out, F4);
  not not_215 (not_215_out, F2);
  not not_216 (not_216_out, OP5);
  not not_217 (not_217_out, OP4);
  not not_218 (not_218_out, OP2);
  not not_219 (not_219_out, OP1);
  not not_220 (not_220_out, OP0);
  not not_221 (not_221_out, OP5);
  not not_222 (not_222_out, OP4);
  not not_223 (not_223_out, OP1);
  not not_224 (not_224_out, OP0);
  not not_225 (not_225_out, OP5);
  not not_226 (not_226_out, OP4);
  not not_227 (not_227_out, OP2);
  not not_228 (not_228_out, OP1);
  not not_229 (not_229_out, OP4);
  not not_230 (not_230_out, OP3);
  not not_231 (not_231_out, OP2);
  not not_232 (not_232_out, OP4);
  not not_233 (not_233_out, OP2);
  not not_234 (not_234_out, OP5);
  not not_235 (not_235_out, OP4);
  not not_236 (not_236_out, OP2);
  not not_237 (not_237_out, OP4);
  not not_238 (not_238_out, OP3);
  not not_239 (not_239_out, OP2);
  not not_240 (not_240_out, OP1);
  not not_241 (not_241_out, OP0);
  not not_242 (not_242_out, OP5);
  not not_243 (not_243_out, OP4);
  not not_244 (not_244_out, OP3);
  not not_245 (not_245_out, OP2);
  not not_246 (not_246_out, OP1);
  not not_247 (not_247_out, OP0);
  not not_248 (not_248_out, F4);
  not not_249 (not_249_out, F3);
  not not_250 (not_250_out, F1);
  not not_251 (not_251_out, OP5);
  not not_252 (not_252_out, OP4);
  not not_253 (not_253_out, OP3);
  not not_254 (not_254_out, OP2);
  not not_255 (not_255_out, OP1);
  not not_256 (not_256_out, OP0);
  not not_257 (not_257_out, F4);
  not not_258 (not_258_out, F3);
  not not_259 (not_259_out, OP5);
  not not_260 (not_260_out, OP4);
  not not_261 (not_261_out, OP3);
  not not_262 (not_262_out, OP2);
  not not_263 (not_263_out, OP1);
  not not_264 (not_264_out, OP0);
  not not_265 (not_265_out, F4);
  not not_266 (not_266_out, F2);
  not not_267 (not_267_out, F0);
  not not_268 (not_268_out, OP5);
  not not_269 (not_269_out, OP4);
  not not_270 (not_270_out, OP3);
  not not_271 (not_271_out, OP2);
  not not_272 (not_272_out, OP1);
  not not_273 (not_273_out, OP0);
  not not_274 (not_274_out, F4);
  not not_275 (not_275_out, F2);
  not not_276 (not_276_out, OP5);
  not not_277 (not_277_out, OP4);
  not not_278 (not_278_out, OP3);
  not not_279 (not_279_out, OP1);
  not not_280 (not_280_out, OP0);
  not not_281 (not_281_out, OP5);
  not not_282 (not_282_out, OP4);
  not not_283 (not_283_out, OP3);
  not not_284 (not_284_out, OP1);
  not not_285 (not_285_out, OP5);
  not not_286 (not_286_out, OP4);
  not not_287 (not_287_out, OP2);
  not not_288 (not_288_out, OP0);
  not not_289 (not_289_out, OP5);
  not not_290 (not_290_out, OP4);
  not not_291 (not_291_out, OP1);
  not not_292 (not_292_out, OP5);
  not not_293 (not_293_out, OP4);
  not not_294 (not_294_out, OP3);
  not not_295 (not_295_out, OP2);
  not not_296 (not_296_out, OP1);
  not not_297 (not_297_out, OP0);
  not not_298 (not_298_out, F4);
  not not_299 (not_299_out, F3);
  not not_300 (not_300_out, F0);
  not not_301 (not_301_out, OP5);
  not not_302 (not_302_out, OP4);
  not not_303 (not_303_out, OP2);
  not not_304 (not_304_out, OP5);
  not not_305 (not_305_out, OP4);
  not not_306 (not_306_out, OP3);
  and and_1 (and_1_out, not_1_out, not_2_out, not_3_out, not_4_out, not_5_out, not_6_out, not_7_out, not_8_out, not_9_out, not_10_out, F1, F0);
  and and_2 (and_2_out, not_11_out, not_12_out, not_13_out, not_14_out, not_15_out, not_16_out, F5, not_17_out, not_18_out, not_19_out, not_20_out, not_21_out);
  and and_3 (and_3_out, not_22_out, not_23_out, not_24_out, not_25_out, not_26_out, not_27_out, F5, not_28_out, not_29_out, not_30_out, not_31_out, F0);
  and and_4 (and_4_out, not_32_out, not_33_out, not_34_out, not_35_out, not_36_out, not_37_out, F5, not_38_out, not_39_out, F2, not_40_out, not_41_out);
  and and_5 (and_5_out, not_42_out, not_43_out, not_44_out, not_45_out, not_46_out, not_47_out, F5, not_48_out, F3, not_49_out, F1, not_50_out);
  and and_6 (and_6_out, not_51_out, not_52_out, not_53_out, OP2, not_54_out, not_55_out);
  and and_7 (and_7_out, not_56_out, not_57_out, not_58_out, OP2, not_59_out, OP0);
  and and_8 (and_8_out, not_60_out, not_61_out, OP3, not_62_out, not_63_out, not_64_out);
  and and_9 (and_9_out, not_65_out, not_66_out, OP3, OP2, not_67_out, not_68_out);
  and and_10 (and_10_out, not_69_out, not_70_out, OP3, not_71_out, not_72_out, OP0);
  and and_11 (and_11_out, not_73_out, not_74_out, OP3, not_75_out, OP1, not_76_out);
  and and_12 (and_12_out, OP5, not_77_out, not_78_out, not_79_out, OP1, OP0);
  and and_13 (and_13_out, OP5, not_80_out, OP3, not_81_out, OP1, OP0);
  and and_14 (and_14_out, not_82_out, not_83_out, not_84_out, not_85_out, not_86_out, not_87_out, F5, not_88_out, not_89_out, F2, F1, not_90_out);
  and and_15 (and_15_out, OP5, not_91_out, not_92_out, not_93_out, not_94_out, not_95_out);
  and and_16 (and_16_out, not_96_out, not_97_out, not_98_out, OP2, OP1, OP0);
  and and_17 (and_17_out, not_99_out, not_100_out, not_101_out, not_102_out, not_103_out, not_104_out, not_105_out, not_106_out, not_107_out, not_108_out, F1, not_109_out);
  and and_18 (and_18_out, not_110_out, not_111_out, not_112_out, not_113_out, not_114_out, not_115_out, F5, not_116_out, not_117_out, not_118_out, F1, not_119_out);
  and and_19 (and_19_out, not_120_out, not_121_out, not_122_out, not_123_out, not_124_out, not_125_out, F5, not_126_out, not_127_out, F2, not_128_out, not_129_out);
  and and_20 (and_20_out, not_130_out, not_131_out, not_132_out, not_133_out, not_134_out, not_135_out, F5, not_136_out, not_137_out, F2, F1, F0);
  and and_21 (and_21_out, not_138_out, not_139_out, not_140_out, not_141_out, not_142_out, not_143_out, F5, not_144_out, F3, not_145_out, F1, not_146_out);
  and and_22 (and_22_out, not_147_out, not_148_out, not_149_out, OP2, not_150_out, not_151_out);
  and and_23 (and_23_out, not_152_out, not_153_out, not_154_out, OP2, not_155_out, OP0);
  and and_24 (and_24_out, not_156_out, not_157_out, OP3, OP2, not_158_out, not_159_out);
  and and_25 (and_25_out, not_160_out, not_161_out, OP3, not_162_out, OP1, not_163_out);
  and and_26 (and_26_out, not_164_out, not_165_out, not_166_out, OP2, OP1, OP0);
  and and_27 (and_27_out, not_167_out, not_168_out, not_169_out, not_170_out, not_171_out, not_172_out, F5, not_173_out, not_174_out, not_175_out, not_176_out, not_177_out);
  and and_28 (and_28_out, not_178_out, not_179_out, not_180_out, not_181_out, not_182_out, not_183_out, F5, not_184_out, not_185_out, not_186_out, not_187_out, F0);
  and and_29 (and_29_out, not_188_out, not_189_out, not_190_out, not_191_out, not_192_out, not_193_out, F5, not_194_out, not_195_out, not_196_out, F1, not_197_out);
  and and_30 (and_30_out, not_198_out, not_199_out, not_200_out, not_201_out, not_202_out, not_203_out, F5, not_204_out, not_205_out, F2, not_206_out, not_207_out);
  and and_31 (and_31_out, not_208_out, not_209_out, not_210_out, not_211_out, not_212_out, not_213_out, F5, not_214_out, F3, not_215_out, F1, F0);
  and and_32 (and_32_out, not_216_out, not_217_out, OP3, not_218_out, not_219_out, not_220_out);
  and and_33 (and_33_out, not_221_out, not_222_out, OP3, OP2, not_223_out, not_224_out);
  and and_34 (and_34_out, not_225_out, not_226_out, OP3, not_227_out, not_228_out, OP0);
  and and_35 (and_35_out, OP5, not_229_out, not_230_out, not_231_out, OP1, OP0);
  and and_36 (and_36_out, OP5, not_232_out, OP3, not_233_out, OP1, OP0);
  and and_37 (and_37_out, not_234_out, not_235_out, OP3, not_236_out, OP1, OP0);
  and and_38 (and_38_out, OP5, not_237_out, not_238_out, not_239_out, not_240_out, not_241_out);
  and and_39 (and_39_out, not_242_out, not_243_out, not_244_out, not_245_out, not_246_out, not_247_out, F5, not_248_out, not_249_out, F2, not_250_out, F0);
  and and_40 (and_40_out, not_251_out, not_252_out, not_253_out, not_254_out, not_255_out, not_256_out, F5, not_257_out, not_258_out, F2, F1, F0);
  and and_41 (and_41_out, not_259_out, not_260_out, not_261_out, not_262_out, not_263_out, not_264_out, F5, not_265_out, F3, not_266_out, F1, not_267_out);
  and and_42 (and_42_out, not_268_out, not_269_out, not_270_out, not_271_out, not_272_out, not_273_out, F5, not_274_out, F3, not_275_out, F1, F0);
  and and_43 (and_43_out, not_276_out, not_277_out, not_278_out, OP2, not_279_out, not_280_out);
  and and_44 (and_44_out, not_281_out, not_282_out, not_283_out, OP2, not_284_out, OP0);
  and and_45 (and_45_out, not_285_out, not_286_out, OP3, not_287_out, OP1, not_288_out);
  and and_46 (and_46_out, not_289_out, not_290_out, OP3, OP2, not_291_out, OP0);
  and and_47 (and_47_out, not_292_out, not_293_out, not_294_out, not_295_out, not_296_out, not_297_out, F5, not_298_out, not_299_out, F2, F1, not_300_out);
  and and_48 (and_48_out, not_301_out, not_302_out, OP3, not_303_out, OP1, OP0);
  and and_49 (and_49_out, not_304_out, not_305_out, not_306_out, OP2, OP1, OP0);
  or or_1 (S1, and_17_out, and_18_out, and_19_out, and_20_out, and_21_out, and_22_out, and_23_out, and_24_out, and_25_out, and_26_out);
  or or_2 (S3, and_39_out, and_40_out, and_41_out, and_42_out, and_43_out, and_44_out, and_45_out, and_46_out, and_47_out, and_48_out, and_49_out);
  or or_3 (S0, and_1_out, and_2_out, and_3_out, and_4_out, and_5_out, and_6_out, and_7_out, and_8_out, and_9_out, and_10_out, and_11_out, and_12_out, and_13_out, and_14_out, and_15_out, and_16_out);
  or or_4 (S2, and_27_out, and_28_out, and_29_out, and_30_out, and_31_out, and_32_out, and_33_out, and_34_out, and_35_out, and_36_out, and_37_out, and_38_out);
endmodule

// 控制信号生成
module \控制信号自动生成  (
  input  OP0,
  input  OP1,
  input  OP2,
  input  OP3,
  input  OP4,
  input  OP5,
  input  F0,
  input  F1,
  input  F2,
  input  F3,
  input  F4,
  input  F5,
  output MemToReg,
  output MemWrite,
  output ALU_SRC,
  output RegWrite,
  output SysCALL,
  output SignedExt,
  output RegDst,
  output BEQ,
  output BNE,
  output JR,
  output JUMP,
  output JAL,
  output BGTZ,
  output LB
);

  wire and_1_out, and_2_out, and_4_out, and_5_out, and_6_out, and_7_out, and_8_out, and_9_out, and_10_out,
       and_11_out, and_12_out, and_13_out, and_14_out, and_15_out, and_16_out, and_18_out, and_19_out,
       and_20_out, and_21_out, and_22_out, and_23_out, and_24_out, and_25_out, and_26_out, and_27_out,
       and_28_out, not_1_out, not_2_out, not_3_out, not_4_out, not_5_out, not_6_out, not_7_out, not_8_out,
       not_9_out, not_10_out, not_11_out, not_12_out, not_13_out, not_14_out, not_15_out, not_16_out,
       not_17_out, not_18_out, not_19_out, not_20_out, not_21_out, not_22_out, not_23_out, not_24_out,
       not_25_out, not_26_out, not_27_out, not_28_out, not_29_out, not_30_out, not_31_out, not_32_out,
       not_33_out, not_34_out, not_35_out, not_36_out, not_37_out, not_38_out, not_39_out, not_40_out,
       not_41_out, not_42_out, not_43_out, not_44_out, not_45_out, not_46_out, not_47_out, not_48_out,
       not_49_out, not_50_out, not_51_out, not_52_out, not_53_out, not_54_out, not_55_out, not_56_out,
       not_57_out, not_58_out, not_59_out, not_60_out, not_61_out, not_62_out, not_63_out, not_64_out,
       not_65_out, not_66_out, not_67_out, not_68_out, not_69_out, not_70_out, not_71_out, not_72_out,
       not_73_out, not_74_out, not_75_out, not_76_out, not_77_out, not_78_out, not_79_out, not_80_out,
       not_81_out, not_82_out, not_83_out, not_84_out, not_85_out, not_86_out, not_87_out, not_88_out,
       not_89_out, not_90_out, not_91_out, not_92_out, not_93_out, not_94_out, not_95_out, not_96_out,
       not_97_out, not_98_out, not_99_out, not_100_out, not_101_out, not_102_out, not_103_out, not_104_out,
       not_105_out, not_106_out, not_107_out, not_108_out, not_109_out, not_110_out, not_111_out,
       not_112_out, not_113_out, not_114_out, not_115_out, not_116_out, not_117_out, not_118_out,
       not_119_out, not_120_out, not_121_out, not_122_out, not_123_out, not_124_out, not_125_out,
       not_126_out, not_127_out, not_128_out, not_129_out, not_130_out, not_131_out, not_132_out,
       not_133_out, not_134_out, not_135_out, not_136_out, not_137_out, not_138_out, not_139_out,
       not_140_out, not_141_out, not_142_out, not_143_out, not_144_out, not_145_out, not_146_out,
       not_147_out, not_148_out, not_149_out, not_150_out, not_151_out, not_152_out, not_153_out,
       not_154_out, not_155_out, not_156_out, not_157_out, not_158_out, not_159_out, not_160_out,
       not_161_out, not_162_out, not_163_out, not_164_out, not_165_out, not_166_out, not_167_out,
       not_168_out, not_169_out, not_170_out, not_171_out, not_172_out, not_173_out, not_174_out,
       not_175_out, not_176_out, not_177_out, not_178_out, not_179_out, not_180_out, not_181_out,
       not_182_out, not_183_out, not_184_out, not_185_out, not_186_out, not_187_out, not_188_out,
       not_189_out, not_190_out, not_191_out, not_192_out, not_193_out, not_194_out, not_195_out,
       not_196_out, not_197_out, not_198_out, not_199_out;

  not not_1 (not_1_out, OP0);
  not not_2 (not_2_out, OP1);
  not not_3 (not_3_out, OP2);
  not not_4 (not_4_out, OP3);
  not not_5 (not_5_out, OP4);
  not not_6 (not_6_out, OP2);
  not not_7 (not_7_out, OP3);
  not not_8 (not_8_out, OP4);
  not not_9 (not_9_out, OP2);
  not not_10 (not_10_out, OP4);
  not not_11 (not_11_out, OP0);
  not not_12 (not_12_out, OP1);
  not not_13 (not_13_out, OP2);
  not not_14 (not_14_out, OP3);
  not not_15 (not_15_out, OP4);
  not not_16 (not_16_out, OP1);
  not not_17 (not_17_out, OP4);
  not not_18 (not_18_out, OP5);
  not not_19 (not_19_out, OP2);
  not not_20 (not_20_out, OP4);
  not not_21 (not_21_out, OP5);
  not not_22 (not_22_out, OP2);
  not not_23 (not_23_out, OP4);
  not not_24 (not_24_out, OP0);
  not not_25 (not_25_out, OP1);
  not not_26 (not_26_out, OP2);
  not not_27 (not_27_out, OP3);
  not not_28 (not_28_out, OP4);
  not not_29 (not_29_out, F0);
  not not_30 (not_30_out, F2);
  not not_31 (not_31_out, F3);
  not not_32 (not_32_out, F4);
  not not_33 (not_33_out, OP0);
  not not_34 (not_34_out, OP1);
  not not_35 (not_35_out, OP2);
  not not_36 (not_36_out, OP3);
  not not_37 (not_37_out, OP4);
  not not_38 (not_38_out, F1);
  not not_39 (not_39_out, F3);
  not not_40 (not_40_out, F4);
  not not_41 (not_41_out, OP0);
  not not_42 (not_42_out, OP1);
  not not_43 (not_43_out, OP2);
  not not_44 (not_44_out, OP3);
  not not_45 (not_45_out, OP4);
  not not_46 (not_46_out, F3);
  not not_47 (not_47_out, F4);
  not not_48 (not_48_out, OP0);
  not not_49 (not_49_out, OP1);
  not not_50 (not_50_out, OP2);
  not not_51 (not_51_out, OP3);
  not not_52 (not_52_out, OP4);
  not not_53 (not_53_out, F2);
  not not_54 (not_54_out, F3);
  not not_55 (not_55_out, F4);
  not not_56 (not_56_out, F5);
  not not_57 (not_57_out, OP0);
  not not_58 (not_58_out, OP1);
  not not_59 (not_59_out, OP2);
  not not_60 (not_60_out, OP3);
  not not_61 (not_61_out, OP4);
  not not_62 (not_62_out, F2);
  not not_63 (not_63_out, F4);
  not not_64 (not_64_out, OP0);
  not not_65 (not_65_out, OP1);
  not not_66 (not_66_out, OP2);
  not not_67 (not_67_out, OP3);
  not not_68 (not_68_out, OP4);
  not not_69 (not_69_out, OP1);
  not not_70 (not_70_out, OP4);
  not not_71 (not_71_out, OP5);
  not not_72 (not_72_out, OP2);
  not not_73 (not_73_out, OP4);
  not not_74 (not_74_out, OP5);
  not not_75 (not_75_out, OP2);
  not not_76 (not_76_out, OP3);
  not not_77 (not_77_out, OP4);
  not not_78 (not_78_out, OP0);
  not not_79 (not_79_out, OP1);
  not not_80 (not_80_out, OP2);
  not not_81 (not_81_out, OP3);
  not not_82 (not_82_out, OP4);
  not not_83 (not_83_out, OP5);
  not not_84 (not_84_out, F0);
  not not_85 (not_85_out, F1);
  not not_86 (not_86_out, F4);
  not not_87 (not_87_out, F5);
  not not_88 (not_88_out, OP0);
  not not_89 (not_89_out, OP1);
  not not_90 (not_90_out, OP2);
  not not_91 (not_91_out, OP3);
  not not_92 (not_92_out, OP4);
  not not_93 (not_93_out, OP0);
  not not_94 (not_94_out, OP2);
  not not_95 (not_95_out, OP4);
  not not_96 (not_96_out, OP5);
  not not_97 (not_97_out, OP1);
  not not_98 (not_98_out, OP2);
  not not_99 (not_99_out, OP4);
  not not_100 (not_100_out, OP5);
  not not_101 (not_101_out, OP1);
  not not_102 (not_102_out, OP3);
  not not_103 (not_103_out, OP4);
  not not_104 (not_104_out, OP5);
  not not_105 (not_105_out, OP2);
  not not_106 (not_106_out, OP4);
  not not_107 (not_107_out, OP0);
  not not_108 (not_108_out, OP1);
  not not_109 (not_109_out, OP2);
  not not_110 (not_110_out, OP3);
  not not_111 (not_111_out, OP4);
  not not_112 (not_112_out, OP5);
  not not_113 (not_113_out, F0);
  not not_114 (not_114_out, F1);
  not not_115 (not_115_out, F2);
  not not_116 (not_116_out, F4);
  not not_117 (not_117_out, F5);
  not not_118 (not_118_out, OP0);
  not not_119 (not_119_out, OP1);
  not not_120 (not_120_out, OP2);
  not not_121 (not_121_out, OP3);
  not not_122 (not_122_out, OP4);
  not not_123 (not_123_out, OP5);
  not not_124 (not_124_out, F0);
  not not_125 (not_125_out, F2);
  not not_126 (not_126_out, F3);
  not not_127 (not_127_out, F4);
  not not_128 (not_128_out, OP0);
  not not_129 (not_129_out, OP1);
  not not_130 (not_130_out, OP2);
  not not_131 (not_131_out, OP3);
  not not_132 (not_132_out, OP4);
  not not_133 (not_133_out, OP5);
  not not_134 (not_134_out, F1);
  not not_135 (not_135_out, F3);
  not not_136 (not_136_out, F4);
  not not_137 (not_137_out, OP0);
  not not_138 (not_138_out, OP1);
  not not_139 (not_139_out, OP2);
  not not_140 (not_140_out, OP3);
  not not_141 (not_141_out, OP4);
  not not_142 (not_142_out, OP5);
  not not_143 (not_143_out, F3);
  not not_144 (not_144_out, F4);
  not not_145 (not_145_out, OP0);
  not not_146 (not_146_out, OP1);
  not not_147 (not_147_out, OP2);
  not not_148 (not_148_out, OP3);
  not not_149 (not_149_out, OP4);
  not not_150 (not_150_out, OP5);
  not not_151 (not_151_out, F2);
  not not_152 (not_152_out, F3);
  not not_153 (not_153_out, F4);
  not not_154 (not_154_out, F5);
  not not_155 (not_155_out, OP0);
  not not_156 (not_156_out, OP1);
  not not_157 (not_157_out, OP2);
  not not_158 (not_158_out, OP3);
  not not_159 (not_159_out, OP4);
  not not_160 (not_160_out, OP5);
  not not_161 (not_161_out, F2);
  not not_162 (not_162_out, F4);
  not not_163 (not_163_out, OP0);
  not not_164 (not_164_out, OP1);
  not not_165 (not_165_out, OP3);
  not not_166 (not_166_out, OP4);
  not not_167 (not_167_out, OP5);
  not not_168 (not_168_out, OP1);
  not not_169 (not_169_out, OP3);
  not not_170 (not_170_out, OP4);
  not not_171 (not_171_out, OP5);
  not not_172 (not_172_out, OP0);
  not not_173 (not_173_out, OP1);
  not not_174 (not_174_out, OP2);
  not not_175 (not_175_out, OP3);
  not not_176 (not_176_out, OP4);
  not not_177 (not_177_out, OP5);
  not not_178 (not_178_out, F0);
  not not_179 (not_179_out, F1);
  not not_180 (not_180_out, F2);
  not not_181 (not_181_out, F4);
  not not_182 (not_182_out, F5);
  not not_183 (not_183_out, OP0);
  not not_184 (not_184_out, OP2);
  not not_185 (not_185_out, OP3);
  not not_186 (not_186_out, OP4);
  not not_187 (not_187_out, OP5);
  not not_188 (not_188_out, OP2);
  not not_189 (not_189_out, OP3);
  not not_190 (not_190_out, OP4);
  not not_191 (not_191_out, OP5);
  not not_192 (not_192_out, OP3);
  not not_193 (not_193_out, OP4);
  not not_194 (not_194_out, OP5);
  not not_195 (not_195_out, OP4);
  not not_196 (not_196_out, OP3);
  not not_197 (not_197_out, OP2);
  not not_198 (not_198_out, OP1);
  not not_199 (not_199_out, OP0);
  and and_1 (and_1_out, not_1_out, not_2_out, not_3_out, not_4_out, not_5_out, OP5);
  and and_2 (and_2_out, OP0, OP1, not_6_out, not_7_out, not_8_out, OP5);
  and and_3 (MemWrite, OP0, OP1, not_9_out, OP3, not_10_out, OP5);
  and and_4 (and_4_out, not_11_out, not_12_out, not_13_out, not_14_out, not_15_out, OP5);
  and and_5 (and_5_out, not_16_out, OP3, not_17_out, not_18_out);
  and and_6 (and_6_out, not_19_out, OP3, not_20_out, not_21_out);
  and and_7 (and_7_out, OP0, OP1, not_22_out, not_23_out);
  and and_8 (and_8_out, not_24_out, not_25_out, not_26_out, not_27_out, not_28_out, not_29_out, not_30_out, not_31_out, not_32_out);
  and and_9 (and_9_out, not_33_out, not_34_out, not_35_out, not_36_out, not_37_out, not_38_out, not_39_out, not_40_out, F5);
  and and_10 (and_10_out, not_41_out, not_42_out, not_43_out, not_44_out, not_45_out, F2, not_46_out, not_47_out, F5);
  and and_11 (and_11_out, not_48_out, not_49_out, not_50_out, not_51_out, not_52_out, F1, not_53_out, not_54_out, not_55_out, not_56_out);
  and and_12 (and_12_out, not_57_out, not_58_out, not_59_out, not_60_out, not_61_out, F1, not_62_out, F3, not_63_out, F5);
  and and_13 (and_13_out, not_64_out, not_65_out, not_66_out, not_67_out, not_68_out, OP5);
  and and_14 (and_14_out, not_69_out, OP3, not_70_out, not_71_out);
  and and_15 (and_15_out, not_72_out, OP3, not_73_out, not_74_out);
  and and_16 (and_16_out, OP0, OP1, not_75_out, not_76_out, not_77_out);
  and and_17 (SysCALL, not_78_out, not_79_out, not_80_out, not_81_out, not_82_out, not_83_out, not_84_out, not_85_out, F2, F3, not_86_out, not_87_out);
  and and_18 (and_18_out, not_88_out, not_89_out, not_90_out, not_91_out, not_92_out, OP5);
  and and_19 (and_19_out, not_93_out, not_94_out, OP3, not_95_out, not_96_out);
  and and_20 (and_20_out, not_97_out, not_98_out, OP3, not_99_out, not_100_out);
  and and_21 (and_21_out, not_101_out, OP2, not_102_out, not_103_out, not_104_out);
  and and_22 (and_22_out, OP0, OP1, not_105_out, not_106_out, OP5);
  and and_23 (and_23_out, not_107_out, not_108_out, not_109_out, not_110_out, not_111_out, not_112_out, not_113_out, not_114_out, not_115_out, not_116_out, not_117_out);
  and and_24 (and_24_out, not_118_out, not_119_out, not_120_out, not_121_out, not_122_out, not_123_out, not_124_out, not_125_out, not_126_out, not_127_out);
  and and_25 (and_25_out, not_128_out, not_129_out, not_130_out, not_131_out, not_132_out, not_133_out, not_134_out, not_135_out, not_136_out, F5);
  and and_26 (and_26_out, not_137_out, not_138_out, not_139_out, not_140_out, not_141_out, not_142_out, F2, not_143_out, not_144_out, F5);
  and and_27 (and_27_out, not_145_out, not_146_out, not_147_out, not_148_out, not_149_out, not_150_out, F1, not_151_out, not_152_out, not_153_out, not_154_out);
  and and_28 (and_28_out, not_155_out, not_156_out, not_157_out, not_158_out, not_159_out, not_160_out, F1, not_161_out, F3, not_162_out, F5);
  and and_29 (BEQ, not_163_out, not_164_out, OP2, not_165_out, not_166_out, not_167_out);
  and and_30 (BNE, OP0, not_168_out, OP2, not_169_out, not_170_out, not_171_out);
  and and_31 (JR, not_172_out, not_173_out, not_174_out, not_175_out, not_176_out, not_177_out, not_178_out, not_179_out, not_180_out, F3, not_181_out, not_182_out);
  and and_32 (JUMP, not_183_out, OP1, not_184_out, not_185_out, not_186_out, not_187_out);
  and and_33 (JAL, OP0, OP1, not_188_out, not_189_out, not_190_out, not_191_out);
  and and_34 (BGTZ, OP0, OP1, OP2, not_192_out, not_193_out, not_194_out);
  and and_35 (LB, OP5, not_195_out, not_196_out, not_197_out, not_198_out, not_199_out);
  or or_1 (MemToReg, and_1_out, and_2_out);
  or or_2 (ALU_SRC, and_4_out, and_5_out, and_6_out, and_7_out);
  or or_3 (RegWrite, and_8_out, and_9_out, and_10_out, and_11_out, and_12_out, and_13_out, and_14_out, and_15_out, and_16_out);
  or or_4 (SignedExt, and_18_out, and_19_out, and_20_out, and_21_out, and_22_out);
  or or_5 (RegDst, and_23_out, and_24_out, and_25_out, and_26_out, and_27_out, and_28_out);
endmodule

// ALU
module MIPS_ALU (
  input  [4:0] shamt,
  input  [31:0] X,
  input  [31:0] Y,
  input  [3:0] AluOP,
  output Equal,
  output [31:0] Result,
  output [31:0] Result_2
);

  wire [0:0] comparator_1_lt, comparator_2_lt;
  wire [31:0] adder_1_out, AND_out, divider_1_out, divider_1_rem, multiplier_1_cout, multiplier_1_out,
       NOR_out, OR_out, shifter_1_out, shifter_2_out, shifter_3_out, subtractor_1_out, XOR_out;

  assign AND_out = X & Y;  // AND_Gate AND, 32 bits wide
  assign OR_out = X | Y;  // OR_Gate OR, 32 bits wide
  Shifter #(.width(32), .shift("ll")) shifter_1 (.in(Y), .\dist (shamt), .out(shifter_1_out));
  Shifter #(.width(32), .shift("ar")) shifter_2 (.in(Y), .\dist (shamt), .out(shifter_2_out));
  Shifter #(.width(32), .shift("lr")) shifter_3 (.in(Y), .\dist (shamt), .out(shifter_3_out));
  Multiplier #(.width(32)) multiplier_1 (.a(X), .b(Y), .out(multiplier_1_out), .cout(multiplier_1_cout));  // open: cin
  Divider #(.width(32)) divider_1 (.a(X), .b(Y), .out(divider_1_out), .rem(divider_1_rem));  // open: upper
  Adder #(.width(32)) adder_1 (.a(X), .b(Y), .out(adder_1_out));  // open: cin, cout
  Subtractor #(.width(32)) subtractor_1 (.a(X), .b(Y), .out(subtractor_1_out));  // open: bin, bout
  assign XOR_out = X ^ Y;  // XOR_Gate XOR, 32 bits wide
  assign NOR_out = ~(X | Y);  // NOR_Gate NOR, 32 bits wide
  Comparator #(.width(32), .mode("twosComplement")) comparator_1 (
    .a(X), .b(Y), .eq(Equal), .lt(comparator_1_lt[0]));  // open: gt
  Comparator #(.width(32), .mode("unsigned")) comparator_2 (.a(X), .b(Y), .lt(comparator_2_lt[0]));  // open: gt, eq
  Multiplexer #(.select(4), .width(32), .disabled("Z"), .enable("false")) multiplexer_1 (
    .in0(shifter_1_out), .in1(shifter_2_out), .in2(shifter_3_out), .in3(multiplier_1_out),
    .in4(divider_1_out), .in5(adder_1_out), .in6(subtractor_1_out), .in7(AND_out), .in8(OR_out),
    .in9(XOR_out), .in10(NOR_out), .in11({{31{1'b0}}, comparator_1_lt[0]}),
    .in12({{31{1'b0}}, comparator_2_lt[0]}), .in13({32{1'b0}}), .in14({32{1'b0}}), .in15({32{1'b0}}),
    .out(Result), .sel(AluOP));
  Multiplexer #(.select(4), .width(32), .disabled("Z"), .enable("false")) multiplexer_2 (
    .in0({32{1'b0}}), .in1({32{1'b0}}), .in2({32{1'b0}}), .in3(multiplier_1_cout), .in4(divider_1_rem),
    .in5({32{1'b0}}), .in6({32{1'b0}}), .in7({32{1'b0}}), .in8({32{1'b0}}), .in9({32{1'b0}}),
    .in10({32{1'b0}}), .in11({32{1'b0}}), .in12({32{1'b0}}), .in13({32{1'b0}}), .in14({32{1'b0}}),
    .in15({32{1'b0}}), .out(Result_2), .sel(AluOP));

  // Other names for the same wires on the sheet: Result2[31:0] = Result_2; S[3:0] = AluOP

  // Notes on the sheet:
  //   不要改变此引脚区域内容，也不要改变ALU封装形式
  //   输入引脚
  //   输出引脚
endmodule

module MIPS_Regifile (
  input  [31:0] Din,
  input  Clk,
  input  WE,
  input  [4:0] R1_num,
  input  [4:0] W_num,
  input  [4:0] R2_num,
  output [31:0] R1,
  output [31:0] R2
);

  // RegisterFile registerfile_1: pin names not known; wires that end beside it: Din, Clk, WE, W_num, R1_num, R2_num, R1, R2
endmodule

module \重定向流水线  (
  output RegWrite,
  output MemWrite,
  output [31:0] IF_PC,
  output [31:0] ID_PC,
  output [31:0] EX_PC,
  output [31:0] M_PC,
  output [31:0] WB_PC,
  output [31:0] RDin,
  output [31:0] MDin,
  output [31:0] LedData
);

  wire AluSrcB, and_1_out, and_2_out, and_4_out, and_5_out, Beq, beq_bne_suc, BGTZ, bgtz_suc, Bne, CLK,
       comparator_1_eq, ex_Beq, ex_BGTZ, ex_Bne, ex_clear, ex_equal, ex_JAL, ex_JMP, ex_JR, ex_mem_1_out_32,
       ex_mem_1_out_37, ex_mem_1_out_39, ex_mem_1_out_40, ex_MemToReg, ex_regwrite, ex_Syscall, Go,
       id_ex_1_out_33, id_ex_1_out_41, id_ex_1_out_44, id_ex_1_out_50, IR1, IR2, IR3, JAL, JMP, JR, LB,
       LoadUse_stall, mem_regwrite, mem_wb_1_out_17, mem_wb_1_out_18, mem_wb_1_out_23, MemToReg, MemWrite1,
       not_1_out, not_2_out, not_3_out, not_4_out, or_1_out, or_2_out, or_4_out, or_5_out, or_6_out, pause,
       R1_used, R2_used, RegDst, RegWrite1, RST, SignedExt, stop, Syscall, W1, W2, W3, WB_pause,
       \寄存器使用情况_2_r1_used , \寄存器使用情况_2_r2_used ;
  wire [1:0] a_f, b_f, \确定pc_1_out_7 ;
  wire [3:0] AluOp, id_ex_1_out_51;
  wire [4:0] EX_R1_num, EX_R2_num, ex_rd, id_ex_1_out_30, mem_rd, mem_wb_1_rd_2, multiplexer_7_out,
       multiplexer_13_out, multiplexer_14_out, R1_num, R2_num, rd1;
  wire [15:0] \LoadUse次数 , \总周期数 , \插入气泡数 , \无条件分支数 , \条件分支成功数 ;
  wire [25:0] address;
  wire [27:0] ex_nextpc;
  wire [31:0] adder_4_out, bit_extender_1_out, ex_mem_1_ir_2, ex_pcbranch, ex_R1data, ex_R2data, ex_Result,
       id_ex_1_a_2, id_ex_1_imm_2, id_ex_1_r2data_2, id_R1data, id_R2data, if_nextpc, mem_alu,
       mem_wb_1_alu_2, mem_wb_1_ir_2, mem_wb_1_md_2, mips_probe_1_p1, multiplexer_1_out, multiplexer_2_out,
       multiplexer_3_out, multiplexer_10_out, multiplexer_11_out, ram_1_data, shifter_1_out;
  wire [31:2] ex_jmppc;
  wire [31:26] id_ex_1_ir_2, IR;

  Button \u_总复位  (.out(RST));
  Button _1 (.out(IR1));
  Button _2 (.out(IR2));
  Button _3 (.out(IR3));
  Button \u_继续运行  (.out(Go));
  LED #(.active("true")) led_1 (.in(W1));
  LED #(.active("true")) led_2 (.in(W2));
  LED #(.active("true")) led_3 (.in(W3));
  Hex_Digit_Display hex_digit_display_1 (.value(LedData[27:24]));  // open: dp
  Hex_Digit_Display hex_digit_display_2 (.value(LedData[31:28]));  // open: dp
  and and_1 (and_1_out, stop, LoadUse_stall);
  D_Flip_Flop #(.trigger("falling"), .Pre_Clr_Positions("ABOVE_BELOW"), .NegatePresetClear("false"), .enable("false"), .NewFFLayout("true")) d_ff_1 (
    .clk(CLK), .D(WB_pause), .Qn(stop), .reset(Go));  // open: Q, preset
  Multiplexer #(.select(1), .width(32), .disabled("Z"), .enable("false")) multiplexer_1 (
    .in0(if_nextpc), .in1(multiplexer_3_out), .out(multiplexer_1_out), .sel(ex_clear));
  Multiplexer #(.select(2), .width(32), .disabled("Z"), .enable("false")) multiplexer_2 (
    .in0(ex_pcbranch), .in1({ex_jmppc[31:28], ex_nextpc}), .in2(ex_R1data), .in3({ex_jmppc, 2'b00}),
    .out(multiplexer_2_out), .sel(\确定pc_1_out_7 ));
  Hex_Digit_Display hex_digit_display_3 (.value(LedData[19:16]));  // open: dp
  Hex_Digit_Display hex_digit_display_4 (.value(LedData[23:20]));  // open: dp
  Register #(.width(32), .trigger("rising"), .Select("low")) PC (
    .D(multiplexer_1_out), .en(and_1_out), .Q(IF_PC), .clk(CLK));  // open: clr
  Multiplexer #(.select(1), .width(32), .disabled("Z"), .enable("false")) multiplexer_3 (
    .in0(multiplexer_2_out), .in1(ex_pcbranch), .out(multiplexer_3_out), .sel(bgtz_suc));
  Hex_Digit_Display hex_digit_display_5 (.value(LedData[11:8]));  // open: dp
  Hex_Digit_Display hex_digit_display_6 (.value(LedData[15:12]));  // open: dp
  // Mips_Probe mips_probe_1: pin names not known; wires that end beside it: mips_probe_1_p1
  Adder #(.width(32)) adder_1 (.a(32'h4), .b(IF_PC), .out(if_nextpc));  // open: cin, cout
  or or_1 (or_1_out, ex_JMP, ex_JAL);
  or or_2 (or_2_out, or_1_out, beq_bne_suc, ex_JR);
  or or_3 (ex_clear, or_2_out, bgtz_suc);
  Hex_Digit_Display hex_digit_display_7 (.value(LedData[7:4]));  // open: dp
  Hex_Digit_Display hex_digit_display_8 (.value(LedData[3:0]));  // open: dp
  Clock #(.highDuration(1), .lowDuration(1)) clock_1 (.out(CLK));
  \确定pc  \u_确定pc_1  (
    .equal(ex_equal), .Beq(ex_Beq), .Bne(ex_Bne), .JR(ex_JR), .j(or_1_out), .out_7(\确定pc_1_out_7 ),
    .beq_bne_suc(beq_bne_suc));
  ROM #(.addrWidth(10), .dataWidth(32), .Select("high")) rom_1 (.addr(IF_PC[11:2]), .data(mips_probe_1_p1));
  and and_2 (and_2_out, LoadUse_stall, stop);
  and and_3 (bgtz_suc, not_1_out, ex_BGTZ);
  not not_1 (not_1_out, ex_Result[0]);
  IF_ID if_id_1 (
    .IR(mips_probe_1_p1), .PC(IF_PC), .IR_2({IR, address}), .PC_2(ID_PC), .clk(CLK), .clear(ex_clear),
    .WE(and_2_out));  // open: yuce_suc, yuce_suc_2
  // Probe on \总周期数 
  // Probe on \无条件分支数 
  // Probe on \条件分支成功数 
  // Probe on \插入气泡数 
  // Probe on \LoadUse次数 
  \寄存器使用情况  \u_寄存器使用情况_1  (.op(IR), .func(address[5:0]), .R1_used(R1_used), .R2_used(R2_used));
  // Mips_Probe mips_probe_2: pin names not known; wires that end beside it: {IR, address}
  // Probe on IF_PC[11:0]
  Multiplexer #(.select(1), .width(5), .disabled("Z"), .enable("false")) multiplexer_4 (
    .in0(address[25:21]), .in1(5'b00100), .out(R1_num), .sel(Syscall));
  Multiplexer #(.select(1), .width(5), .disabled("Z"), .enable("false")) multiplexer_5 (
    .in0(address[20:16]), .in1(5'b00010), .out(R2_num), .sel(Syscall));
  Multiplexer #(.select(1), .width(5), .disabled("Z"), .enable("false")) multiplexer_6 (
    .in0(address[20:16]), .in1(address[15:11]), .out(rd1), .sel(RegDst));
  Comparator #(.width(32), .mode("unsigned")) comparator_1 (
    .a(ex_R2data), .b(32'h22), .eq(comparator_1_eq));  // open: gt, lt
  // Probe on ID_PC[11:0]
  // Probe on IF_PC[11:0]
  // Probe on ID_PC[11:0]
  // Probe on EX_PC[11:0]
  \单周期硬布线控制器  \u_单周期硬布线控制器_1  (
    .Func(address[5:0]), .OP(IR), .ALU_OP(AluOp), .MemToReg(MemToReg), .MemWrite(MemWrite1),
    .ALU_SRC(AluSrcB), .RegWrite(RegWrite1), .SysCALL(Syscall), .SignedExt(SignedExt), .RegDst(RegDst),
    .JR(JR), .JMP(JMP), .Beq(Beq), .JAL(JAL), .Bne(Bne), .BGTZ(BGTZ), .LB(LB));
  not not_2 (not_2_out, comparator_1_eq);
  // Probe on EX_PC[11:0]
  // Probe on M_PC[11:0]
  \流水线mips_regifile  \u_流水线mips_regifile_1  (
    .Din(RDin), .Clk(CLK), .R1(id_R1data), .R2(id_R2data), .WE(RegWrite), .W_num(multiplexer_14_out),
    .R1_num(R1_num), .R2_num(R2_num));
  and and_4 (and_4_out, SignedExt, address[15]);
  and and_5 (and_5_out, ex_Syscall, comparator_1_eq);
  and and_6 (pause, ex_Syscall, not_2_out);
  // Probe on WB_PC[11:0]
  // Probe on M_PC[11:0]
  // Probe on WB_PC[11:0]
  assign bit_extender_1_out = {{16{and_4_out}}, address[15:0]};  // Bit_Extender bit_extender_1
  Register #(.width(32), .trigger("rising"), .Select("low")) register_1 (
    .D(ex_R1data), .en(and_5_out), .Q(LedData), .clk(CLK));  // open: clr
  Multiplexer #(.select(1), .width(5), .disabled("Z"), .enable("false")) multiplexer_7 (
    .in0(rd1), .in1({5{1'b1}}), .out(multiplexer_7_out), .sel(JAL));
  ID_EX id_ex_1 (
    .JMP(JMP), .AluSrcB(AluSrcB), .JR(JR), .RegWrite(RegWrite1), .IR({IR, address}), .syscall(Syscall),
    .JAL(JAL), .BGTZ(BGTZ), .RegDst(RegDst), .PC(ID_PC), .pause(pause), .Beq(Beq), .A(id_R1data), .Bne(Bne),
    .R2data(id_R2data), .MemWrite(MemWrite1), .AluOP(AluOp), .IMM(bit_extender_1_out), .out_32(ex_JMP),
    .out_33(id_ex_1_out_33), .out_35(ex_JR), .out_36(ex_regwrite), .IR_2({id_ex_1_ir_2, ex_jmppc[27:2]}),
    .out_38(ex_Syscall), .out_39(ex_JAL), .out_40(ex_BGTZ), .out_41(id_ex_1_out_41), .PC_2(EX_PC),
    .out_44(id_ex_1_out_44), .A_2(id_ex_1_a_2), .out_46(ex_Beq), .out_48(ex_Bne),
    .R2data_2(id_ex_1_r2data_2), .out_50(id_ex_1_out_50), .out_51(id_ex_1_out_51), .IMM_2(id_ex_1_imm_2),
    .clk(CLK), .clear(or_4_out), .out_47(ex_MemToReg), .MemToReg(MemToReg), .shamt(address[10:6]),
    .out_30(id_ex_1_out_30), .rd(multiplexer_7_out), .rd_2(ex_rd), .WE(stop), .R1_num(R1_num),
    .R2_num(R2_num), .R1_num_2(EX_R1_num), .R2_num_2(EX_R2_num));  // open: LB, out_43, yuce_suc, yuce_suc_2
  not not_3 (not_3_out, LoadUse_stall);
  \数据相关检测逻辑子电路  \u_数据相关检测逻辑子电路_1  (
    .R1_num(R1_num), .R2_num(R2_num), .EX_WriteReg_num(ex_rd), .MEM_WriteReg_num(mem_rd), .R1_Used(R1_used),
    .R2_Used(R2_used), .ex_RegWrite(ex_regwrite), .mem_RegWrite(mem_regwrite), .LoadUse_stall(LoadUse_stall),
    .ex_MemToReg(ex_MemToReg));  // open: stall
  Shifter #(.width(32), .shift("ll")) shifter_1 (.in(id_ex_1_imm_2), .\dist (5'b00010), .out(shifter_1_out));
  or or_4 (or_4_out, ex_clear, not_3_out);
  Adder #(.width(32)) adder_2 (
    .a(shifter_1_out), .b({ex_jmppc[31:28], ex_nextpc}), .out(ex_pcbranch));  // open: cin, cout
  Multiplexer #(.select(2), .width(32), .disabled("Z"), .enable("false")) multiplexer_8 (
    .in0(id_ex_1_a_2), .in1(RDin), .in2(RDin), .in3(mem_alu), .out(ex_R1data), .sel(a_f));
  Multiplexer #(.select(2), .width(32), .disabled("Z"), .enable("false")) multiplexer_9 (
    .in0(id_ex_1_r2data_2), .in1(RDin), .in2(RDin), .in3(mem_alu), .out(ex_R2data), .sel(b_f));
  Multiplexer #(.select(1), .width(32), .disabled("Z"), .enable("false")) multiplexer_10 (
    .in0(ex_R2data), .in1(id_ex_1_imm_2), .out(multiplexer_10_out), .sel(id_ex_1_out_33));
  Adder #(.width(32)) adder_3 (.a(EX_PC), .b(32'h4), .out({ex_jmppc[31:28], ex_nextpc}));  // open: cin, cout
  // Mips_Probe mips_probe_3: pin names not known; wires that end beside it: {id_ex_1_ir_2, ex_jmppc[27:2]}
  \寄存器使用情况  \u_寄存器使用情况_2  (
    .op(id_ex_1_ir_2), .func(ex_jmppc[7:2]), .R1_used(\寄存器使用情况_2_r1_used ), .R2_used(\寄存器使用情况_2_r2_used ));
  \重定向forward  \u_重定向forward_1  (
    .ex_R1_num(EX_R1_num), .ex_R2_num(EX_R2_num), .mem_rd_num(mem_rd), .wb_rd_num(multiplexer_14_out),
    .forward_a(a_f), .forward_b(b_f), .ex_R1_used(\寄存器使用情况_2_r1_used ), .ex_R2_used(\寄存器使用情况_2_r2_used ),
    .mem_regwrite(mem_regwrite), .wb_regwrite(RegWrite));
  MIPS_ALU mips_alu_1 (
    .X(ex_R1data), .Y(multiplexer_10_out), .AluOP(id_ex_1_out_51), .Equal(ex_equal), .Result(ex_Result),
    .shamt(id_ex_1_out_30));  // open: Result_2
  Counter #(.width(16), .max('hffff), .ongoal("wrap"), .trigger("rising"), .behavior("new")) counter_1 (
    .count(stop), .Q(\总周期数 ), .clk(CLK));  // open: load, D, carry, clr, preset, down
  Counter #(.width(16), .max('hffff), .ongoal("wrap"), .trigger("rising"), .behavior("old")) counter_2 (
    .count(not_4_out), .Q(\LoadUse次数 ), .clk(CLK));  // open: load, D, carry, clr, preset
  not not_4 (not_4_out, LoadUse_stall);
  EX_MEM ex_mem_1 (
    .IR({id_ex_1_ir_2, ex_jmppc[27:2]}), .PC(EX_PC), .MemToReg(ex_MemToReg), .MemWrite(id_ex_1_out_50),
    .R2Data(ex_R2data), .RegWrite(ex_regwrite), .JAL(ex_JAL), .ALU(ex_Result), .RegDst(id_ex_1_out_41),
    .pause(id_ex_1_out_44), .IR_2(ex_mem_1_ir_2), .PC_2(M_PC), .out_32(ex_mem_1_out_32), .out_33(MemWrite),
    .R2data_2(MDin), .out_36(mem_regwrite), .out_37(ex_mem_1_out_37), .ALU_2(mem_alu),
    .out_39(ex_mem_1_out_39), .out_40(ex_mem_1_out_40), .clk(CLK), .rd(ex_rd), .rd_2(mem_rd), .WE(stop));  // open: JMP, JR, SignedExt, BGTZ, LB, Beq, Bne, AluSrcB, out_23, out_24, out_25, out_26, out_27, out_29, out_30, out_35, clear
  // Mips_Probe mips_probe_4: pin names not known; wires that end beside it: ex_mem_1_ir_2
  Counter #(.width(16), .max('hffff), .ongoal("wrap"), .trigger("rising"), .behavior("old")) counter_3 (
    .count(or_5_out), .Q(\条件分支成功数 ), .clk(CLK));  // open: load, D, carry, clr, preset
  or or_5 (or_5_out, beq_bne_suc, bgtz_suc);
  Counter #(.width(16), .max('hffff), .ongoal("wrap"), .trigger("rising"), .behavior("old")) counter_4 (
    .count(or_6_out), .Q(\无条件分支数 ), .clk(CLK));  // open: load, D, carry, clr, preset
  or or_6 (or_6_out, ex_JMP, ex_JR, ex_JAL);
  RAM #(.addrWidth(10), .dataWidth(32), .bus("separate"), .Select("high")) ram_1 (
    .addr(mem_alu[11:2]), .din(MDin), .data(ram_1_data), .str(MemWrite), .clk(CLK));  // open: sel, ld, clr
  MEM_WB mem_wb_1 (
    .IR(ex_mem_1_ir_2), .PC(M_PC), .ALU(mem_alu), .MD(ram_1_data), .MemToReg(ex_mem_1_out_32),
    .IR_2(mem_wb_1_ir_2), .PC_2(WB_PC), .ALU_2(mem_wb_1_alu_2), .MD_2(mem_wb_1_md_2),
    .out_23(mem_wb_1_out_23), .CLK(CLK), .Regwrite(mem_regwrite), .out_21(RegWrite), .rd(mem_rd),
    .rd_2(mem_wb_1_rd_2), .RegDst(ex_mem_1_out_39), .out_18(mem_wb_1_out_18), .WE(stop),
    .jal(ex_mem_1_out_37), .out_17(mem_wb_1_out_17), .pause(ex_mem_1_out_40), .out_15(WB_pause));  // open: CLEAR
  // Mips_Probe mips_probe_5: pin names not known; wires that end beside it: mem_wb_1_ir_2
  Multiplexer #(.select(1), .width(32), .disabled("Z"), .enable("false")) multiplexer_11 (
    .in0(mem_wb_1_alu_2), .in1(mem_wb_1_md_2), .out(multiplexer_11_out), .sel(mem_wb_1_out_23));
  Multiplexer #(.select(1), .width(32), .disabled("Z"), .enable("false")) multiplexer_12 (
    .in0(multiplexer_11_out), .in1(adder_4_out), .out(RDin), .sel(mem_wb_1_out_17));
  Adder #(.width(32)) adder_4 (.a(WB_PC), .b(32'h4), .out(adder_4_out));  // open: cin, cout
  Multiplexer #(.select(1), .width(5), .disabled("Z"), .enable("false")) multiplexer_13 (
    .in0(mem_wb_1_ir_2[20:16]), .in1(mem_wb_1_rd_2), .out(multiplexer_13_out), .sel(mem_wb_1_out_18));
  Multiplexer #(.select(1), .width(5), .disabled("Z"), .enable("false")) multiplexer_14 (
    .in0(multiplexer_13_out), .in1({5{1'b1}}), .out(multiplexer_14_out), .sel(mem_wb_1_out_17));

  // Other names for the same wires on the sheet: ex_nextpc[31:28] = ex_jmppc[31:28]; IR[25:0] = address;
  //   shamt[4:0] = address[10:6]; MEM_PC[31:0] = M_PC; PC[31:0] = ID_PC; wb_data[31:0] = RDin

  // Notes on the sheet:
  //   中断源
  //   中断等待指示
  //   数码管输出
  //   IF
  //   传入的pc是下一条指令的pc地址
  //   指令存储器
  //   contents of rom_1 (hex, n*v repeats v):
  //   20110001 8000c05 20110001 20120002 20130003 8000c09 20110001 20120002 20130003 8000c0d 20110001
  //   20120002 20130003 8000c11 20110001 20120002 20130003 c000cb8 20100001 20110001 118fc0 112020
  //   20020022 c 118882 12200001 8000c15 112020 20020022 c 20110001 118880 112020 20020022 c 12200001
  //   8000c1f 20110001 118fc0 112020 20020022 c 1188c3 112020 20020022 c 118903 112020 20020022 c 118903
  //   112020 20020022 c 118903 112020 20020022 c 118903 112020 20020022 c 118903 112020 20020022 c 118903
  //   112020 20020022 c 118903 112020 20020022 c 20100001 109fc0 139fc3 8021 2012000c 24160003 26100001
  //   3210000f 20080008 20090001 139900 2709825 132020 20020022 c 1094022 1500fff9 22100001 2018000f
  //   2188024 108700 20080008 20090001 139902 2709825 132021 20020022 c 1094022 1500fff9 108702 2c9b022
  //   12c00001 8000c50 4020 1084027 84400 3508ffff 82021 20020022 c 2010ffff 20110000 ae300000 22100001
  //   22310004 ae300000 22100001 22310004 ae300000 22100001 22310004 ae300000 22100001 22310004 ae300000
  //   22100001 22310004 ae300000 22100001 22310004 ae300000 22100001 22310004 ae300000 22100001 22310004
  //   ae300000 22100001 22310004 ae300000 22100001 22310004 ae300000 22100001 22310004 ae300000 22100001
  //   22310004 ae300000 22100001 22310004 ae300000 22100001 22310004 ae300000 22100001 22310004 ae300000
  //   22100001 22310004 22100001 8020 2011003c 8e130000 8e340000 274402a 11000002 ae330000 ae140000
  //   2231fffc 1611fff8 102020 20020022 c 22100004 2011003c 1611fff2 20020032 c 20100000 22100001 102020
  //   20020022 c 22100002 102020 20020022 c 22100003 102020 20020022 c 22100004 102020 20020022 c 22100005
  //   102020 20020022 c 22100006 102020 20020022 c 22100007 102020 20020022 c 22100008 102020 20020022
  //   20020022 c 3e00008
  //   rs
  //   指令字
  //   rt
  //   rd
  //   ID
  //   OP
  //   Func
  //   流水调试日志用
  //   低电平表示冲突
  //   取非高电平表示冲突
  //   为方便自动评测，需要输出流水线各段保存的PC值，注意是PC不是PC+4，另外ID段寄存器写入信息，Mem段内存写入信息也要输出
  //   执行
  //   EX
  //   MEM
  //   WB
endmodule

module \理想流水线  (
  output RegWrite,
  output MemWrite,
  output [31:0] IF_PC,
  output [31:0] ID_PC,
  output [31:0] EX_PC,
  output [31:0] M_PC,
  output [31:0] WB_PC,
  output [31:0] RDin,
  output [31:0] MDin,
  output [31:0] LedData
);

  wire and_1_out, and_2_out, CLK, comparator_1_eq, ex_mem_1_out_32, ex_mem_1_out_36, ex_mem_1_out_40, Go,
       id_ex_1_out_33, id_ex_1_out_36, id_ex_1_out_44, id_ex_1_out_47, id_ex_1_out_50, IR1, IR2, IR3,
       mem_wb_1_out_23, not_1_out, pause, RST, SignedExt, stop, Syscall, W1, W2, W3, WB_pause,
       \单周期硬布线控制器_1_alu_src , \单周期硬布线控制器_1_memtoreg , \单周期硬布线控制器_1_memwrite , \单周期硬布线控制器_1_regwrite ;
  wire [3:0] id_ex_1_out_51, \单周期硬布线控制器_1_alu_op ;
  wire [4:0] ex_mem_1_rd_2, id_ex_1_out_30, id_ex_1_rd_2, mem_wb_1_rd_2, multiplexer_1_out, multiplexer_2_out;
  wire [9:0] ex_mem_1_alu_2_2;
  wire [15:0] \LoadUse次数 , \总周期数 , \插入气泡数 , \无条件分支数 , \条件分支成功数 ;
  wire [25:0] address;
  wire [31:0] adder_1_out, bit_extender_1_out, ex_mem_1_alu_2, ex_mem_1_ir_2, id_ex_1_a_2, id_ex_1_imm_2,
       id_ex_1_ir_2, id_ex_1_r2data_2, mem_wb_1_alu_2, mem_wb_1_md_2, mips_alu_1_result, multiplexer_3_out,
       R1data, R2data, ram_1_data, rom_1_data;
  wire [31:26] IR;

  Button \u_总复位  (.out(RST));
  Button _1 (.out(IR1));
  Button _2 (.out(IR2));
  Button _3 (.out(IR3));
  Button \u_继续运行  (.out(Go));
  LED #(.active("true")) led_1 (.in(W1));
  LED #(.active("true")) led_2 (.in(W2));
  LED #(.active("true")) led_3 (.in(W3));
  D_Flip_Flop #(.trigger("falling"), .Pre_Clr_Positions("ABOVE_BELOW"), .NegatePresetClear("false"), .enable("false"), .NewFFLayout("true")) d_ff_1 (
    .clk(CLK), .D(WB_pause), .Qn(stop), .reset(Go));  // open: Q, preset
  Hex_Digit_Display hex_digit_display_1 (.value(LedData[27:24]));  // open: dp
  Hex_Digit_Display hex_digit_display_2 (.value(LedData[31:28]));  // open: dp
  Register #(.width(32), .trigger("rising"), .Select("low")) PC (
    .D(adder_1_out), .en(stop), .Q(IF_PC), .clk(CLK));  // open: clr
  Hex_Digit_Display hex_digit_display_3 (.value(LedData[23:20]));  // open: dp
  Hex_Digit_Display hex_digit_display_4 (.value(LedData[19:16]));  // open: dp
  Adder #(.width(32)) adder_1 (.a(32'h4), .b(IF_PC), .out(adder_1_out));  // open: cin, cout
  Hex_Digit_Display hex_digit_display_5 (.value(LedData[11:8]));  // open: dp
  Hex_Digit_Display hex_digit_display_6 (.value(LedData[15:12]));  // open: dp
  Hex_Digit_Display hex_digit_display_7 (.value(LedData[3:0]));  // open: dp
  Hex_Digit_Display hex_digit_display_8 (.value(LedData[7:4]));  // open: dp
  Clock #(.highDuration(1), .lowDuration(1)) clock_1 (.out(CLK));
  ROM #(.addrWidth(10), .dataWidth(32), .Select("high")) rom_1 (.addr(IF_PC[11:2]), .data(rom_1_data));
  IF_ID if_id_1 (
    .IR(rom_1_data), .PC(IF_PC), .IR_2({IR, address}), .PC_2(ID_PC), .clk(CLK), .WE(stop));  // open: clear, yuce_suc, yuce_suc_2
  // Probe on \总周期数 
  // Probe on \无条件分支数 
  // Probe on \条件分支成功数 
  // Probe on \插入气泡数 
  // Probe on \LoadUse次数 
  Comparator #(.width(32), .mode("unsigned")) comparator_1 (
    .a(R2data), .b(32'h22), .eq(comparator_1_eq));  // open: gt, lt
  // Probe on IF_PC[11:0]
  \单周期硬布线控制器  \u_单周期硬布线控制器_1  (
    .Func(address[5:0]), .OP(IR), .ALU_OP(\单周期硬布线控制器_1_alu_op ), .MemToReg(\单周期硬布线控制器_1_memtoreg ),
    .MemWrite(\单周期硬布线控制器_1_memwrite ), .ALU_SRC(\单周期硬布线控制器_1_alu_src ), .RegWrite(\单周期硬布线控制器_1_regwrite ),
    .SysCALL(Syscall), .SignedExt(SignedExt));  // open: RegDst, JR, JMP, Beq, JAL, Bne, BGTZ, LB
  Multiplexer #(.select(1), .width(5), .disabled("Z"), .enable("false")) multiplexer_1 (
    .in0(address[25:21]), .in1(5'b00100), .out(multiplexer_1_out), .sel(Syscall));
  Multiplexer #(.select(1), .width(5), .disabled("Z"), .enable("false")) multiplexer_2 (
    .in0(address[20:16]), .in1(5'b00010), .out(multiplexer_2_out), .sel(Syscall));
  not not_1 (not_1_out, comparator_1_eq);
  // Probe on EX_PC[11:0]
  // Probe on ID_PC[11:0]
  and and_1 (and_1_out, SignedExt, address[15]);
  and and_2 (and_2_out, Syscall, comparator_1_eq);
  and and_3 (pause, Syscall, not_1_out);
  // Probe on M_PC[11:0]
  \流水线mips_regifile  \u_流水线mips_regifile_1  (
    .Din(RDin), .Clk(CLK), .R1(R1data), .R2(R2data), .WE(RegWrite), .W_num(mem_wb_1_rd_2),
    .R1_num(multiplexer_1_out), .R2_num(multiplexer_2_out));
  assign bit_extender_1_out = {{16{and_1_out}}, address[15:0]};  // Bit_Extender bit_extender_1
  Register #(.width(32), .trigger("rising"), .Select("low")) register_1 (
    .D(R1data), .en(and_2_out), .Q(LedData), .clk(CLK));  // open: clr
  // Probe on WB_PC[11:0]
  ID_EX id_ex_1 (
    .AluSrcB(\单周期硬布线控制器_1_alu_src ), .RegWrite(\单周期硬布线控制器_1_regwrite ), .IR({IR, address}), .PC(ID_PC),
    .pause(pause), .A(R1data), .R2data(R2data), .MemWrite(\单周期硬布线控制器_1_memwrite ),
    .AluOP(\单周期硬布线控制器_1_alu_op ), .IMM(bit_extender_1_out), .out_33(id_ex_1_out_33), .out_36(id_ex_1_out_36),
    .IR_2(id_ex_1_ir_2), .PC_2(EX_PC), .out_44(id_ex_1_out_44), .A_2(id_ex_1_a_2),
    .R2data_2(id_ex_1_r2data_2), .out_50(id_ex_1_out_50), .out_51(id_ex_1_out_51), .IMM_2(id_ex_1_imm_2),
    .clk(CLK), .out_47(id_ex_1_out_47), .MemToReg(\单周期硬布线控制器_1_memtoreg ), .shamt(address[10:6]),
    .out_30(id_ex_1_out_30), .rd(address[20:16]), .rd_2(id_ex_1_rd_2), .WE(stop));  // open: JMP, JR, syscall, JAL, BGTZ, RegDst, LB, Beq, Bne, out_32, out_35, out_38, out_39, out_40, out_41, out_43, out_46, out_48, clear, R1_num, R2_num, R1_num_2, R2_num_2, yuce_suc, yuce_suc_2
  Multiplexer #(.select(1), .width(32), .disabled("Z"), .enable("false")) multiplexer_3 (
    .in0(id_ex_1_r2data_2), .in1(id_ex_1_imm_2), .out(multiplexer_3_out), .sel(id_ex_1_out_33));
  MIPS_ALU mips_alu_1 (
    .X(id_ex_1_a_2), .Y(multiplexer_3_out), .AluOP(id_ex_1_out_51), .Result(mips_alu_1_result),
    .shamt(id_ex_1_out_30));  // open: Equal, Result_2
  EX_MEM ex_mem_1 (
    .IR(id_ex_1_ir_2), .PC(EX_PC), .MemToReg(id_ex_1_out_47), .MemWrite(id_ex_1_out_50),
    .R2Data(id_ex_1_r2data_2), .RegWrite(id_ex_1_out_36), .ALU(mips_alu_1_result), .pause(id_ex_1_out_44),
    .IR_2(ex_mem_1_ir_2), .PC_2(M_PC), .out_32(ex_mem_1_out_32), .out_33(MemWrite), .R2data_2(MDin),
    .out_36(ex_mem_1_out_36), .ALU_2({ex_mem_1_alu_2[31:12], ex_mem_1_alu_2_2, ex_mem_1_alu_2[1:0]}),
    .out_40(ex_mem_1_out_40), .clk(CLK), .rd(id_ex_1_rd_2), .rd_2(ex_mem_1_rd_2), .WE(stop));  // open: JMP, JR, SignedExt, BGTZ, LB, Beq, Bne, AluSrcB, JAL, RegDst, out_23, out_24, out_25, out_26, out_27, out_29, out_30, out_35, out_37, out_39, clear
  RAM #(.addrWidth(10), .dataWidth(32), .bus("separate"), .Select("high")) ram_1 (
    .addr(ex_mem_1_alu_2_2), .din(MDin), .data(ram_1_data), .str(MemWrite), .clk(CLK));  // open: sel, ld, clr
  MEM_WB mem_wb_1 (
    .IR(ex_mem_1_ir_2), .PC(M_PC), .ALU({ex_mem_1_alu_2[31:12], ex_mem_1_alu_2_2, ex_mem_1_alu_2[1:0]}),
    .MD(ram_1_data), .MemToReg(ex_mem_1_out_32), .PC_2(WB_PC), .ALU_2(mem_wb_1_alu_2), .MD_2(mem_wb_1_md_2),
    .out_23(mem_wb_1_out_23), .CLK(CLK), .Regwrite(ex_mem_1_out_36), .out_21(RegWrite), .rd(ex_mem_1_rd_2),
    .rd_2(mem_wb_1_rd_2), .WE(stop), .pause(ex_mem_1_out_40), .out_15(WB_pause));  // open: IR_2, CLEAR, RegDst, out_18, jal, out_17
  Multiplexer #(.select(1), .width(32), .disabled("Z"), .enable("false")) multiplexer_4 (
    .in0(mem_wb_1_alu_2), .in1(mem_wb_1_md_2), .out(RDin), .sel(mem_wb_1_out_23));
  Counter #(.width(16), .max('hffff), .ongoal("wrap"), .trigger("rising"), .behavior("new")) counter_1 (
    .count(stop), .Q(\总周期数 ), .clk(CLK));  // open: load, D, carry, clr, preset, down

  // Other names for the same wires on the sheet: IR[25:0] = address; shamt[4:0] = address[10:6];
  //   rd[4:0] = address[20:16]; MEM_PC[31:0] = M_PC; PC[31:0] = ID_PC

  // Notes on the sheet:
  //   中断源
  //   中断等待指示
  //   IF
  //   数码管输出
  //   指令存储器
  //   contents of rom_1 (hex, n*v repeats v):
  //   20100000 20110000 20120000 20130000 36100000 36310001 36520002 36730003 ae100000 ae110004 ae120008
  //   ae13000c 2002000a 20110000 20120000 20130000 c
  //   指令字
  //   OP
  //   Func
  //   Func
  //   rs
  //   rt
  //   rd
  //   ID
  //   流水调试日志用
  //   EX
  //   执行
  //   为方便自动评测，需要输出流水线各段保存的PC值，注意是PC不是PC+4，另外ID段寄存器写入信息，Mem段内存写入信息也要输出
  //   MEM
  //   WB
endmodule

module \气泡流水线  (
  output RegWrite,
  output MemWrite,
  output [31:0] IF_PC,
  output [31:0] ID_PC,
  output [31:0] EX_PC,
  output [31:0] M_PC,
  output [31:0] WB_PC,
  output [31:0] RDin,
  output [31:0] MDin,
  output [31:0] LedData
);

  wire AluSrcB, and_1_out, and_3_out, and_4_out, and_5_out, Beq, beq_bne_suc, BGTZ, bgtz_suc, Bne, CLK,
       comparator_1_eq, ex_Beq, ex_BGTZ, ex_Bne, ex_clear, ex_equal, ex_JAL, ex_JMP, ex_JR, ex_mem_1_out_32,
       ex_mem_1_out_37, ex_mem_1_out_39, ex_mem_1_out_40, ex_regwrite, Go, id_ex_1_out_33, id_ex_1_out_41,
       id_ex_1_out_44, id_ex_1_out_47, id_ex_1_out_50, IR1, IR2, IR3, JAL, JMP, JR, LB, mem_regwrite,
       mem_wb_1_out_17, mem_wb_1_out_18, mem_wb_1_out_23, MemToReg, MemWrite1, not_1_out, not_2_out,
       not_3_out, or_1_out, or_2_out, or_4_out, or_5_out, or_6_out, pause, R1_used, R2_used, RegDst,
       RegWrite1, RST, SignedExt, stall, stop, Syscall, W1, W2, W3, WB_pause;
  wire [1:0] \确定pc_1_out_7 ;
  wire [3:0] AluOp, id_ex_1_out_51;
  wire [4:0] ex_rd, id_ex_1_out_30, mem_rd, mem_wb_1_rd_2, multiplexer_7_out, multiplexer_11_out,
       multiplexer_12_out, R1_num, R2_num, rd1;
  wire [15:0] \LoadUse次数 , \总周期数 , \插入气泡数 , \无条件分支数 , \条件分支成功数 ;
  wire [25:0] address;
  wire [27:0] ex_nextpc;
  wire [31:0] adder_4_out, bit_extender_1_out, ex_mem_1_alu_2, ex_mem_1_ir_2, ex_pcbranch, ex_R1data,
       ex_Result, id_ex_1_imm_2, id_ex_1_r2data_2, id_R1data, id_R2data, if_nextpc, mem_wb_1_alu_2,
       mem_wb_1_ir_2, mem_wb_1_md_2, mips_probe_1_p1, multiplexer_1_out, multiplexer_2_out,
       multiplexer_3_out, multiplexer_8_out, multiplexer_9_out, ram_1_data, shifter_1_out;
  wire [31:2] ex_jmppc;
  wire [31:26] id_ex_1_ir_2, IR;

  Button \u_总复位  (.out(RST));
  Button _1 (.out(IR1));
  Button _2 (.out(IR2));
  Button _3 (.out(IR3));
  Button \u_继续运行  (.out(Go));
  LED #(.active("true")) led_1 (.in(W1));
  LED #(.active("true")) led_2 (.in(W2));
  LED #(.active("true")) led_3 (.in(W3));
  and and_1 (and_1_out, stop, stall);
  D_Flip_Flop #(.trigger("falling"), .Pre_Clr_Positions("ABOVE_BELOW"), .NegatePresetClear("false"), .enable("false"), .NewFFLayout("true")) d_ff_1 (
    .clk(CLK), .D(WB_pause), .Qn(stop), .reset(Go));  // open: Q, preset
  Hex_Digit_Display hex_digit_display_1 (.value(LedData[27:24]));  // open: dp
  Hex_Digit_Display hex_digit_display_2 (.value(LedData[31:28]));  // open: dp
  Register #(.width(32), .trigger("rising"), .Select("low")) PC (
    .D(multiplexer_1_out), .en(and_1_out), .Q(IF_PC), .clk(CLK));  // open: clr
  Multiplexer #(.select(1), .width(32), .disabled("Z"), .enable("false")) multiplexer_1 (
    .in0(if_nextpc), .in1(multiplexer_2_out), .out(multiplexer_1_out), .sel(ex_clear));
  Multiplexer #(.select(1), .width(32), .disabled("Z"), .enable("false")) multiplexer_2 (
    .in0(multiplexer_3_out), .in1(ex_pcbranch), .out(multiplexer_2_out), .sel(bgtz_suc));
  Multiplexer #(.select(2), .width(32), .disabled("Z"), .enable("false")) multiplexer_3 (
    .in0(ex_pcbranch), .in1({ex_jmppc[31:28], ex_nextpc}), .in2(ex_R1data), .in3({ex_jmppc, 2'b00}),
    .out(multiplexer_3_out), .sel(\确定pc_1_out_7 ));
  Hex_Digit_Display hex_digit_display_3 (.value(LedData[23:20]));  // open: dp
  Hex_Digit_Display hex_digit_display_4 (.value(LedData[19:16]));  // open: dp
  Adder #(.width(32)) adder_1 (.a(32'h4), .b(IF_PC), .out(if_nextpc));  // open: cin, cout
  or or_1 (or_1_out, ex_JMP, ex_JAL);
  Hex_Digit_Display hex_digit_display_5 (.value(LedData[11:8]));  // open: dp
  Hex_Digit_Display hex_digit_display_6 (.value(LedData[15:12]));  // open: dp
  or or_2 (or_2_out, or_1_out, beq_bne_suc, ex_JR);
  or or_3 (ex_clear, or_2_out, bgtz_suc);
  Hex_Digit_Display hex_digit_display_7 (.value(LedData[3:0]));  // open: dp
  Hex_Digit_Display hex_digit_display_8 (.value(LedData[7:4]));  // open: dp
  Clock #(.highDuration(1), .lowDuration(1)) clock_1 (.out(CLK));
  // Mips_Probe mips_probe_1: pin names not known; wires that end beside it: mips_probe_1_p1
  ROM #(.addrWidth(10), .dataWidth(32), .Select("high")) rom_1 (.addr(IF_PC[11:2]), .data(mips_probe_1_p1));
  \确定pc  \u_确定pc_1  (
    .equal(ex_equal), .Beq(ex_Beq), .Bne(ex_Bne), .JR(ex_JR), .j(or_1_out), .out_7(\确定pc_1_out_7 ),
    .beq_bne_suc(beq_bne_suc));
  and and_2 (bgtz_suc, not_1_out, ex_BGTZ);
  not not_1 (not_1_out, ex_Result[0]);
  // Mips_Probe mips_probe_2: pin names not known; wires that end beside it: {IR, address}
  IF_ID if_id_1 (
    .IR(mips_probe_1_p1), .PC(IF_PC), .IR_2({IR, address}), .PC_2(ID_PC), .clk(CLK), .clear(ex_clear),
    .WE(and_3_out));  // open: yuce_suc, yuce_suc_2
  and and_3 (and_3_out, stall, stop);
  \寄存器使用情况  \u_寄存器使用情况_1  (.op(IR), .func(address[5:0]), .R1_used(R1_used), .R2_used(R2_used));
  // Probe on \总周期数 
  // Probe on \无条件分支数 
  // Probe on \条件分支成功数 
  // Probe on \插入气泡数 
  // Probe on \LoadUse次数 
  Comparator #(.width(32), .mode("unsigned")) comparator_1 (
    .a(id_R2data), .b(32'h22), .eq(comparator_1_eq));  // open: gt, lt
  // Probe on IF_PC[11:0]
  // Probe on IF_PC[11:0]
  \单周期硬布线控制器  \u_单周期硬布线控制器_1  (
    .Func(address[5:0]), .OP(IR), .ALU_OP(AluOp), .MemToReg(MemToReg), .MemWrite(MemWrite1),
    .ALU_SRC(AluSrcB), .RegWrite(RegWrite1), .SysCALL(Syscall), .SignedExt(SignedExt), .RegDst(RegDst),
    .JR(JR), .JMP(JMP), .Beq(Beq), .JAL(JAL), .Bne(Bne), .BGTZ(BGTZ), .LB(LB));
  Multiplexer #(.select(1), .width(5), .disabled("Z"), .enable("false")) multiplexer_4 (
    .in0(address[25:21]), .in1(5'b00100), .out(R1_num), .sel(Syscall));
  Multiplexer #(.select(1), .width(5), .disabled("Z"), .enable("false")) multiplexer_5 (
    .in0(address[20:16]), .in1(5'b00010), .out(R2_num), .sel(Syscall));
  Multiplexer #(.select(1), .width(5), .disabled("Z"), .enable("false")) multiplexer_6 (
    .in0(address[20:16]), .in1(address[15:11]), .out(rd1), .sel(RegDst));
  not not_2 (not_2_out, comparator_1_eq);
  // Probe on EX_PC[11:0]
  // Probe on ID_PC[11:0]
  // Probe on ID_PC[11:0]
  // Probe on EX_PC[11:0]
  and and_4 (and_4_out, SignedExt, address[15]);
  and and_5 (and_5_out, Syscall, comparator_1_eq);
  and and_6 (pause, Syscall, not_2_out);
  // Probe on M_PC[11:0]
  // Probe on M_PC[11:0]
  \流水线mips_regifile  \u_流水线mips_regifile_1  (
    .Din(RDin), .Clk(CLK), .R1(id_R1data), .R2(id_R2data), .WE(RegWrite), .W_num(multiplexer_12_out),
    .R1_num(R1_num), .R2_num(R2_num));
  assign bit_extender_1_out = {{16{and_4_out}}, address[15:0]};  // Bit_Extender bit_extender_1
  Register #(.width(32), .trigger("rising"), .Select("low")) register_1 (
    .D(id_R1data), .en(and_5_out), .Q(LedData), .clk(CLK));  // open: clr
  // Probe on WB_PC[11:0]
  // Probe on WB_PC[11:0]
  Multiplexer #(.select(1), .width(5), .disabled("Z"), .enable("false")) multiplexer_7 (
    .in0(rd1), .in1({5{1'b1}}), .out(multiplexer_7_out), .sel(JAL));
  ID_EX id_ex_1 (
    .JMP(JMP), .AluSrcB(AluSrcB), .JR(JR), .RegWrite(RegWrite1), .IR({IR, address}), .JAL(JAL), .BGTZ(BGTZ),
    .RegDst(RegDst), .PC(ID_PC), .pause(pause), .Beq(Beq), .A(id_R1data), .Bne(Bne), .R2data(id_R2data),
    .MemWrite(MemWrite1), .AluOP(AluOp), .IMM(bit_extender_1_out), .out_32(ex_JMP), .out_33(id_ex_1_out_33),
    .out_35(ex_JR), .out_36(ex_regwrite), .IR_2({id_ex_1_ir_2, ex_jmppc[27:2]}), .out_39(ex_JAL),
    .out_40(ex_BGTZ), .out_41(id_ex_1_out_41), .PC_2(EX_PC), .out_44(id_ex_1_out_44), .A_2(ex_R1data),
    .out_46(ex_Beq), .out_48(ex_Bne), .R2data_2(id_ex_1_r2data_2), .out_50(id_ex_1_out_50),
    .out_51(id_ex_1_out_51), .IMM_2(id_ex_1_imm_2), .clk(CLK), .clear(or_4_out), .out_47(id_ex_1_out_47),
    .MemToReg(MemToReg), .shamt(address[10:6]), .out_30(id_ex_1_out_30), .rd(multiplexer_7_out),
    .rd_2(ex_rd), .WE(stop));  // open: syscall, LB, out_38, out_43, R1_num, R2_num, R1_num_2, R2_num_2, yuce_suc, yuce_suc_2
  Shifter #(.width(32), .shift("ll")) shifter_1 (.in(id_ex_1_imm_2), .\dist (5'b00010), .out(shifter_1_out));
  or or_4 (or_4_out, ex_clear, not_3_out);
  not not_3 (not_3_out, stall);
  \数据相关检测逻辑子电路  \u_数据相关检测逻辑子电路_1  (
    .R1_num(R1_num), .R2_num(R2_num), .EX_WriteReg_num(ex_rd), .MEM_WriteReg_num(mem_rd), .stall(stall),
    .R1_Used(R1_used), .R2_Used(R2_used), .ex_RegWrite(ex_regwrite), .mem_RegWrite(mem_regwrite));  // open: LoadUse_stall, ex_MemToReg
  Multiplexer #(.select(1), .width(32), .disabled("Z"), .enable("false")) multiplexer_8 (
    .in0(id_ex_1_r2data_2), .in1(id_ex_1_imm_2), .out(multiplexer_8_out), .sel(id_ex_1_out_33));
  Adder #(.width(32)) adder_2 (
    .a(shifter_1_out), .b({ex_jmppc[31:28], ex_nextpc}), .out(ex_pcbranch));  // open: cin, cout
  MIPS_ALU mips_alu_1 (
    .X(ex_R1data), .Y(multiplexer_8_out), .AluOP(id_ex_1_out_51), .Equal(ex_equal), .Result(ex_Result),
    .shamt(id_ex_1_out_30));  // open: Result_2
  Adder #(.width(32)) adder_3 (.a(EX_PC), .b(32'h4), .out({ex_jmppc[31:28], ex_nextpc}));  // open: cin, cout
  // Mips_Probe mips_probe_3: pin names not known; wires that end beside it: {id_ex_1_ir_2, ex_jmppc[27:2]}
  Counter #(.width(16), .max('hffff), .ongoal("wrap"), .trigger("rising"), .behavior("new")) counter_1 (
    .count(stop), .Q(\总周期数 ), .clk(CLK));  // open: load, D, carry, clr, preset, down
  EX_MEM ex_mem_1 (
    .IR({id_ex_1_ir_2, ex_jmppc[27:2]}), .PC(EX_PC), .MemToReg(id_ex_1_out_47), .MemWrite(id_ex_1_out_50),
    .R2Data(id_ex_1_r2data_2), .RegWrite(ex_regwrite), .JAL(ex_JAL), .ALU(ex_Result),
    .RegDst(id_ex_1_out_41), .pause(id_ex_1_out_44), .IR_2(ex_mem_1_ir_2), .PC_2(M_PC),
    .out_32(ex_mem_1_out_32), .out_33(MemWrite), .R2data_2(MDin), .out_36(mem_regwrite),
    .out_37(ex_mem_1_out_37), .ALU_2(ex_mem_1_alu_2), .out_39(ex_mem_1_out_39), .out_40(ex_mem_1_out_40),
    .clk(CLK), .rd(ex_rd), .rd_2(mem_rd), .WE(stop));  // open: JMP, JR, SignedExt, BGTZ, LB, Beq, Bne, AluSrcB, out_23, out_24, out_25, out_26, out_27, out_29, out_30, out_35, clear
  // Mips_Probe mips_probe_4: pin names not known; wires that end beside it: ex_mem_1_ir_2
  Counter #(.width(16), .max('hffff), .ongoal("wrap"), .trigger("rising"), .behavior("old")) counter_2 (
    .count(or_5_out), .Q(\条件分支成功数 ), .clk(CLK));  // open: load, D, carry, clr, preset
  or or_5 (or_5_out, beq_bne_suc, bgtz_suc);
  Counter #(.width(16), .max('hffff), .ongoal("wrap"), .trigger("rising"), .behavior("old")) counter_3 (
    .count(or_6_out), .Q(\无条件分支数 ), .clk(CLK));  // open: load, D, carry, clr, preset
  or or_6 (or_6_out, ex_JMP, ex_JR, ex_JAL);
  RAM #(.addrWidth(10), .dataWidth(32), .bus("separate"), .Select("high")) ram_1 (
    .addr(ex_mem_1_alu_2[11:2]), .din(MDin), .data(ram_1_data), .str(MemWrite), .clk(CLK));  // open: sel, ld, clr
  MEM_WB mem_wb_1 (
    .IR(ex_mem_1_ir_2), .PC(M_PC), .ALU(ex_mem_1_alu_2), .MD(ram_1_data), .MemToReg(ex_mem_1_out_32),
    .IR_2(mem_wb_1_ir_2), .PC_2(WB_PC), .ALU_2(mem_wb_1_alu_2), .MD_2(mem_wb_1_md_2),
    .out_23(mem_wb_1_out_23), .CLK(CLK), .Regwrite(mem_regwrite), .out_21(RegWrite), .rd(mem_rd),
    .rd_2(mem_wb_1_rd_2), .RegDst(ex_mem_1_out_39), .out_18(mem_wb_1_out_18), .WE(stop),
    .jal(ex_mem_1_out_37), .out_17(mem_wb_1_out_17), .pause(ex_mem_1_out_40), .out_15(WB_pause));  // open: CLEAR
  // Mips_Probe mips_probe_5: pin names not known; wires that end beside it: mem_wb_1_ir_2
  Multiplexer #(.select(1), .width(32), .disabled("Z"), .enable("false")) multiplexer_9 (
    .in0(mem_wb_1_alu_2), .in1(mem_wb_1_md_2), .out(multiplexer_9_out), .sel(mem_wb_1_out_23));
  Multiplexer #(.select(1), .width(32), .disabled("Z"), .enable("false")) multiplexer_10 (
    .in0(multiplexer_9_out), .in1(adder_4_out), .out(RDin), .sel(mem_wb_1_out_17));
  Adder #(.width(32)) adder_4 (.a(WB_PC), .b(32'h4), .out(adder_4_out));  // open: cin, cout
  Multiplexer #(.select(1), .width(5), .disabled("Z"), .enable("false")) multiplexer_11 (
    .in0(mem_wb_1_ir_2[20:16]), .in1(mem_wb_1_rd_2), .out(multiplexer_11_out), .sel(mem_wb_1_out_18));
  Multiplexer #(.select(1), .width(5), .disabled("Z"), .enable("false")) multiplexer_12 (
    .in0(multiplexer_11_out), .in1({5{1'b1}}), .out(multiplexer_12_out), .sel(mem_wb_1_out_17));

  // Other names for the same wires on the sheet: ex_nextpc[31:28] = ex_jmppc[31:28]; IR[25:0] = address;
  //   shamt[4:0] = address[10:6]; MEM_PC[31:0] = M_PC; PC[31:0] = ID_PC

  // Notes on the sheet:
  //   中断源
  //   中断等待指示
  //   总复位信号应将除ROM以外所有存储组件全部清零
  //   IF
  //   传入的pc是下一条指令的pc地址
  //   数码管输出
  //   指令存储器
  //   数码管输出应该用寄存器锁存，否则显示数据只能一闪而过
  //   contents of rom_1 (hex, n*v repeats v):
  //   20110001 8000c05 20110001 20120002 20130003 8000c09 20110001 20120002 20130003 8000c0d 20110001
  //   20120002 20130003 8000c11 20110001 20120002 20130003 c000cb8 20100001 20110001 118fc0 112020
  //   20020022 c 118882 12200001 8000c15 112020 20020022 c 20110001 118880 112020 20020022 c 12200001
  //   8000c1f 20110001 118fc0 112020 20020022 c 1188c3 112020 20020022 c 118903 112020 20020022 c 118903
  //   112020 20020022 c 118903 112020 20020022 c 118903 112020 20020022 c 118903 112020 20020022 c 118903
  //   112020 20020022 c 118903 112020 20020022 c 20100001 109fc0 139fc3 8021 2012000c 24160003 26100001
  //   3210000f 20080008 20090001 139900 2709825 132020 20020022 c 1094022 1500fff9 22100001 2018000f
  //   2188024 108700 20080008 20090001 139902 2709825 132021 20020022 c 1094022 1500fff9 108702 2c9b022
  //   12c00001 8000c50 4020 1084027 84400 3508ffff 82021 20020022 c 2010ffff 20110000 ae300000 22100001
  //   22310004 ae300000 22100001 22310004 ae300000 22100001 22310004 ae300000 22100001 22310004 ae300000
  //   22100001 22310004 ae300000 22100001 22310004 ae300000 22100001 22310004 ae300000 22100001 22310004
  //   ae300000 22100001 22310004 ae300000 22100001 22310004 ae300000 22100001 22310004 ae300000 22100001
  //   22310004 ae300000 22100001 22310004 ae300000 22100001 22310004 ae300000 22100001 22310004 ae300000
  //   22100001 22310004 22100001 8020 2011003c 8e130000 8e340000 274402a 11000002 ae330000 ae140000
  //   2231fffc 1611fff8 102020 20020022 c 22100004 2011003c 1611fff2 20020032 c 20100000 22100001 102020
  //   20020022 c 22100002 102020 20020022 c 22100003 102020 20020022 c 22100004 102020 20020022 c 22100005
  //   102020 20020022 c 22100006 102020 20020022 c 22100007 102020 20020022 c 22100008 102020 20020022
  //   20020022 c 3e00008
  //   指令字
  //   OP
  //   Func
  //   Func
  //   rs
  //   rt
  //   rd
  //   ID
  //   流水调试日志用
  //   取非高电平表示冲突
  //   低电平表示冲突
  //   为方便自动评测，需要输出流水线各段保存的PC值，注意是PC不是PC+4，另外ID段寄存器写入信息，Mem段内存写入信息也要输出
  //   执行
  //   EX
  //   MEM
  //   WB
endmodule

module \中断按键参考电路  (
  input  \同步清零信号 ,
  output \与中断屏蔽位与 
);

  wire \_1号中断_out , and_1_out, clock_1_out, d_ff_1_q, or_1_out, or_2_out;

  Clock #(.highDuration(1), .lowDuration(1)) clock_1 (.out(clock_1_out));
  Button \_1号中断  (.out(\_1号中断_out ));
  or or_1 (or_1_out, \与中断屏蔽位与 , d_ff_1_q);
  LED #(.active("true")) \_1号中断等待指示灯  (.in(or_1_out));
  D_Flip_Flop #(.trigger("rising"), .Pre_Clr_Positions("LEGACY"), .NegatePresetClear("false"), .enable("true"), .NewFFLayout("false")) d_ff_1 (
    .clk(\_1号中断_out ), .D(1'b1), .Q(d_ff_1_q), .reset(\与中断屏蔽位与 ));  // open: Qn, preset, en
  or or_2 (or_2_out, d_ff_1_q, \与中断屏蔽位与 );
  and and_1 (and_1_out, or_2_out, ~\同步清零信号 );  // AND_Gate
  D_Flip_Flop #(.trigger("rising"), .Pre_Clr_Positions("LEGACY"), .NegatePresetClear("false"), .enable("true"), .NewFFLayout("false")) IR1 (
    .clk(clock_1_out), .D(and_1_out), .Q(\与中断屏蔽位与 ));  // open: Qn, preset, en, reset
  \单周期硬布线控制器  \u_单周期硬布线控制器_1  ();  // open: Func, OP, ALU_OP, MemToReg, MemWrite, ALU_SRC, RegWrite, SysCALL, SignedExt, RegDst, JR, JMP, Beq, JAL, Bne, BGTZ, LB

  // Notes on the sheet:
  //   中断信号采样参考电路
  //   Reset 
endmodule

module \确定pc  (
  input  equal,
  input  Beq,
  input  Bne,
  input  JR,
  input  j,
  output beq_bne_suc,
  output [1:0] out_7
);

  wire and_1_out, and_2_out, and_3_out, and_4_out, and_5_out, not_1_out, not_2_out, or_1_out, or_2_out;
  wire [1:1] or_4_out;

  or or_1 (or_1_out, Beq, Bne);
  and and_1 (and_1_out, equal, or_1_out);
  or or_2 (or_2_out, Beq, and_1_out, Bne, JR, j);
  not not_1 (not_1_out, and_1_out);
  not not_2 (not_2_out, or_2_out);
  and and_2 (and_2_out, and_1_out, Beq);
  and and_3 (and_3_out, not_1_out, Bne);
  and and_4 (and_4_out, Beq, not_1_out);
  and and_5 (and_5_out, Bne, and_1_out);
  or or_3 (beq_bne_suc, and_2_out, and_3_out);
  or or_4 (or_4_out[1], and_4_out, not_2_out, and_5_out);
  Multiplexer #(.select(4), .width(2), .disabled("Z"), .enable("false")) multiplexer_1 (
    .in1(2'b00), .in2(2'b01), .in4(2'b10), .in8(2'b11), .out(out_7), .sel({j, JR, or_4_out[1], beq_bne_suc}));  // open: in0, in3, in5, in6, in7, in9, in10, in11, in12, in13, in14, in15
endmodule

module IF_ID (
  input  yuce_suc,
  input  [31:0] IR,
  input  [31:0] PC,
  input  WE,
  input  clk,
  input  clear,
  output yuce_suc_2,
  output [31:0] IR_2,
  output [31:0] PC_2
);

  wire d_ff_1_q;

  Register #(.width(1), .trigger("rising"), .Select("low")) BHT (
    .D(yuce_suc), .en(WE), .Q(yuce_suc_2), .clk(clk), .clr(d_ff_1_q));
  Register #(.width(32), .trigger("rising"), .Select("low")) register_1 (
    .D(IR), .en(WE), .Q(IR_2), .clk(clk), .clr(d_ff_1_q));
  Register #(.width(32), .trigger("rising"), .Select("low")) register_2 (
    .D(PC), .en(WE), .Q(PC_2), .clk(clk), .clr(d_ff_1_q));
  D_Flip_Flop #(.trigger("rising"), .Pre_Clr_Positions("LEGACY"), .NegatePresetClear("false"), .enable("true"), .NewFFLayout("false")) d_ff_1 (
    .clk(clk), .D(clear), .Q(d_ff_1_q), .en(WE), .reset(d_ff_1_q));  // open: Qn, preset
endmodule

module ID_EX (
  input  yuce_suc,
  input  [4:0] shamt,
  input  [4:0] R1_num,
  input  JMP,
  input  AluSrcB,
  input  [4:0] R2_num,
  input  JR,
  input  RegWrite,
  input  [31:0] IR,
  input  syscall,
  input  JAL,
  input  BGTZ,
  input  RegDst,
  input  [31:0] PC,
  input  LB,
  input  pause,
  input  Beq,
  input  MemToReg,
  input  [31:0] A,
  input  Bne,
  input  [31:0] R2data,
  input  MemWrite,
  input  [3:0] AluOP,
  input  [31:0] IMM,
  input  [4:0] rd,
  input  clk,
  input  clear,
  input  WE,
  output yuce_suc_2,
  output [4:0] out_30,
  output [4:0] R1_num_2,
  output out_32,
  output out_33,
  output [4:0] R2_num_2,
  output out_35,
  output out_36,
  output [31:0] IR_2,
  output out_38,
  output out_39,
  output out_40,
  output out_41,
  output [31:0] PC_2,
  output out_43,
  output out_44,
  output [31:0] A_2,
  output out_46,
  output out_47,
  output out_48,
  output [31:0] R2data_2,
  output out_50,
  output [3:0] out_51,
  output [31:0] IMM_2,
  output [4:0] rd_2
);

  wire d_ff_1_q;

  Register #(.width(1), .trigger("rising"), .Select("low")) register_1 (
    .D(yuce_suc), .en(WE), .Q(yuce_suc_2), .clk(clk), .clr(d_ff_1_q));
  Register #(.width(5), .trigger("rising"), .Select("low")) register_2 (
    .D(R1_num), .en(WE), .Q(R1_num_2), .clk(clk), .clr(d_ff_1_q));
  Register #(.width(5), .trigger("rising"), .Select("low")) register_3 (
    .D(R2_num), .en(WE), .Q(R2_num_2), .clk(clk), .clr(d_ff_1_q));
  Register #(.width(32), .trigger("rising"), .Select("low")) register_4 (
    .D(IR), .en(WE), .Q(IR_2), .clk(clk), .clr(d_ff_1_q));
  Register #(.width(32), .trigger("rising"), .Select("low")) register_5 (
    .D(PC), .en(WE), .Q(PC_2), .clk(clk), .clr(d_ff_1_q));
  Register #(.width(32), .trigger("rising"), .Select("low")) register_6 (
    .D(A), .en(WE), .Q(A_2), .clk(clk), .clr(d_ff_1_q));
  Register #(.width(32), .trigger("rising"), .Select("low")) register_7 (
    .D(R2data), .en(WE), .Q(R2data_2), .clk(clk), .clr(d_ff_1_q));
  Register #(.width(32), .trigger("rising"), .Select("low")) register_8 (
    .D(IMM), .en(WE), .Q(IMM_2), .clk(clk), .clr(d_ff_1_q));
  Register #(.width(5), .trigger("rising"), .Select("low")) register_9 (
    .D(rd), .en(WE), .Q(rd_2), .clk(clk), .clr(d_ff_1_q));
  D_Flip_Flop #(.trigger("rising"), .Pre_Clr_Positions("LEGACY"), .NegatePresetClear("false"), .enable("true"), .NewFFLayout("false")) d_ff_1 (
    .clk(clk), .D(clear), .Q(d_ff_1_q), .en(WE), .reset(d_ff_1_q));  // open: Qn, preset
  Register #(.width(5), .trigger("rising"), .Select("low")) register_10 (
    .D(shamt), .Q(out_30), .clk(clk), .clr(d_ff_1_q));  // open: en
  Register #(.width(1), .trigger("rising"), .Select("low")) register_11 (
    .D(JMP), .en(WE), .Q(out_32), .clk(clk), .clr(d_ff_1_q));
  Register #(.width(1), .trigger("rising"), .Select("low")) register_12 (
    .D(JR), .en(WE), .Q(out_35), .clk(clk), .clr(d_ff_1_q));
  Register #(.width(1), .trigger("rising"), .Select("low")) register_13 (
    .D(syscall), .en(WE), .Q(out_38), .clk(clk), .clr(d_ff_1_q));
  Register #(.width(1), .trigger("rising"), .Select("low")) register_14 (
    .D(BGTZ), .en(WE), .Q(out_40), .clk(clk), .clr(d_ff_1_q));
  Register #(.width(1), .trigger("rising"), .Select("low")) register_15 (
    .D(LB), .en(WE), .Q(out_43), .clk(clk), .clr(d_ff_1_q));
  Register #(.width(1), .trigger("rising"), .Select("low")) register_16 (
    .D(Beq), .en(WE), .Q(out_46), .clk(clk), .clr(d_ff_1_q));
  Register #(.width(1), .trigger("rising"), .Select("low")) register_17 (
    .D(Bne), .en(WE), .Q(out_48), .clk(clk), .clr(d_ff_1_q));
  Register #(.width(1), .trigger("rising"), .Select("low")) register_18 (
    .D(MemWrite), .en(WE), .Q(out_50), .clk(clk), .clr(d_ff_1_q));
  Register #(.width(4), .trigger("rising"), .Select("low")) register_19 (
    .D(AluOP), .en(WE), .Q(out_51), .clk(clk), .clr(d_ff_1_q));
  Register #(.width(1), .trigger("rising"), .Select("low")) register_20 (
    .D(AluSrcB), .en(WE), .Q(out_33), .clk(clk), .clr(d_ff_1_q));
  Register #(.width(1), .trigger("rising"), .Select("low")) register_21 (
    .D(RegWrite), .en(WE), .Q(out_36), .clk(clk), .clr(d_ff_1_q));
  Register #(.width(1), .trigger("rising"), .Select("low")) register_22 (
    .D(JAL), .en(WE), .Q(out_39), .clk(clk), .clr(d_ff_1_q));
  Register #(.width(1), .trigger("rising"), .Select("low")) register_23 (
    .D(RegDst), .en(WE), .Q(out_41), .clk(clk), .clr(d_ff_1_q));
  Register #(.width(1), .trigger("rising"), .Select("low")) register_24 (
    .D(pause), .en(WE), .Q(out_44), .clk(clk), .clr(d_ff_1_q));
  Register #(.width(1), .trigger("rising"), .Select("low")) register_25 (
    .D(MemToReg), .en(WE), .Q(out_47), .clk(clk), .clr(d_ff_1_q));
endmodule

module EX_MEM (
  input  JMP,
  input  JR,
  input  SignedExt,
  input  BGTZ,
  input  LB,
  input  [31:0] IR,
  input  Beq,
  input  Bne,
  input  [31:0] PC,
  input  MemToReg,
  input  MemWrite,
  input  [31:0] R2Data,
  input  AluSrcB,
  input  RegWrite,
  input  JAL,
  input  [31:0] ALU,
  input  RegDst,
  input  pause,
  input  [4:0] rd,
  input  WE,
  input  clk,
  input  clear,
  output out_23,
  output out_24,
  output out_25,
  output out_26,
  output out_27,
  output [31:0] IR_2,
  output out_29,
  output out_30,
  output [31:0] PC_2,
  output out_32,
  output out_33,
  output [31:0] R2data_2,
  output out_35,
  output out_36,
  output out_37,
  output [31:0] ALU_2,
  output out_39,
  output out_40,
  output [4:0] rd_2
);

  wire d_ff_1_q;

  Register #(.width(32), .trigger("rising"), .Select("low")) register_1 (
    .D(IR), .en(WE), .Q(IR_2), .clk(clk), .clr(d_ff_1_q));
  Register #(.width(32), .trigger("rising"), .Select("low")) register_2 (
    .D(PC), .en(WE), .Q(PC_2), .clk(clk), .clr(d_ff_1_q));
  Register #(.width(32), .trigger("rising"), .Select("low")) register_3 (
    .D(R2Data), .en(WE), .Q(R2data_2), .clk(clk), .clr(d_ff_1_q));
  Register #(.width(32), .trigger("rising"), .Select("low")) register_4 (
    .D(ALU), .en(WE), .Q(ALU_2), .clk(clk), .clr(d_ff_1_q));
  Register #(.width(5), .trigger("rising"), .Select("low")) register_5 (
    .D(rd), .en(WE), .Q(rd_2), .clk(clk), .clr(d_ff_1_q));
  Register #(.width(1), .trigger("rising"), .Select("low")) register_6 (
    .D(JMP), .en(WE), .Q(out_23), .clk(clk), .clr(d_ff_1_q));
  Register #(.width(1), .trigger("rising"), .Select("low")) register_7 (
    .D(JR), .en(WE), .Q(out_24), .clk(clk), .clr(d_ff_1_q));
  Register #(.width(1), .trigger("rising"), .Select("low")) register_8 (
    .D(SignedExt), .en(WE), .Q(out_25), .clk(clk), .clr(d_ff_1_q));
  Register #(.width(1), .trigger("rising"), .Select("low")) register_9 (
    .D(BGTZ), .en(WE), .Q(out_26), .clk(clk), .clr(d_ff_1_q));
  Register #(.width(1), .trigger("rising"), .Select("low")) register_10 (
    .D(LB), .en(WE), .Q(out_27), .clk(clk), .clr(d_ff_1_q));
  Register #(.width(1), .trigger("rising"), .Select("low")) register_11 (
    .D(Beq), .en(WE), .Q(out_29), .clk(clk), .clr(d_ff_1_q));
  Register #(.width(1), .trigger("rising"), .Select("low")) register_12 (
    .D(Bne), .en(WE), .Q(out_30), .clk(clk), .clr(d_ff_1_q));
  Register #(.width(1), .trigger("rising"), .Select("low")) register_13 (
    .D(MemToReg), .en(WE), .Q(out_32), .clk(clk), .clr(d_ff_1_q));
  Register #(.width(1), .trigger("rising"), .Select("low")) register_14 (
    .D(MemWrite), .en(WE), .Q(out_33), .clk(clk), .clr(d_ff_1_q));
  Register #(.width(1), .trigger("rising"), .Select("low")) register_15 (
    .D(AluSrcB), .en(WE), .Q(out_35), .clk(clk), .clr(d_ff_1_q));
  Register #(.width(1), .trigger("rising"), .Select("low")) register_16 (
    .D(RegWrite), .en(WE), .Q(out_36), .clk(clk), .clr(d_ff_1_q));
  Register #(.width(1), .trigger("rising"), .Select("low")) register_17 (
    .D(JAL), .en(WE), .Q(out_37), .clk(clk), .clr(d_ff_1_q));
  Register #(.width(1), .trigger("rising"), .Select("low")) register_18 (
    .D(RegDst), .en(WE), .Q(out_39), .clk(clk), .clr(d_ff_1_q));
  Register #(.width(1), .trigger("rising"), .Select("low")) register_19 (
    .D(pause), .en(WE), .Q(out_40), .clk(clk), .clr(d_ff_1_q));
  D_Flip_Flop #(.trigger("rising"), .Pre_Clr_Positions("LEGACY"), .NegatePresetClear("false"), .enable("true"), .NewFFLayout("false")) d_ff_1 (
    .clk(clk), .D(clear), .Q(d_ff_1_q), .en(WE), .reset(d_ff_1_q));  // open: Qn, preset
endmodule
// MemToReg
module MEM_WB (
  input  [31:0] IR,
  input  pause,
  input  [31:0] PC,
  input  jal,
  input  RegDst,
  input  [31:0] ALU,
  input  [4:0] rd,
  input  Regwrite,
  input  [31:0] MD,
  input  MemToReg,
  input  CLK,
  input  CLEAR,
  input  WE,
  output [31:0] IR_2,
  output out_15,
  output [31:0] PC_2,
  output out_17,
  output out_18,
  output [31:0] ALU_2,
  output [4:0] rd_2,
  output out_21,
  output [31:0] MD_2,
  output out_23
);

  wire d_ff_1_q;

  Register #(.width(32), .trigger("rising"), .Select("low")) register_1 (
    .D(IR), .en(WE), .Q(IR_2), .clk(CLK), .clr(d_ff_1_q));
  Register #(.width(32), .trigger("rising"), .Select("low")) register_2 (
    .D(PC), .en(WE), .Q(PC_2), .clk(CLK), .clr(d_ff_1_q));
  Register #(.width(32), .trigger("rising"), .Select("low")) register_3 (
    .D(ALU), .en(WE), .Q(ALU_2), .clk(CLK), .clr(d_ff_1_q));
  Register #(.width(32), .trigger("rising"), .Select("low")) register_4 (
    .D(MD), .en(WE), .Q(MD_2), .clk(CLK), .clr(d_ff_1_q));
  D_Flip_Flop #(.trigger("rising"), .Pre_Clr_Positions("LEGACY"), .NegatePresetClear("false"), .enable("true"), .NewFFLayout("false")) d_ff_1 (
    .clk(CLK), .D(CLEAR), .Q(d_ff_1_q), .en(WE), .reset(d_ff_1_q));  // open: Qn, preset
  Register #(.width(1), .trigger("rising"), .Select("low")) register_5 (
    .D(pause), .en(WE), .Q(out_15), .clk(CLK), .clr(d_ff_1_q));
  Register #(.width(1), .trigger("rising"), .Select("low")) register_6 (
    .D(jal), .en(WE), .Q(out_17), .clk(CLK), .clr(d_ff_1_q));
  Register #(.width(1), .trigger("rising"), .Select("low")) register_7 (
    .D(RegDst), .en(WE), .Q(out_18), .clk(CLK), .clr(d_ff_1_q));
  Register #(.width(5), .trigger("rising"), .Select("low")) register_8 (
    .D(rd), .en(WE), .Q(rd_2), .clk(CLK), .clr(d_ff_1_q));
  Register #(.width(1), .trigger("rising"), .Select("low")) register_9 (
    .D(Regwrite), .en(WE), .Q(out_21), .clk(CLK), .clr(d_ff_1_q));
  Register #(.width(1), .trigger("rising"), .Select("low")) register_10 (
    .D(MemToReg), .en(WE), .Q(out_23), .clk(CLK), .clr(d_ff_1_q));
endmodule

module \寄存器使用情况  (
  input  [5:0] op,
  input  [5:0] func,
  output R1_used,
  output R2_used
);

  \寄存器使用情况自动生成  \u_寄存器使用情况自动生成_1  (
    .OP0(op[0]), .OP1(op[1]), .OP2(op[2]), .OP3(op[3]), .OP4(op[4]), .OP5(op[5]), .F0(func[0]), .F1(func[1]),
    .F2(func[2]), .F3(func[3]), .F4(func[4]), .F5(func[5]), .R1_Used(R1_used), .R2_Used(R2_used));
endmodule

module \寄存器使用情况自动生成  (
  input  OP0,
  input  OP1,
  input  OP2,
  input  OP3,
  input  OP4,
  input  OP5,
  input  F0,
  input  F1,
  input  F2,
  input  F3,
  input  F4,
  input  F5,
  output R1_Used,
  output R2_Used
);

  wire and_1_out, and_2_out, and_3_out, and_4_out, and_5_out, and_6_out, and_7_out, and_8_out, and_9_out,
       and_10_out, and_11_out, and_12_out, and_13_out, and_14_out, and_15_out, and_16_out, and_17_out,
       and_18_out, and_19_out, and_20_out, and_21_out, and_22_out, and_23_out, and_24_out, and_25_out,
       and_26_out, and_27_out, and_28_out, and_29_out, and_30_out, and_31_out, and_32_out, and_33_out,
       and_34_out, and_35_out, and_36_out, and_37_out, and_38_out, and_39_out, and_40_out, not_1_out,
       not_2_out, not_3_out, not_4_out, not_5_out, not_6_out, not_7_out, not_8_out, not_9_out, not_10_out,
       not_11_out, not_12_out, not_13_out, not_14_out, not_15_out, not_16_out, not_17_out, not_18_out,
       not_19_out, not_20_out, not_21_out, not_22_out, not_23_out, not_24_out, not_25_out, not_26_out,
       not_27_out, not_28_out, not_29_out, not_30_out, not_31_out, not_32_out, not_33_out, not_34_out,
       not_35_out, not_36_out, not_37_out, not_38_out, not_39_out, not_40_out, not_41_out, not_42_out,
       not_43_out, not_44_out, not_45_out, not_46_out, not_47_out, not_48_out, not_49_out, not_50_out,
       not_51_out, not_52_out, not_53_out, not_54_out, not_55_out, not_56_out, not_57_out, not_58_out,
       not_59_out, not_60_out, not_61_out, not_62_out, not_63_out, not_64_out, not_65_out, not_66_out,
       not_67_out, not_68_out, not_69_out, not_70_out, not_71_out, not_72_out, not_73_out, not_74_out,
       not_75_out, not_76_out, not_77_out, not_78_out, not_79_out, not_80_out, not_81_out, not_82_out,
       not_83_out, not_84_out, not_85_out, not_86_out, not_87_out, not_88_out, not_89_out, not_90_out,
       not_91_out, not_92_out, not_93_out, not_94_out, not_95_out, not_96_out, not_97_out, not_98_out,
       not_99_out, not_100_out, not_101_out, not_102_out, not_103_out, not_104_out, not_105_out, not_106_out,
       not_107_out, not_108_out, not_109_out, not_110_out, not_111_out, not_112_out, not_113_out,
       not_114_out, not_115_out, not_116_out, not_117_out, not_118_out, not_119_out, not_120_out,
       not_121_out, not_122_out, not_123_out, not_124_out, not_125_out, not_126_out, not_127_out,
       not_128_out, not_129_out, not_130_out, not_131_out, not_132_out, not_133_out, not_134_out,
       not_135_out, not_136_out, not_137_out, not_138_out, not_139_out, not_140_out, not_141_out,
       not_142_out, not_143_out, not_144_out, not_145_out, not_146_out, not_147_out, not_148_out,
       not_149_out, not_150_out, not_151_out, not_152_out, not_153_out, not_154_out, not_155_out,
       not_156_out, not_157_out, not_158_out, not_159_out, not_160_out, not_161_out, not_162_out,
       not_163_out, not_164_out, not_165_out, not_166_out, not_167_out, not_168_out, not_169_out,
       not_170_out, not_171_out, not_172_out, not_173_out, not_174_out, not_175_out, not_176_out,
       not_177_out, not_178_out, not_179_out, not_180_out, not_181_out, not_182_out, not_183_out,
       not_184_out, not_185_out, not_186_out, not_187_out, not_188_out, not_189_out, not_190_out,
       not_191_out, not_192_out, not_193_out, not_194_out, not_195_out, not_196_out, not_197_out,
       not_198_out, not_199_out, not_200_out, not_201_out, not_202_out, not_203_out, not_204_out,
       not_205_out, not_206_out, not_207_out, not_208_out, not_209_out, not_210_out, not_211_out,
       not_212_out, not_213_out, not_214_out, not_215_out, not_216_out, not_217_out, not_218_out,
       not_219_out, not_220_out, not_221_out, not_222_out, not_223_out, not_224_out, not_225_out,
       not_226_out, not_227_out, not_228_out, not_229_out, not_230_out, not_231_out, not_232_out,
       not_233_out, not_234_out, not_235_out, not_236_out, not_237_out, not_238_out, not_239_out,
       not_240_out, not_241_out, not_242_out, not_243_out, not_244_out, not_245_out, not_246_out,
       not_247_out, not_248_out, not_249_out, not_250_out, not_251_out, not_252_out, not_253_out,
       not_254_out, not_255_out, not_256_out, not_257_out, not_258_out, not_259_out, not_260_out,
       not_261_out, not_262_out, not_263_out, not_264_out, not_265_out, not_266_out, not_267_out,
       not_268_out, not_269_out, not_270_out, not_271_out, not_272_out, not_273_out, not_274_out,
       not_275_out, not_276_out, not_277_out, not_278_out, not_279_out, not_280_out, not_281_out,
       not_282_out, not_283_out, not_284_out, not_285_out, not_286_out, not_287_out, not_288_out,
       not_289_out, not_290_out, not_291_out, not_292_out, not_293_out;

  not not_1 (not_1_out, OP5);
  not not_2 (not_2_out, OP4);
  not not_3 (not_3_out, OP3);
  not not_4 (not_4_out, OP2);
  not not_5 (not_5_out, OP1);
  not not_6 (not_6_out, OP0);
  not not_7 (not_7_out, F4);
  not not_8 (not_8_out, F3);
  not not_9 (not_9_out, F2);
  not not_10 (not_10_out, F1);
  not not_11 (not_11_out, F0);
  not not_12 (not_12_out, OP5);
  not not_13 (not_13_out, OP4);
  not not_14 (not_14_out, OP3);
  not not_15 (not_15_out, OP2);
  not not_16 (not_16_out, OP1);
  not not_17 (not_17_out, OP0);
  not not_18 (not_18_out, F4);
  not not_19 (not_19_out, F3);
  not not_20 (not_20_out, F2);
  not not_21 (not_21_out, F1);
  not not_22 (not_22_out, OP5);
  not not_23 (not_23_out, OP4);
  not not_24 (not_24_out, OP3);
  not not_25 (not_25_out, OP2);
  not not_26 (not_26_out, OP1);
  not not_27 (not_27_out, OP0);
  not not_28 (not_28_out, F4);
  not not_29 (not_29_out, F3);
  not not_30 (not_30_out, F2);
  not not_31 (not_31_out, F0);
  not not_32 (not_32_out, OP5);
  not not_33 (not_33_out, OP4);
  not not_34 (not_34_out, OP3);
  not not_35 (not_35_out, OP2);
  not not_36 (not_36_out, OP1);
  not not_37 (not_37_out, OP0);
  not not_38 (not_38_out, F4);
  not not_39 (not_39_out, F3);
  not not_40 (not_40_out, F1);
  not not_41 (not_41_out, F0);
  not not_42 (not_42_out, OP5);
  not not_43 (not_43_out, OP4);
  not not_44 (not_44_out, OP3);
  not not_45 (not_45_out, OP2);
  not not_46 (not_46_out, OP1);
  not not_47 (not_47_out, OP0);
  not not_48 (not_48_out, F4);
  not not_49 (not_49_out, F3);
  not not_50 (not_50_out, F1);
  not not_51 (not_51_out, OP5);
  not not_52 (not_52_out, OP4);
  not not_53 (not_53_out, OP3);
  not not_54 (not_54_out, OP2);
  not not_55 (not_55_out, OP1);
  not not_56 (not_56_out, OP0);
  not not_57 (not_57_out, F4);
  not not_58 (not_58_out, F3);
  not not_59 (not_59_out, OP5);
  not not_60 (not_60_out, OP4);
  not not_61 (not_61_out, OP3);
  not not_62 (not_62_out, OP2);
  not not_63 (not_63_out, OP1);
  not not_64 (not_64_out, OP0);
  not not_65 (not_65_out, F4);
  not not_66 (not_66_out, F2);
  not not_67 (not_67_out, F0);
  not not_68 (not_68_out, OP5);
  not not_69 (not_69_out, OP4);
  not not_70 (not_70_out, OP3);
  not not_71 (not_71_out, OP2);
  not not_72 (not_72_out, OP1);
  not not_73 (not_73_out, OP0);
  not not_74 (not_74_out, F4);
  not not_75 (not_75_out, F2);
  not not_76 (not_76_out, OP5);
  not not_77 (not_77_out, OP4);
  not not_78 (not_78_out, OP3);
  not not_79 (not_79_out, OP2);
  not not_80 (not_80_out, OP1);
  not not_81 (not_81_out, OP0);
  not not_82 (not_82_out, F5);
  not not_83 (not_83_out, F4);
  not not_84 (not_84_out, F2);
  not not_85 (not_85_out, F1);
  not not_86 (not_86_out, F0);
  not not_87 (not_87_out, OP5);
  not not_88 (not_88_out, OP4);
  not not_89 (not_89_out, OP3);
  not not_90 (not_90_out, OP2);
  not not_91 (not_91_out, OP1);
  not not_92 (not_92_out, OP0);
  not not_93 (not_93_out, F5);
  not not_94 (not_94_out, F4);
  not not_95 (not_95_out, F1);
  not not_96 (not_96_out, F0);
  not not_97 (not_97_out, OP5);
  not not_98 (not_98_out, OP4);
  not not_99 (not_99_out, OP3);
  not not_100 (not_100_out, OP1);
  not not_101 (not_101_out, OP0);
  not not_102 (not_102_out, OP5);
  not not_103 (not_103_out, OP4);
  not not_104 (not_104_out, OP3);
  not not_105 (not_105_out, OP1);
  not not_106 (not_106_out, OP5);
  not not_107 (not_107_out, OP4);
  not not_108 (not_108_out, OP2);
  not not_109 (not_109_out, OP1);
  not not_110 (not_110_out, OP0);
  not not_111 (not_111_out, OP5);
  not not_112 (not_112_out, OP4);
  not not_113 (not_113_out, OP1);
  not not_114 (not_114_out, OP0);
  not not_115 (not_115_out, OP5);
  not not_116 (not_116_out, OP4);
  not not_117 (not_117_out, OP2);
  not not_118 (not_118_out, OP1);
  not not_119 (not_119_out, OP5);
  not not_120 (not_120_out, OP4);
  not not_121 (not_121_out, OP2);
  not not_122 (not_122_out, OP0);
  not not_123 (not_123_out, OP5);
  not not_124 (not_124_out, OP4);
  not not_125 (not_125_out, OP1);
  not not_126 (not_126_out, OP4);
  not not_127 (not_127_out, OP3);
  not not_128 (not_128_out, OP2);
  not not_129 (not_129_out, OP4);
  not not_130 (not_130_out, OP2);
  not not_131 (not_131_out, OP5);
  not not_132 (not_132_out, OP4);
  not not_133 (not_133_out, OP3);
  not not_134 (not_134_out, OP2);
  not not_135 (not_135_out, OP1);
  not not_136 (not_136_out, OP0);
  not not_137 (not_137_out, F4);
  not not_138 (not_138_out, F3);
  not not_139 (not_139_out, F0);
  not not_140 (not_140_out, OP5);
  not not_141 (not_141_out, OP4);
  not not_142 (not_142_out, OP2);
  not not_143 (not_143_out, OP4);
  not not_144 (not_144_out, OP3);
  not not_145 (not_145_out, OP2);
  not not_146 (not_146_out, OP1);
  not not_147 (not_147_out, OP0);
  not not_148 (not_148_out, OP5);
  not not_149 (not_149_out, OP4);
  not not_150 (not_150_out, OP3);
  not not_151 (not_151_out, OP5);
  not not_152 (not_152_out, OP4);
  not not_153 (not_153_out, OP3);
  not not_154 (not_154_out, OP2);
  not not_155 (not_155_out, OP1);
  not not_156 (not_156_out, OP0);
  not not_157 (not_157_out, F5);
  not not_158 (not_158_out, F4);
  not not_159 (not_159_out, F3);
  not not_160 (not_160_out, F2);
  not not_161 (not_161_out, F1);
  not not_162 (not_162_out, F0);
  not not_163 (not_163_out, OP5);
  not not_164 (not_164_out, OP4);
  not not_165 (not_165_out, OP3);
  not not_166 (not_166_out, OP2);
  not not_167 (not_167_out, OP1);
  not not_168 (not_168_out, OP0);
  not not_169 (not_169_out, F5);
  not not_170 (not_170_out, F4);
  not not_171 (not_171_out, F3);
  not not_172 (not_172_out, F2);
  not not_173 (not_173_out, OP5);
  not not_174 (not_174_out, OP4);
  not not_175 (not_175_out, OP3);
  not not_176 (not_176_out, OP2);
  not not_177 (not_177_out, OP1);
  not not_178 (not_178_out, OP0);
  not not_179 (not_179_out, F5);
  not not_180 (not_180_out, F4);
  not not_181 (not_181_out, F3);
  not not_182 (not_182_out, F2);
  not not_183 (not_183_out, F0);
  not not_184 (not_184_out, OP5);
  not not_185 (not_185_out, OP4);
  not not_186 (not_186_out, OP3);
  not not_187 (not_187_out, OP2);
  not not_188 (not_188_out, OP1);
  not not_189 (not_189_out, OP0);
  not not_190 (not_190_out, F4);
  not not_191 (not_191_out, F3);
  not not_192 (not_192_out, F2);
  not not_193 (not_193_out, F1);
  not not_194 (not_194_out, F0);
  not not_195 (not_195_out, OP5);
  not not_196 (not_196_out, OP4);
  not not_197 (not_197_out, OP3);
  not not_198 (not_198_out, OP2);
  not not_199 (not_199_out, OP1);
  not not_200 (not_200_out, OP0);
  not not_201 (not_201_out, F4);
  not not_202 (not_202_out, F3);
  not not_203 (not_203_out, F2);
  not not_204 (not_204_out, F1);
  not not_205 (not_205_out, OP5);
  not not_206 (not_206_out, OP4);
  not not_207 (not_207_out, OP3);
  not not_208 (not_208_out, OP2);
  not not_209 (not_209_out, OP1);
  not not_210 (not_210_out, OP0);
  not not_211 (not_211_out, F4);
  not not_212 (not_212_out, F3);
  not not_213 (not_213_out, F2);
  not not_214 (not_214_out, F0);
  not not_215 (not_215_out, OP5);
  not not_216 (not_216_out, OP4);
  not not_217 (not_217_out, OP3);
  not not_218 (not_218_out, OP2);
  not not_219 (not_219_out, OP1);
  not not_220 (not_220_out, OP0);
  not not_221 (not_221_out, F4);
  not not_222 (not_222_out, F3);
  not not_223 (not_223_out, F1);
  not not_224 (not_224_out, F0);
  not not_225 (not_225_out, OP5);
  not not_226 (not_226_out, OP4);
  not not_227 (not_227_out, OP3);
  not not_228 (not_228_out, OP2);
  not not_229 (not_229_out, OP1);
  not not_230 (not_230_out, OP0);
  not not_231 (not_231_out, F4);
  not not_232 (not_232_out, F3);
  not not_233 (not_233_out, F1);
  not not_234 (not_234_out, OP5);
  not not_235 (not_235_out, OP4);
  not not_236 (not_236_out, OP3);
  not not_237 (not_237_out, OP2);
  not not_238 (not_238_out, OP1);
  not not_239 (not_239_out, OP0);
  not not_240 (not_240_out, F4);
  not not_241 (not_241_out, F3);
  not not_242 (not_242_out, OP5);
  not not_243 (not_243_out, OP4);
  not not_244 (not_244_out, OP3);
  not not_245 (not_245_out, OP2);
  not not_246 (not_246_out, OP1);
  not not_247 (not_247_out, OP0);
  not not_248 (not_248_out, F4);
  not not_249 (not_249_out, F2);
  not not_250 (not_250_out, F0);
  not not_251 (not_251_out, OP5);
  not not_252 (not_252_out, OP4);
  not not_253 (not_253_out, OP3);
  not not_254 (not_254_out, OP2);
  not not_255 (not_255_out, OP1);
  not not_256 (not_256_out, OP0);
  not not_257 (not_257_out, F4);
  not not_258 (not_258_out, F2);
  not not_259 (not_259_out, OP5);
  not not_260 (not_260_out, OP4);
  not not_261 (not_261_out, OP3);
  not not_262 (not_262_out, OP2);
  not not_263 (not_263_out, OP1);
  not not_264 (not_264_out, OP0);
  not not_265 (not_265_out, F5);
  not not_266 (not_266_out, F4);
  not not_267 (not_267_out, F1);
  not not_268 (not_268_out, F0);
  not not_269 (not_269_out, OP5);
  not not_270 (not_270_out, OP4);
  not not_271 (not_271_out, OP3);
  not not_272 (not_272_out, OP1);
  not not_273 (not_273_out, OP0);
  not not_274 (not_274_out, OP5);
  not not_275 (not_275_out, OP4);
  not not_276 (not_276_out, OP3);
  not not_277 (not_277_out, OP1);
  not not_278 (not_278_out, OP4);
  not not_279 (not_279_out, OP2);
  not not_280 (not_280_out, OP5);
  not not_281 (not_281_out, OP4);
  not not_282 (not_282_out, OP3);
  not not_283 (not_283_out, OP2);
  not not_284 (not_284_out, OP1);
  not not_285 (not_285_out, OP0);
  not not_286 (not_286_out, F4);
  not not_287 (not_287_out, F3);
  not not_288 (not_288_out, F0);
  not not_289 (not_289_out, OP4);
  not not_290 (not_290_out, OP3);
  not not_291 (not_291_out, OP2);
  not not_292 (not_292_out, OP1);
  not not_293 (not_293_out, OP0);
  and and_1 (and_1_out, not_1_out, not_2_out, not_3_out, not_4_out, not_5_out, not_6_out, F5, not_7_out, not_8_out, not_9_out, not_10_out, not_11_out);
  and and_2 (and_2_out, not_12_out, not_13_out, not_14_out, not_15_out, not_16_out, not_17_out, F5, not_18_out, not_19_out, not_20_out, not_21_out, F0);
  and and_3 (and_3_out, not_22_out, not_23_out, not_24_out, not_25_out, not_26_out, not_27_out, F5, not_28_out, not_29_out, not_30_out, F1, not_31_out);
  and and_4 (and_4_out, not_32_out, not_33_out, not_34_out, not_35_out, not_36_out, not_37_out, F5, not_38_out, not_39_out, F2, not_40_out, not_41_out);
  and and_5 (and_5_out, not_42_out, not_43_out, not_44_out, not_45_out, not_46_out, not_47_out, F5, not_48_out, not_49_out, F2, not_50_out, F0);
  and and_6 (and_6_out, not_51_out, not_52_out, not_53_out, not_54_out, not_55_out, not_56_out, F5, not_57_out, not_58_out, F2, F1, F0);
  and and_7 (and_7_out, not_59_out, not_60_out, not_61_out, not_62_out, not_63_out, not_64_out, F5, not_65_out, F3, not_66_out, F1, not_67_out);
  and and_8 (and_8_out, not_68_out, not_69_out, not_70_out, not_71_out, not_72_out, not_73_out, F5, not_74_out, F3, not_75_out, F1, F0);
  and and_9 (and_9_out, not_76_out, not_77_out, not_78_out, not_79_out, not_80_out, not_81_out, not_82_out, not_83_out, F3, not_84_out, not_85_out, not_86_out);
  and and_10 (and_10_out, not_87_out, not_88_out, not_89_out, not_90_out, not_91_out, not_92_out, not_93_out, not_94_out, F3, F2, not_95_out, not_96_out);
  and and_11 (and_11_out, not_97_out, not_98_out, not_99_out, OP2, not_100_out, not_101_out);
  and and_12 (and_12_out, not_102_out, not_103_out, not_104_out, OP2, not_105_out, OP0);
  and and_13 (and_13_out, not_106_out, not_107_out, OP3, not_108_out, not_109_out, not_110_out);
  and and_14 (and_14_out, not_111_out, not_112_out, OP3, OP2, not_113_out, not_114_out);
  and and_15 (and_15_out, not_115_out, not_116_out, OP3, not_117_out, not_118_out, OP0);
  and and_16 (and_16_out, not_119_out, not_120_out, OP3, not_121_out, OP1, not_122_out);
  and and_17 (and_17_out, not_123_out, not_124_out, OP3, OP2, not_125_out, OP0);
  and and_18 (and_18_out, OP5, not_126_out, not_127_out, not_128_out, OP1, OP0);
  and and_19 (and_19_out, OP5, not_129_out, OP3, not_130_out, OP1, OP0);
  and and_20 (and_20_out, not_131_out, not_132_out, not_133_out, not_134_out, not_135_out, not_136_out, F5, not_137_out, not_138_out, F2, F1, not_139_out);
  and and_21 (and_21_out, not_140_out, not_141_out, OP3, not_142_out, OP1, OP0);
  and and_22 (and_22_out, OP5, not_143_out, not_144_out, not_145_out, not_146_out, not_147_out);
  and and_23 (and_23_out, not_148_out, not_149_out, not_150_out, OP2, OP1, OP0);
  and and_24 (and_24_out, not_151_out, not_152_out, not_153_out, not_154_out, not_155_out, not_156_out, not_157_out, not_158_out, not_159_out, not_160_out, not_161_out, not_162_out);
  and and_25 (and_25_out, not_163_out, not_164_out, not_165_out, not_166_out, not_167_out, not_168_out, not_169_out, not_170_out, not_171_out, not_172_out, F1, F0);
  and and_26 (and_26_out, not_173_out, not_174_out, not_175_out, not_176_out, not_177_out, not_178_out, not_179_out, not_180_out, not_181_out, not_182_out, F1, not_183_out);
  and and_27 (and_27_out, not_184_out, not_185_out, not_186_out, not_187_out, not_188_out, not_189_out, F5, not_190_out, not_191_out, not_192_out, not_193_out, not_194_out);
  and and_28 (and_28_out, not_195_out, not_196_out, not_197_out, not_198_out, not_199_out, not_200_out, F5, not_201_out, not_202_out, not_203_out, not_204_out, F0);
  and and_29 (and_29_out, not_205_out, not_206_out, not_207_out, not_208_out, not_209_out, not_210_out, F5, not_211_out, not_212_out, not_213_out, F1, not_214_out);
  and and_30 (and_30_out, not_215_out, not_216_out, not_217_out, not_218_out, not_219_out, not_220_out, F5, not_221_out, not_222_out, F2, not_223_out, not_224_out);
  and and_31 (and_31_out, not_225_out, not_226_out, not_227_out, not_228_out, not_229_out, not_230_out, F5, not_231_out, not_232_out, F2, not_233_out, F0);
  and and_32 (and_32_out, not_234_out, not_235_out, not_236_out, not_237_out, not_238_out, not_239_out, F5, not_240_out, not_241_out, F2, F1, F0);
  and and_33 (and_33_out, not_242_out, not_243_out, not_244_out, not_245_out, not_246_out, not_247_out, F5, not_248_out, F3, not_249_out, F1, not_250_out);
  and and_34 (and_34_out, not_251_out, not_252_out, not_253_out, not_254_out, not_255_out, not_256_out, F5, not_257_out, F3, not_258_out, F1, F0);
  and and_35 (and_35_out, not_259_out, not_260_out, not_261_out, not_262_out, not_263_out, not_264_out, not_265_out, not_266_out, F3, F2, not_267_out, not_268_out);
  and and_36 (and_36_out, not_269_out, not_270_out, not_271_out, OP2, not_272_out, not_273_out);
  and and_37 (and_37_out, not_274_out, not_275_out, not_276_out, OP2, not_277_out, OP0);
  and and_38 (and_38_out, OP5, not_278_out, OP3, not_279_out, OP1, OP0);
  and and_39 (and_39_out, not_280_out, not_281_out, not_282_out, not_283_out, not_284_out, not_285_out, F5, not_286_out, not_287_out, F2, F1, not_288_out);
  and and_40 (and_40_out, OP5, not_289_out, not_290_out, not_291_out, not_292_out, not_293_out);
  or or_1 (R1_Used, and_1_out, and_2_out, and_3_out, and_4_out, and_5_out, and_6_out, and_7_out, and_8_out, and_9_out, and_10_out, and_11_out, and_12_out, and_13_out, and_14_out, and_15_out, and_16_out, and_17_out, and_18_out, and_19_out, and_20_out, and_21_out, and_22_out, and_23_out);
  or or_2 (R2_Used, and_24_out, and_25_out, and_26_out, and_27_out, and_28_out, and_29_out, and_30_out, and_31_out, and_32_out, and_33_out, and_34_out, and_35_out, and_36_out, and_37_out, and_38_out, and_39_out, and_40_out);
endmodule

module \数据相关检测逻辑子电路  (
  input  R1_Used,
  input  R2_Used,
  input  ex_MemToReg,
  input  [4:0] R1_num,
  input  [4:0] R2_num,
  input  [4:0] EX_WriteReg_num,
  input  [4:0] MEM_WriteReg_num,
  input  ex_RegWrite,
  input  mem_RegWrite,
  output LoadUse_stall,
  output stall
);

  wire and_1_out, and_2_out, and_3_out, and_4_out, and_5_out, and_6_out, comparator_1_eq, comparator_2_eq,
       comparator_3_eq, comparator_4_eq, comparator_5_eq, comparator_6_eq, not_1_out, not_2_out;

  Comparator #(.width(5), .mode("unsigned")) comparator_1 (
    .a(R1_num), .b({5{1'b0}}), .eq(comparator_1_eq));  // open: gt, lt
  Comparator #(.width(5), .mode("unsigned")) comparator_2 (
    .a(R1_num), .b(EX_WriteReg_num), .eq(comparator_2_eq));  // open: gt, lt
  Comparator #(.width(5), .mode("unsigned")) comparator_3 (
    .a(R2_num), .b({5{1'b0}}), .eq(comparator_3_eq));  // open: gt, lt
  Comparator #(.width(5), .mode("unsigned")) comparator_4 (
    .a(R2_num), .b(EX_WriteReg_num), .eq(comparator_4_eq));  // open: gt, lt
  Comparator #(.width(5), .mode("unsigned")) comparator_5 (
    .a(MEM_WriteReg_num), .b(R1_num), .eq(comparator_5_eq));  // open: gt, lt
  Comparator #(.width(5), .mode("unsigned")) comparator_6 (
    .a(MEM_WriteReg_num), .b(R2_num), .eq(comparator_6_eq));  // open: gt, lt
  not not_1 (not_1_out, comparator_1_eq);
  not not_2 (not_2_out, comparator_3_eq);
  and and_1 (and_1_out, ex_RegWrite, not_1_out, comparator_2_eq, R1_Used);
  and and_2 (and_2_out, ex_RegWrite, not_2_out, comparator_4_eq, R2_Used);
  and and_3 (and_3_out, mem_RegWrite, not_1_out, comparator_5_eq, R1_Used);
  and and_4 (and_4_out, mem_RegWrite, comparator_6_eq, not_2_out, R2_Used);
  and and_5 (and_5_out, ex_MemToReg, and_1_out);
  and and_6 (and_6_out, ex_MemToReg, and_2_out);
  nor nor_1 (stall, and_1_out, and_2_out, and_3_out, and_4_out);
  nor nor_2 (LoadUse_stall, and_5_out, and_6_out);
endmodule

module \流水线mips_regifile  (
  input  [31:0] Din,
  input  Clk,
  input  WE,
  input  [4:0] R1_num,
  input  [4:0] W_num,
  input  [4:0] R2_num,
  output [31:0] R1,
  output [31:0] R2
);

  // RegisterFile registerfile_1: pin names not known; wires that end beside it: Din, Clk, WE, W_num, R1_num, R2_num, R1, R2
endmodule

module \重定向forward  (
  input  ex_R1_used,
  input  ex_R2_used,
  input  [4:0] ex_R1_num,
  input  [4:0] ex_R2_num,
  input  [4:0] mem_rd_num,
  input  [4:0] wb_rd_num,
  input  mem_regwrite,
  input  wb_regwrite,
  output [1:0] forward_a,
  output [1:0] forward_b
);

  wire and_1_out, and_2_out, and_3_out, and_4_out, comparator_1_eq, comparator_2_eq, comparator_3_eq,
       comparator_4_eq, comparator_5_eq, comparator_6_eq, not_1_out, not_2_out;
  wire [1:0] multiplexer_2_out, multiplexer_4_out;

  Comparator #(.width(5), .mode("unsigned")) comparator_1 (
    .a(ex_R1_num), .b({5{1'b0}}), .eq(comparator_1_eq));  // open: gt, lt
  Comparator #(.width(5), .mode("unsigned")) comparator_2 (
    .a(ex_R1_num), .b(mem_rd_num), .eq(comparator_2_eq));  // open: gt, lt
  Comparator #(.width(5), .mode("unsigned")) comparator_3 (
    .a(ex_R2_num), .b({5{1'b0}}), .eq(comparator_3_eq));  // open: gt, lt
  Comparator #(.width(5), .mode("unsigned")) comparator_4 (
    .a(ex_R2_num), .b(mem_rd_num), .eq(comparator_4_eq));  // open: gt, lt
  Comparator #(.width(5), .mode("unsigned")) comparator_5 (
    .a(wb_rd_num), .b(ex_R1_num), .eq(comparator_5_eq));  // open: gt, lt
  Comparator #(.width(5), .mode("unsigned")) comparator_6 (
    .a(wb_rd_num), .b(ex_R2_num), .eq(comparator_6_eq));  // open: gt, lt
  not not_1 (not_1_out, comparator_1_eq);
  not not_2 (not_2_out, comparator_3_eq);
  and and_1 (and_1_out, mem_regwrite, not_1_out, comparator_2_eq, ex_R1_used);
  and and_2 (and_2_out, mem_regwrite, not_2_out, comparator_4_eq, ex_R2_used);
  and and_3 (and_3_out, wb_regwrite, not_1_out, comparator_5_eq, ex_R1_used);
  and and_4 (and_4_out, wb_regwrite, comparator_6_eq, not_2_out, ex_R2_used);
  Multiplexer #(.select(1), .width(2), .disabled("Z"), .enable("false")) multiplexer_1 (
    .in0(multiplexer_2_out), .in1(2'b11), .out(forward_a), .sel(and_1_out));
  Multiplexer #(.select(1), .width(2), .disabled("Z"), .enable("false")) multiplexer_2 (
    .in0(2'b00), .in1(2'b01), .out(multiplexer_2_out), .sel(and_3_out));
  Multiplexer #(.select(1), .width(2), .disabled("Z"), .enable("false")) multiplexer_3 (
    .in0(multiplexer_4_out), .in1(2'b11), .out(forward_b), .sel(and_2_out));
  Multiplexer #(.select(1), .width(2), .disabled("Z"), .enable("false")) multiplexer_4 (
    .in0(2'b00), .in1(2'b01), .out(multiplexer_4_out), .sel(and_4_out));
endmodule

module \单级中断  (
  input  \_1同步清零信号 ,
  input  clk,
  input  IR1,
  input  \_2同步清零信号 ,
  input  IR2,
  input  IR3,
  input  \_3同步清零信号 ,
  output \_1与中断屏蔽位与 ,
  output \_1号中断等待指示 ,
  output \_2与中断屏蔽位与 ,
  output \_2号中断等待指示 ,
  output \_3与中断屏蔽位与 ,
  output \_3号中断等待指示 
);

  wire and_1_out, and_2_out, and_3_out, d_ff_1_q, d_ff_2_q, d_ff_3_q, or_4_out, or_5_out, or_6_out;

  or or_1 (\_1号中断等待指示 , \_1与中断屏蔽位与 , d_ff_1_q);
  or or_2 (\_2号中断等待指示 , \_2与中断屏蔽位与 , d_ff_2_q);
  or or_3 (\_3号中断等待指示 , \_3与中断屏蔽位与 , d_ff_3_q);
  D_Flip_Flop #(.trigger("rising"), .Pre_Clr_Positions("LEGACY"), .NegatePresetClear("false"), .enable("true"), .NewFFLayout("false")) d_ff_1 (
    .clk(IR1), .D(1'b1), .Q(d_ff_1_q), .reset(\_1与中断屏蔽位与 ));  // open: Qn, preset, en
  D_Flip_Flop #(.trigger("rising"), .Pre_Clr_Positions("LEGACY"), .NegatePresetClear("false"), .enable("true"), .NewFFLayout("false")) d_ff_2 (
    .clk(IR2), .D(1'b1), .Q(d_ff_2_q), .reset(\_2与中断屏蔽位与 ));  // open: Qn, preset, en
  D_Flip_Flop #(.trigger("rising"), .Pre_Clr_Positions("LEGACY"), .NegatePresetClear("false"), .enable("true"), .NewFFLayout("false")) d_ff_3 (
    .clk(IR3), .D(1'b1), .Q(d_ff_3_q), .reset(\_3与中断屏蔽位与 ));  // open: Qn, preset, en
  Pull_Resistor #(.pull(0)) pull_resistor_1 (.node(\_1同步清零信号 ));
  or or_4 (or_4_out, d_ff_1_q, \_1与中断屏蔽位与 );
  Pull_Resistor #(.pull(0)) pull_resistor_2 (.node(\_2同步清零信号 ));
  or or_5 (or_5_out, d_ff_2_q, \_2与中断屏蔽位与 );
  or or_6 (or_6_out, d_ff_3_q, \_3与中断屏蔽位与 );
  Pull_Resistor #(.pull(0)) pull_resistor_3 (.node(\_3同步清零信号 ));
  and and_1 (and_1_out, or_4_out, ~\_1同步清零信号 );  // AND_Gate
  and and_2 (and_2_out, or_5_out, ~\_2同步清零信号 );  // AND_Gate
  and and_3 (and_3_out, or_6_out, ~\_3同步清零信号 );  // AND_Gate
  D_Flip_Flop #(.trigger("rising"), .Pre_Clr_Positions("LEGACY"), .NegatePresetClear("false"), .enable("true"), .NewFFLayout("false")) u_IR1 (
    .clk(clk), .D(and_1_out), .Q(\_1与中断屏蔽位与 ));  // open: Qn, preset, en, reset
  D_Flip_Flop #(.trigger("rising"), .Pre_Clr_Positions("LEGACY"), .NegatePresetClear("false"), .enable("true"), .NewFFLayout("false")) IR1_2 (
    .clk(clk), .D(and_2_out), .Q(\_2与中断屏蔽位与 ));  // open: Qn, preset, en, reset
  D_Flip_Flop #(.trigger("rising"), .Pre_Clr_Positions("LEGACY"), .NegatePresetClear("false"), .enable("true"), .NewFFLayout("false")) IR1_3 (
    .clk(clk), .D(and_3_out), .Q(\_3与中断屏蔽位与 ));  // open: Qn, preset, en, reset

  // Notes on the sheet:
  //   Reset 
  //   Reset 
  //   Reset 
endmodule

module \单周期MIPS_单级中断  (
  input  IR1,
  input  IR2,
  input  IR3,
  output RegWrite,
  output MemWrite,
  output [31:0] PC,
  output [31:0] IR,
  output [31:0] RDin,
  output [31:0] MDin,
  output [31:0] LedData
);

  wire _1_out, _2_out, _3_out, and_2_out, and_3_out, Beq, beq_bne_suc, BGTZ, bgtz_suc, Bne, CLK,
       comparator_3_eq, comparator_4_eq, comparator_5_eq, comparator_6_eq, comparator_7_eq,
       demultiplexer_1_out1, demultiplexer_1_out2, demultiplexer_1_out3, equal, ERET, Go, interrupt, IR1_t,
       IR2_t, IR3_t, IRA, IRB, IRC, isI, isJ, isRTYPE, JAL, JMP, JR, LB, not_1_out, not_2_out, not_4_out,
       not_5_out, or_1_out, or_6_out, or_7_out, or_8_out, or_9_out, pause, priority_encoder_1_gs, SignedExt,
       stop, Syscall, W1, W2, W3, \为0表示开中断_q , \单周期硬布线控制器_1_alu_src , \单周期硬布线控制器_1_memtoreg ,
       \单周期硬布线控制器_1_regdst , \单级中断_1__1与中断屏蔽位与 , \单级中断_1__2与中断屏蔽位与 , \单级中断_1__3与中断屏蔽位与 ;
  wire [1:0] index, interrupt_addr_index, register_2_q, \确定pc_1_out_7 ;
  wire [3:0] \单周期硬布线控制器_1_alu_op ;
  wire [4:0] multiplexer_5_out, multiplexer_6_out, multiplexer_7_out, multiplexer_8_out, multiplexer_12_out;
  wire [7:0] LBans;
  wire [15:0] \总周期数 , \无条件分支数 , \条件分支成功数 ;
  wire [27:0] nextpc;
  wire [31:0] bit_extender_1_out, bit_extender_2_out, EPC, interrupt_addr, multiplexer_1_out,
       multiplexer_2_out, multiplexer_3_out, multiplexer_4_out, multiplexer_10_out, multiplexer_11_out,
       multiplexer_14_out, pcbranch, R1data, ram_1_data, shifter_1_out;
  wire [31:2] mips_alu_1_result;
  wire [31:28] jmppc;

  Clock #(.highDuration(1), .lowDuration(1)) clock_1 (.out(CLK));
  Button _1 (.out(_1_out));
  Button _2 (.out(_2_out));
  Button _3 (.out(_3_out));
  Button \u_继续运行  (.out(Go));
  LED #(.active("true")) led_1 (.in(W1));
  LED #(.active("true")) led_2 (.in(W2));
  LED #(.active("true")) led_3 (.in(W3));
  or or_1 (or_1_out, JMP, JAL);
  Hex_Digit_Display hex_digit_display_1 (.value(LedData[31:28]));  // open: dp
  \确定pc  \u_确定pc_1  (
    .equal(equal), .Beq(Beq), .Bne(Bne), .JR(JR), .j(or_1_out), .out_7(\确定pc_1_out_7 ),
    .beq_bne_suc(beq_bne_suc));
  Multiplexer #(.select(2), .width(32), .disabled("Z"), .enable("false")) multiplexer_1 (
    .in0(pcbranch), .in1({jmppc, nextpc}), .in2(R1data), .in3({jmppc, IR[25:0], 2'b00}),
    .out(multiplexer_1_out), .sel(\确定pc_1_out_7 ));
  Hex_Digit_Display hex_digit_display_2 (.value(LedData[23:20]));  // open: dp
  Hex_Digit_Display hex_digit_display_3 (.value(LedData[27:24]));  // open: dp
  not not_1 (not_1_out, RDin[0]);
  and and_1 (bgtz_suc, BGTZ, not_1_out);
  Multiplexer #(.select(1), .width(32), .disabled("Z"), .enable("false")) multiplexer_2 (
    .in0(multiplexer_1_out), .in1(pcbranch), .out(multiplexer_2_out), .sel(bgtz_suc));
  Hex_Digit_Display hex_digit_display_4 (.value(LedData[15:12]));  // open: dp
  Hex_Digit_Display hex_digit_display_5 (.value(LedData[19:16]));  // open: dp
  Multiplexer #(.select(1), .width(32), .disabled("Z"), .enable("false")) multiplexer_3 (
    .in0(multiplexer_2_out), .in1(interrupt_addr), .out(multiplexer_3_out), .sel(interrupt));
  Hex_Digit_Display hex_digit_display_6 (.value(LedData[7:4]));  // open: dp
  Hex_Digit_Display hex_digit_display_7 (.value(LedData[11:8]));  // open: dp
  // Probe on \总周期数 
  Multiplexer #(.select(1), .width(32), .disabled("Z"), .enable("false")) multiplexer_4 (
    .in0(multiplexer_3_out), .in1(EPC), .out(multiplexer_4_out), .sel(ERET));
  D_Flip_Flop #(.trigger("falling"), .Pre_Clr_Positions("ABOVE_BELOW"), .NegatePresetClear("false"), .enable("false"), .NewFFLayout("true")) d_ff_1 (
    .clk(CLK), .D(pause), .Qn(stop), .reset(Go));  // open: Q, preset
  Hex_Digit_Display hex_digit_display_8 (.value(LedData[3:0]));  // open: dp
  Register #(.width(32), .trigger("rising"), .Select("low")) u_EPC (
    .D(multiplexer_2_out), .en(interrupt), .Q(EPC), .clk(CLK));  // open: clr
  Register #(.width(32), .trigger("rising"), .Select("low")) u_PC (
    .D(multiplexer_4_out), .en(stop), .Q(PC), .clk(CLK));  // open: clr
  or or_2 (IR1_t, IR1, IRA);
  Comparator #(.width(6), .mode("unsigned")) comparator_1 (.a(6'b010000), .b(IR[31:26]), .eq(ERET));  // open: gt, lt
  Adder #(.width(32)) adder_1 (.a(PC), .b(32'h4), .out({jmppc, nextpc}));  // open: cin, cout
  or or_3 (IR2_t, IR2, IRB);
  Counter #(.width(16), .max('hffff), .ongoal("wrap"), .trigger("rising"), .behavior("new")) counter_1 (
    .count(stop), .Q(\总周期数 ), .clk(CLK));  // open: load, D, carry, clr, preset, down
  Comparator #(.width(6), .mode("unsigned")) comparator_2 (.a({6{1'b0}}), .b(IR[31:26]), .eq(isRTYPE));  // open: gt, lt
  ROM #(.addrWidth(10), .dataWidth(32), .Select("high")) rom_1 (.addr(PC[11:2]), .data(IR));
  or or_4 (IR3_t, IR3, IRC);
  // Mips_Probe mips_probe_1: pin names not known; wires that end beside it: IR
  \单周期硬布线控制器  \u_单周期硬布线控制器_1  (
    .Func(IR[5:0]), .OP(IR[31:26]), .ALU_OP(\单周期硬布线控制器_1_alu_op ), .MemToReg(\单周期硬布线控制器_1_memtoreg ),
    .MemWrite(MemWrite), .ALU_SRC(\单周期硬布线控制器_1_alu_src ), .RegWrite(RegWrite), .SysCALL(Syscall),
    .SignedExt(SignedExt), .RegDst(\单周期硬布线控制器_1_regdst ), .JR(JR), .JMP(JMP), .Beq(Beq), .JAL(JAL),
    .Bne(Bne), .BGTZ(BGTZ), .LB(LB));
  Multiplexer #(.select(1), .width(5), .disabled("Z"), .enable("false")) multiplexer_5 (
    .in0(IR[20:16]), .in1(IR[15:11]), .out(multiplexer_5_out), .sel(\单周期硬布线控制器_1_regdst ));
  and and_2 (and_2_out, SignedExt, IR[15]);
  Multiplexer #(.select(1), .width(5), .disabled("Z"), .enable("false")) multiplexer_6 (
    .in0(IR[25:21]), .in1(5'b00100), .out(multiplexer_6_out), .sel(Syscall));
  Multiplexer #(.select(1), .width(5), .disabled("Z"), .enable("false")) multiplexer_7 (
    .in0(IR[20:16]), .in1(5'b00010), .out(multiplexer_7_out), .sel(Syscall));
  Multiplexer #(.select(1), .width(5), .disabled("Z"), .enable("false")) multiplexer_8 (
    .in0(multiplexer_5_out), .in1({5{1'b1}}), .out(multiplexer_8_out), .sel(JAL));
  assign bit_extender_1_out = {{16{and_2_out}}, IR[15:0]};  // Bit_Extender bit_extender_1
  Multiplexer #(.select(1), .width(32), .disabled("Z"), .enable("false")) multiplexer_9 (
    .in0(multiplexer_11_out), .in1({jmppc, nextpc}), .out(RDin), .sel(JAL));
  Comparator #(.width(32), .mode("unsigned")) comparator_3 (
    .a(MDin), .b(32'h22), .eq(comparator_3_eq));  // open: gt, lt
  not not_2 (not_2_out, comparator_3_eq);
  MIPS_Regifile mips_regifile_1 (
    .Din(RDin), .Clk(CLK), .R1(R1data), .R2(MDin), .WE(RegWrite), .W_num(multiplexer_8_out),
    .R1_num(multiplexer_6_out), .R2_num(multiplexer_7_out));
  Multiplexer #(.select(1), .width(32), .disabled("Z"), .enable("false")) multiplexer_10 (
    .in0(MDin), .in1(bit_extender_1_out), .out(multiplexer_10_out), .sel(\单周期硬布线控制器_1_alu_src ));
  Shifter #(.width(32), .shift("ll")) shifter_1 (.in(bit_extender_1_out), .\dist (5'b00010), .out(shifter_1_out));
  Multiplexer #(.select(1), .width(32), .disabled("Z"), .enable("false")) multiplexer_11 (
    .in0(multiplexer_14_out), .in1(bit_extender_2_out), .out(multiplexer_11_out), .sel(LB));
  and and_3 (and_3_out, Syscall, comparator_3_eq);
  and and_4 (pause, Syscall, not_2_out);
  or or_5 (isJ, JMP, JAL);
  Adder #(.width(32)) adder_2 (.a(shifter_1_out), .b({jmppc, nextpc}), .out(pcbranch));  // open: cin, cout
  Register #(.width(32), .trigger("rising"), .Select("low")) register_1 (
    .D(R1data), .en(and_3_out), .Q(LedData), .clk(CLK));  // open: clr
  or or_6 (or_6_out, isJ, isRTYPE, Syscall);
  not not_3 (isI, or_6_out);
  MIPS_ALU mips_alu_1 (
    .X(R1data), .Y(multiplexer_10_out), .AluOP(\单周期硬布线控制器_1_alu_op ), .Equal(equal),
    .Result({mips_alu_1_result, index}), .shamt(multiplexer_12_out));  // open: Result_2
  Multiplexer #(.select(1), .width(5), .disabled("Z"), .enable("false")) multiplexer_12 (
    .in0({5{1'b0}}), .in1(IR[10:6]), .out(multiplexer_12_out), .sel(isRTYPE));
  assign bit_extender_2_out = {{24{multiplexer_14_out[31]}}, LBans};  // Bit_Extender bit_extender_2
  RAM #(.addrWidth(10), .dataWidth(32), .bus("separate"), .Select("high")) ram_1 (
    .addr(mips_alu_1_result[11:2]), .din(MDin), .data(ram_1_data), .str(MemWrite), .clk(CLK));  // open: sel, ld, clr
  Multiplexer #(.select(2), .width(8), .disabled("Z"), .enable("false")) multiplexer_13 (
    .in0(multiplexer_14_out[7:0]), .in1(multiplexer_14_out[15:8]), .in2(multiplexer_14_out[23:16]),
    .in3(multiplexer_14_out[31:24]), .out(LBans), .sel(index));
  Counter #(.width(16), .max('hffff), .ongoal("wrap"), .trigger("rising"), .behavior("old")) counter_2 (
    .count(or_7_out), .Q(\条件分支成功数 ), .clk(CLK));  // open: load, D, carry, clr, preset
  or or_7 (or_7_out, beq_bne_suc, bgtz_suc);
  Counter #(.width(16), .max('hffff), .ongoal("wrap"), .trigger("rising"), .behavior("old")) counter_3 (
    .count(or_8_out), .Q(\无条件分支数 ), .clk(CLK));  // open: load, D, carry, clr, preset
  or or_8 (or_8_out, JMP, JR, JAL);
  Multiplexer #(.select(1), .width(32), .disabled("Z"), .enable("false")) multiplexer_14 (
    .in0({mips_alu_1_result, index}), .in1(ram_1_data), .out(multiplexer_14_out), .sel(\单周期硬布线控制器_1_memtoreg ));
  Register #(.width(2), .trigger("rising"), .Select("low")) register_2 (
    .D(interrupt_addr_index), .en(interrupt), .Q(register_2_q), .clk(CLK));  // open: clr
  Demultiplexer #(.select(2), .width(1), .tristate("false"), .disabled("Z"), .enable("false")) demultiplexer_1 (
    .out1(demultiplexer_1_out1), .out2(demultiplexer_1_out2), .out3(demultiplexer_1_out3), .in(ERET),
    .sel(register_2_q));  // open: out0
  Comparator #(.width(16), .mode("twosComplement")) comparator_4 (
    .a(16'h23b), .b(\总周期数 ), .eq(comparator_4_eq));  // open: gt, lt
  Comparator #(.width(16), .mode("twosComplement")) comparator_5 (
    .a(\总周期数 ), .b(16'h1), .eq(comparator_5_eq));  // open: gt, lt
  Comparator #(.width(16), .mode("twosComplement")) comparator_6 (
    .a(\总周期数 ), .b(16'h4), .eq(comparator_6_eq));  // open: gt, lt
  Comparator #(.width(16), .mode("twosComplement")) comparator_7 (
    .a(\总周期数 ), .b(16'h7), .eq(comparator_7_eq));  // open: gt, lt
  \单级中断  \u_单级中断_1  (
    .\_1同步清零信号 (demultiplexer_1_out1), .clk(CLK), .IR1(IR1_t), .\_1号中断等待指示 (W1), .IR2(IR2_t),
    .\_2号中断等待指示 (W2), .IR3(IR3_t), .\_3号中断等待指示 (W3), .\_3与中断屏蔽位与 (\单级中断_1__3与中断屏蔽位与 ),
    .\_2与中断屏蔽位与 (\单级中断_1__2与中断屏蔽位与 ), .\_1与中断屏蔽位与 (\单级中断_1__1与中断屏蔽位与 ), .\_2同步清零信号 (demultiplexer_1_out2),
    .\_3同步清零信号 (demultiplexer_1_out3));
  Multiplexer #(.select(2), .width(32), .disabled("Z"), .enable("false")) multiplexer_15 (
    .in1(32'h30ac), .in2(32'h3150), .in3(32'h31f4), .out(interrupt_addr), .sel(interrupt_addr_index));  // open: in0
  or or_9 (or_9_out, comparator_4_eq, comparator_5_eq);
  assign IRA = or_9_out ? ~CLK : 1'bz;  // Controlled_Inverter controlled_inverter_1
  assign IRB = comparator_6_eq ? ~CLK : 1'bz;  // Controlled_Inverter controlled_inverter_2
  assign IRC = comparator_7_eq ? ~CLK : 1'bz;  // Controlled_Inverter controlled_inverter_3
  Register #(.width(1), .trigger("rising"), .Select("low")) \u_为0表示开中断  (
    .D(interrupt), .en(not_4_out), .Q(\为0表示开中断_q ), .clk(CLK), .clr(ERET));
  not not_4 (not_4_out, \为0表示开中断_q );
  Pull_Resistor #(.pull(0)) pull_resistor_1 (.node(IRA));
  Pull_Resistor #(.pull(0)) pull_resistor_2 (.node(IRB));
  Pull_Resistor #(.pull(0)) pull_resistor_3 (.node(IRC));
  Priority_Encoder #(.select(2), .disabled("Z")) priority_encoder_1 (
    .in1(\单级中断_1__1与中断屏蔽位与 ), .in2(\单级中断_1__2与中断屏蔽位与 ), .in3(\单级中断_1__3与中断屏蔽位与 ), .out(interrupt_addr_index),
    .gs(priority_encoder_1_gs));  // open: in0, en_out, en_in
  not not_5 (not_5_out, \为0表示开中断_q );
  and and_5 (interrupt, priority_encoder_1_gs, not_5_out);

  // Other names for the same wires on the sheet: address[25:0] = IR[25:0]; jmppc[27:2] = IR[25:0];
  //   shamt[4:0] = IR[10:6]; nextpc[31:28] = jmppc; R2data[31:0] = MDin

  // Notes on the sheet:
  //   中断源
  //   中断等待指示
  //   总复位信号应将除ROM以外所有存储组件全部清零
  //   数码管输出应该用寄存器锁存，否则显示数据只能一闪而过
  //   数码管输出
  //   指令存储器
  //   指令字
  //   contents of rom_1 (hex, n*v repeats v):
  //   201d07d0 20100001 109fc0 139fc3 8021 2012000c 24160008 26100001 3210000f 20080008 20090001 139900
  //   2709825 132020 20020022 c 1094022 1500fff9 22100001 2018000f 2188024 108700 20080008 20090001 139902
  //   2709825 132021 20020022 c 1094022 1500fff9 108702 2c9b022 12c00001 8000c07 4020 1084027 84400
  //   3508ffff 82021 20020022 c 8000c01 afa20000 23bd0004 afa40000 23bd0004 afb00000 23bd0004 afb30000
  //   23bd0004 afb40000 23bd0004 afb50000 23bd0004 afb60000 23bd0004 20160001 20140003 20150001 168020
  //   108100 2149825 132020 20020022 c 1600fffa 295a022 1680fff7 23bdfffc 8fb60000 23bdfffc 8fb50000
  //   23bdfffc 8fb40000 23bdfffc 8fb30000 23bdfffc 8fb00000 23bdfffc 8fa40000 23bdfffc 8fa20000 42000018
  //   afa20000 23bd0004 afa40000 23bd0004 afb00000 23bd0004 afb30000 23bd0004 afb40000 23bd0004 afb50000
  //   23bd0004 afb60000 23bd0004 20160002 20140003 20150001 168020 108100 2149825 132020 20020022 c
  //   1600fffa 295a022 1680fff7 23bdfffc 8fb60000 23bdfffc 8fb50000 23bdfffc 8fb40000 23bdfffc 8fb30000
  //   23bdfffc 8fb00000 23bdfffc 8fa40000 23bdfffc 8fa20000 42000018 afa20000 23bd0004 afa40000 23bd0004
  //   afb00000 23bd0004 afb30000 23bd0004 afb40000 23bd0004 afb50000 23bd0004 afb60000 23bd0004 20160003
  //   20140003 20150001 168020 108100 2149825 132020 20020022 c 1600fffa 295a022 1680fff7 23bdfffc
  //   8fb60000 23bdfffc 8fb50000 23bdfffc 8fb40000 23bdfffc 8fb30000 23bdfffc 8fb00000 23bdfffc 8fa40000
  //   23bdfffc 8fa20000 42000018
  //   rd
  //   JMP
  //   JR
  //   OP
  //   OP
  //   Func
  //   Func
  //   rs
  //   rt
  //   rd
  //   Beq
  //   Bne
  //   MemToReg
  //   MemWrite
  //   AluOP
  //   AluSrcB
  //   RegWrite
  //   JAL
  //   RegDst
  //   Syscall
  //   为方便自动评测，需要输出PC，IR，寄存器堆写如数据RDin
  //   RAM写使能MemWrite、RAM写入数据MDin等信号
  //   j型指令
  //   I型指令
  //   单级中断测试信号
  //   先断开三个按钮和IRA~IRC的连接
  //   再加入这个电路
endmodule

module \动态分支预测  (
  output RegWrite,
  output MemWrite,
  output [31:0] IF_PC,
  output [31:0] ID_PC,
  output [31:0] EX_PC,
  output [31:0] M_PC,
  output [31:0] WB_PC,
  output [31:0] RDin,
  output [31:0] MDin,
  output [31:0] LedData
);

  wire AluSrcB, and_1_out, and_4_out, and_5_out, and_6_out, Beq, beq_bne_suc, BGTZ, bgtz_suc, \bht表_1_hit ,
       Bne, CLK, comparator_1_eq, decoder_1_out2, decoder_1_out3, ex_Beq, ex_BGTZ, ex_Bne, ex_clear,
       ex_equal, ex_JAL, ex_JMP, ex_jmpsuc, ex_JR, ex_mem_1_out_32, ex_mem_1_out_37, ex_mem_1_out_39,
       ex_mem_1_out_40, ex_MemToReg, ex_regwrite, ex_Syscall, ex_yuce_suc, Go, id_ex_1_out_33,
       id_ex_1_out_41, id_ex_1_out_44, id_ex_1_out_50, id_yuce_suc, IR1, IR2, IR3, JAL, JMP, JR, LB,
       LoadUse_stall, mem_regwrite, mem_wb_1_out_17, mem_wb_1_out_18, mem_wb_1_out_23, MemToReg, MemWrite1,
       not_1_out, not_2_out, not_3_out, not_4_out, or_1_out, or_2_out, or_3_out, or_4_out, or_6_out,
       or_7_out, pause, R1_used, R2_used, RegDst, RegWrite1, RST, SignedExt, stop, Syscall, W1, W2, W3,
       WB_pause, xnor_1_out, yuce_suc, \寄存器使用情况_2_r1_used , \寄存器使用情况_2_r2_used , \无条件_suc ;
  wire [1:0] a_f, b_f, \bht表_1_fsm_out , multiplexer_1_out, \双预测位状态机_1_下一状态 , \确定pc_1_out_7 ;
  wire [3:0] AluOp, id_ex_1_out_51;
  wire [4:0] EX_R1_num, EX_R2_num, ex_rd, id_ex_1_out_30, mem_rd, mem_wb_1_rd_2, multiplexer_11_out,
       multiplexer_17_out, multiplexer_18_out, R1_num, R2_num, rd1;
  wire [5:0] id_ex_1_ir_2;
  wire [15:0] \LoadUse次数 , \总周期数 , \插入气泡数 , \无条件分支数 , \条件分支成功数 ;
  wire [25:0] address;
  wire [27:0] ex_nextpc;
  wire [31:0] adder_4_out, \bht表_1_pc_next_2 , bit_extender_1_out, clearpc, ex_mem_1_ir_2, ex_pcbranch,
       ex_R1data, ex_R2data, ex_Result, id_ex_1_a_2, id_ex_1_imm_2, id_ex_1_r2data_2, id_R1data, id_R2data,
       if_nextpc, mem_alu, mem_wb_1_alu_2, mem_wb_1_ir_2, mem_wb_1_md_2, mips_probe_1_p1, multiplexer_2_out,
       multiplexer_3_out, multiplexer_6_out, multiplexer_14_out, multiplexer_15_out, pc_in, ram_1_data,
       shifter_1_out;
  wire [31:2] ex_jmppc;
  wire [31:26] IR;

  Button \u_总复位  (.out(RST));
  Button _1 (.out(IR1));
  Button _2 (.out(IR2));
  Button _3 (.out(IR3));
  Button \u_继续运行  (.out(Go));
  LED #(.active("true")) led_1 (.in(W1));
  LED #(.active("true")) led_2 (.in(W2));
  LED #(.active("true")) led_3 (.in(W3));
  Multiplexer #(.select(1), .width(2), .disabled("Z"), .enable("false")) multiplexer_1 (
    .in0(\双预测位状态机_1_下一状态 ), .in1(2'b10), .out(multiplexer_1_out), .sel(\无条件_suc ));
  Hex_Digit_Display hex_digit_display_1 (.value(LedData[31:28]));  // open: dp
  Hex_Digit_Display hex_digit_display_2 (.value(LedData[27:24]));  // open: dp
  \BHT表  \bht表_1  (
    .clk(CLK), .PC(EX_PC), .PC_next(pc_in), .fsm_in(multiplexer_1_out), .fenzhi_write(or_1_out),
    .PC_next_2(\bht表_1_pc_next_2 ), .fsm_out(\bht表_1_fsm_out ), .hit(\bht表_1_hit ), .if_PC(IF_PC));
  or or_1 (or_1_out, ex_BGTZ, ex_Beq, ex_Bne, ex_JR, ex_JMP, ex_JAL);
  Hex_Digit_Display hex_digit_display_3 (.value(LedData[23:20]));  // open: dp
  Hex_Digit_Display hex_digit_display_4 (.value(LedData[19:16]));  // open: dp
  Decoder #(.select(2), .tristate("false"), .disabled("Z"), .enable("false")) decoder_1 (
    .out2(decoder_1_out2), .out3(decoder_1_out3), .sel(\bht表_1_fsm_out ));  // open: out0, out1
  \双预测位状态机  \u_双预测位状态机_1  (.\下一状态 (\双预测位状态机_1_下一状态 ), .\分支跳转情况 (ex_jmpsuc), .\原状态位 (\bht表_1_fsm_out ));
  Hex_Digit_Display hex_digit_display_5 (.value(LedData[15:12]));  // open: dp
  Hex_Digit_Display hex_digit_display_6 (.value(LedData[11:8]));  // open: dp
  and and_1 (and_1_out, stop, LoadUse_stall);
  D_Flip_Flop #(.trigger("falling"), .Pre_Clr_Positions("ABOVE_BELOW"), .NegatePresetClear("false"), .enable("false"), .NewFFLayout("true")) d_ff_1 (
    .clk(CLK), .D(WB_pause), .Qn(stop), .reset(Go));  // open: Q, preset
  or or_2 (or_2_out, decoder_1_out2, decoder_1_out3);
  and and_2 (yuce_suc, or_2_out, \bht表_1_hit );
  Hex_Digit_Display hex_digit_display_7 (.value(LedData[7:4]));  // open: dp
  Hex_Digit_Display hex_digit_display_8 (.value(LedData[3:0]));  // open: dp
  Clock #(.highDuration(1), .lowDuration(1)) clock_1 (.out(CLK));
  Register #(.width(32), .trigger("rising"), .Select("low")) PC (
    .D(multiplexer_2_out), .en(and_1_out), .Q(IF_PC), .clk(CLK));  // open: clr
  Multiplexer #(.select(1), .width(32), .disabled("Z"), .enable("false")) multiplexer_2 (
    .in0(multiplexer_3_out), .in1(clearpc), .out(multiplexer_2_out), .sel(ex_clear));
  Multiplexer #(.select(1), .width(32), .disabled("Z"), .enable("false")) multiplexer_3 (
    .in0(pc_in), .in1(\bht表_1_pc_next_2 ), .out(multiplexer_3_out), .sel(yuce_suc));
  Multiplexer #(.select(1), .width(32), .disabled("Z"), .enable("false")) multiplexer_4 (
    .in0(if_nextpc), .in1(clearpc), .out(pc_in), .sel(ex_jmpsuc));
  Multiplexer #(.select(1), .width(32), .disabled("Z"), .enable("false")) multiplexer_5 (
    .in0(multiplexer_6_out), .in1(ex_pcbranch), .out(clearpc), .sel(bgtz_suc));
  Multiplexer #(.select(2), .width(32), .disabled("Z"), .enable("false")) multiplexer_6 (
    .in0(ex_pcbranch), .in1({ex_jmppc[31:28], ex_nextpc}), .in2(ex_R1data), .in3({ex_jmppc, 2'b00}),
    .out(multiplexer_6_out), .sel(\确定pc_1_out_7 ));
  // Mips_Probe mips_probe_1: pin names not known; wires that end beside it: mips_probe_1_p1
  Adder #(.width(32)) adder_1 (.a(32'h4), .b(IF_PC), .out(if_nextpc));  // open: cin, cout
  or or_3 (or_3_out, ex_JMP, ex_JAL);
  or or_4 (or_4_out, or_3_out, beq_bne_suc, ex_JR);
  \确定pc  \u_确定pc_1  (
    .equal(ex_equal), .Beq(ex_Beq), .Bne(ex_Bne), .JR(ex_JR), .j(or_3_out), .out_7(\确定pc_1_out_7 ),
    .beq_bne_suc(beq_bne_suc));
  or or_5 (ex_jmpsuc, or_4_out, bgtz_suc);
  // Probe on \总周期数 
  // Probe on \无条件分支数 
  // Probe on \条件分支成功数 
  // Probe on \插入气泡数 
  // Probe on \LoadUse次数 
  ROM #(.addrWidth(10), .dataWidth(32), .Select("high")) rom_1 (.addr(IF_PC[11:2]), .data(mips_probe_1_p1));
  and and_3 (bgtz_suc, not_1_out, ex_BGTZ);
  not not_1 (not_1_out, ex_Result[0]);
  // Probe on IF_PC[11:0]
  IF_ID if_id_1 (
    .IR(mips_probe_1_p1), .PC(IF_PC), .IR_2({IR, address}), .PC_2(ID_PC), .clk(CLK), .clear(ex_clear),
    .WE(and_4_out), .yuce_suc(yuce_suc), .yuce_suc_2(id_yuce_suc));
  and and_4 (and_4_out, LoadUse_stall, stop);
  // Probe on ID_PC[11:0]
  // Probe on IF_PC[11:0]
  // Probe on ID_PC[11:0]
  // Probe on EX_PC[11:0]
  \寄存器使用情况  \u_寄存器使用情况_1  (.op(IR), .func(address[5:0]), .R1_used(R1_used), .R2_used(R2_used));
  // Mips_Probe mips_probe_2: pin names not known; wires that end beside it: {IR, address}
  // Probe on EX_PC[11:0]
  // Probe on M_PC[11:0]
  Multiplexer #(.select(1), .width(5), .disabled("Z"), .enable("false")) multiplexer_7 (
    .in0(address[20:16]), .in1(address[15:11]), .out(rd1), .sel(RegDst));
  Comparator #(.width(32), .mode("unsigned")) comparator_1 (
    .a(ex_R2data), .b(32'h22), .eq(comparator_1_eq));  // open: gt, lt
  // Probe on M_PC[11:0]
  // Probe on WB_PC[11:0]
  xnor xnor_1 (xnor_1_out, ex_yuce_suc, ex_jmpsuc);
  // Probe on WB_PC[11:0]
  \单周期硬布线控制器  \u_单周期硬布线控制器_1  (
    .Func(address[5:0]), .OP(IR), .ALU_OP(AluOp), .MemToReg(MemToReg), .MemWrite(MemWrite1),
    .ALU_SRC(AluSrcB), .RegWrite(RegWrite1), .SysCALL(Syscall), .SignedExt(SignedExt), .RegDst(RegDst),
    .JR(JR), .JMP(JMP), .Beq(Beq), .JAL(JAL), .Bne(Bne), .BGTZ(BGTZ), .LB(LB));
  Multiplexer #(.select(1), .width(5), .disabled("Z"), .enable("false")) multiplexer_8 (
    .in0(address[25:21]), .in1(5'b00100), .out(R1_num), .sel(Syscall));
  Multiplexer #(.select(1), .width(5), .disabled("Z"), .enable("false")) multiplexer_9 (
    .in0(address[20:16]), .in1(5'b00010), .out(R2_num), .sel(Syscall));
  not not_2 (not_2_out, comparator_1_eq);
  Multiplexer #(.select(1), .width(1), .disabled("Z"), .enable("false")) multiplexer_10 (
    .in0(1'b1), .in1(1'b0), .out(ex_clear), .sel(xnor_1_out));
  and and_5 (and_5_out, SignedExt, address[15]);
  and and_6 (and_6_out, ex_Syscall, comparator_1_eq);
  and and_7 (pause, ex_Syscall, not_2_out);
  \流水线mips_regifile  \u_流水线mips_regifile_1  (
    .Din(RDin), .Clk(CLK), .R1(id_R1data), .R2(id_R2data), .WE(RegWrite), .W_num(multiplexer_18_out),
    .R1_num(R1_num), .R2_num(R2_num));
  assign bit_extender_1_out = {{16{and_5_out}}, address[15:0]};  // Bit_Extender bit_extender_1
  Register #(.width(32), .trigger("rising"), .Select("low")) register_1 (
    .D(ex_R1data), .en(and_6_out), .Q(LedData), .clk(CLK));  // open: clr
  Multiplexer #(.select(1), .width(5), .disabled("Z"), .enable("false")) multiplexer_11 (
    .in0(rd1), .in1({5{1'b1}}), .out(multiplexer_11_out), .sel(JAL));
  ID_EX id_ex_1 (
    .JMP(JMP), .AluSrcB(AluSrcB), .JR(JR), .RegWrite(RegWrite1), .IR({IR, address}), .syscall(Syscall),
    .JAL(JAL), .BGTZ(BGTZ), .RegDst(RegDst), .PC(ID_PC), .pause(pause), .Beq(Beq), .A(id_R1data), .Bne(Bne),
    .R2data(id_R2data), .MemWrite(MemWrite1), .AluOP(AluOp), .IMM(bit_extender_1_out), .out_32(ex_JMP),
    .out_33(id_ex_1_out_33), .out_35(ex_JR), .out_36(ex_regwrite), .IR_2({id_ex_1_ir_2, ex_jmppc[27:2]}),
    .out_38(ex_Syscall), .out_39(ex_JAL), .out_40(ex_BGTZ), .out_41(id_ex_1_out_41), .PC_2(EX_PC),
    .out_44(id_ex_1_out_44), .A_2(id_ex_1_a_2), .out_46(ex_Beq), .out_48(ex_Bne),
    .R2data_2(id_ex_1_r2data_2), .out_50(id_ex_1_out_50), .out_51(id_ex_1_out_51), .IMM_2(id_ex_1_imm_2),
    .clk(CLK), .clear(or_6_out), .out_47(ex_MemToReg), .MemToReg(MemToReg), .shamt(address[10:6]),
    .out_30(id_ex_1_out_30), .rd(multiplexer_11_out), .rd_2(ex_rd), .WE(stop), .R1_num(R1_num),
    .R2_num(R2_num), .R1_num_2(EX_R1_num), .R2_num_2(EX_R2_num), .yuce_suc(id_yuce_suc),
    .yuce_suc_2(ex_yuce_suc));  // open: LB, out_43
  Shifter #(.width(32), .shift("ll")) shifter_1 (.in(id_ex_1_imm_2), .\dist (5'b00010), .out(shifter_1_out));
  or or_6 (or_6_out, ex_clear, not_3_out);
  not not_3 (not_3_out, LoadUse_stall);
  \数据相关检测逻辑子电路  \u_数据相关检测逻辑子电路_1  (
    .R1_num(R1_num), .R2_num(R2_num), .EX_WriteReg_num(ex_rd), .MEM_WriteReg_num(mem_rd), .R1_Used(R1_used),
    .R2_Used(R2_used), .ex_RegWrite(ex_regwrite), .mem_RegWrite(mem_regwrite), .LoadUse_stall(LoadUse_stall),
    .ex_MemToReg(ex_MemToReg));  // open: stall
  Adder #(.width(32)) adder_2 (
    .a(shifter_1_out), .b({ex_jmppc[31:28], ex_nextpc}), .out(ex_pcbranch));  // open: cin, cout
  Multiplexer #(.select(2), .width(32), .disabled("Z"), .enable("false")) multiplexer_12 (
    .in0(id_ex_1_a_2), .in1(RDin), .in2(RDin), .in3(mem_alu), .out(ex_R1data), .sel(a_f));
  Multiplexer #(.select(2), .width(32), .disabled("Z"), .enable("false")) multiplexer_13 (
    .in0(id_ex_1_r2data_2), .in1(RDin), .in2(RDin), .in3(mem_alu), .out(ex_R2data), .sel(b_f));
  Adder #(.width(32)) adder_3 (.a(EX_PC), .b(32'h4), .out({ex_jmppc[31:28], ex_nextpc}));  // open: cin, cout
  // Mips_Probe mips_probe_3: pin names not known; wires that end beside it: {id_ex_1_ir_2, ex_jmppc[27:2]}
  Multiplexer #(.select(1), .width(32), .disabled("Z"), .enable("false")) multiplexer_14 (
    .in0(ex_R2data), .in1(id_ex_1_imm_2), .out(multiplexer_14_out), .sel(id_ex_1_out_33));
  MIPS_ALU mips_alu_1 (
    .X(ex_R1data), .Y(multiplexer_14_out), .AluOP(id_ex_1_out_51), .Equal(ex_equal), .Result(ex_Result),
    .shamt(id_ex_1_out_30));  // open: Result_2
  \寄存器使用情况  \u_寄存器使用情况_2  (
    .op(id_ex_1_ir_2), .func(ex_jmppc[7:2]), .R1_used(\寄存器使用情况_2_r1_used ), .R2_used(\寄存器使用情况_2_r2_used ));
  \重定向forward  \u_重定向forward_1  (
    .ex_R1_num(EX_R1_num), .ex_R2_num(EX_R2_num), .mem_rd_num(mem_rd), .wb_rd_num(multiplexer_18_out),
    .forward_a(a_f), .forward_b(b_f), .ex_R1_used(\寄存器使用情况_2_r1_used ), .ex_R2_used(\寄存器使用情况_2_r2_used ),
    .mem_regwrite(mem_regwrite), .wb_regwrite(RegWrite));
  Counter #(.width(16), .max('hffff), .ongoal("wrap"), .trigger("rising"), .behavior("new")) counter_1 (
    .count(stop), .Q(\总周期数 ), .clk(CLK));  // open: load, D, carry, clr, preset, down
  not not_4 (not_4_out, LoadUse_stall);
  EX_MEM ex_mem_1 (
    .IR({id_ex_1_ir_2, ex_jmppc[27:2]}), .PC(EX_PC), .MemToReg(ex_MemToReg), .MemWrite(id_ex_1_out_50),
    .R2Data(ex_R2data), .RegWrite(ex_regwrite), .JAL(ex_JAL), .ALU(ex_Result), .RegDst(id_ex_1_out_41),
    .pause(id_ex_1_out_44), .IR_2(ex_mem_1_ir_2), .PC_2(M_PC), .out_32(ex_mem_1_out_32), .out_33(MemWrite),
    .R2data_2(MDin), .out_36(mem_regwrite), .out_37(ex_mem_1_out_37), .ALU_2(mem_alu),
    .out_39(ex_mem_1_out_39), .out_40(ex_mem_1_out_40), .clk(CLK), .rd(ex_rd), .rd_2(mem_rd), .WE(stop));  // open: JMP, JR, SignedExt, BGTZ, LB, Beq, Bne, AluSrcB, out_23, out_24, out_25, out_26, out_27, out_29, out_30, out_35, clear
  Counter #(.width(16), .max('hffff), .ongoal("wrap"), .trigger("rising"), .behavior("old")) counter_2 (
    .count(not_4_out), .Q(\LoadUse次数 ), .clk(CLK));  // open: load, D, carry, clr, preset
  // Mips_Probe mips_probe_4: pin names not known; wires that end beside it: ex_mem_1_ir_2
  or or_7 (or_7_out, beq_bne_suc, bgtz_suc);
  or or_8 (\无条件_suc , ex_JMP, ex_JR, ex_JAL);
  Counter #(.width(16), .max('hffff), .ongoal("wrap"), .trigger("rising"), .behavior("old")) counter_3 (
    .count(or_7_out), .Q(\条件分支成功数 ), .clk(CLK));  // open: load, D, carry, clr, preset
  Counter #(.width(16), .max('hffff), .ongoal("wrap"), .trigger("rising"), .behavior("old")) counter_4 (
    .count(\无条件_suc ), .Q(\无条件分支数 ), .clk(CLK));  // open: load, D, carry, clr, preset
  RAM #(.addrWidth(10), .dataWidth(32), .bus("separate"), .Select("high")) ram_1 (
    .addr(mem_alu[11:2]), .din(MDin), .data(ram_1_data), .str(MemWrite), .clk(CLK));  // open: sel, ld, clr
  MEM_WB mem_wb_1 (
    .IR(ex_mem_1_ir_2), .PC(M_PC), .ALU(mem_alu), .MD(ram_1_data), .MemToReg(ex_mem_1_out_32),
    .IR_2(mem_wb_1_ir_2), .PC_2(WB_PC), .ALU_2(mem_wb_1_alu_2), .MD_2(mem_wb_1_md_2),
    .out_23(mem_wb_1_out_23), .CLK(CLK), .Regwrite(mem_regwrite), .out_21(RegWrite), .rd(mem_rd),
    .rd_2(mem_wb_1_rd_2), .RegDst(ex_mem_1_out_39), .out_18(mem_wb_1_out_18), .WE(stop),
    .jal(ex_mem_1_out_37), .out_17(mem_wb_1_out_17), .pause(ex_mem_1_out_40), .out_15(WB_pause));  // open: CLEAR
  // Mips_Probe mips_probe_5: pin names not known; wires that end beside it: mem_wb_1_ir_2
  Multiplexer #(.select(1), .width(32), .disabled("Z"), .enable("false")) multiplexer_15 (
    .in0(mem_wb_1_alu_2), .in1(mem_wb_1_md_2), .out(multiplexer_15_out), .sel(mem_wb_1_out_23));
  Multiplexer #(.select(1), .width(32), .disabled("Z"), .enable("false")) multiplexer_16 (
    .in0(multiplexer_15_out), .in1(adder_4_out), .out(RDin), .sel(mem_wb_1_out_17));
  Adder #(.width(32)) adder_4 (.a(WB_PC), .b(32'h4), .out(adder_4_out));  // open: cin, cout
  Multiplexer #(.select(1), .width(5), .disabled("Z"), .enable("false")) multiplexer_17 (
    .in0(mem_wb_1_ir_2[20:16]), .in1(mem_wb_1_rd_2), .out(multiplexer_17_out), .sel(mem_wb_1_out_18));
  Multiplexer #(.select(1), .width(5), .disabled("Z"), .enable("false")) multiplexer_18 (
    .in0(multiplexer_17_out), .in1({5{1'b1}}), .out(multiplexer_18_out), .sel(mem_wb_1_out_17));

  // Other names for the same wires on the sheet: ex_nextpc[31:28] = ex_jmppc[31:28]; IR[25:0] = address;
  //   shamt[4:0] = address[10:6]; MEM_PC[31:0] = M_PC; PC[31:0] = ID_PC; wb_data[31:0] = RDin

  // Notes on the sheet:
  //   中断源
  //   中断等待指示
  //   hit且预测跳转送预测pc
  //   数码管输出
  //   IF
  //   指令存储器
  //   contents of rom_1 (hex, n*v repeats v):
  //   20110005 8100006 20110001 20120002 20130003 20140004 810000b 20110001 20120002 20130003 20140004
  //   8100010 20110001 20120002 20130003 20140004 8100015 20110001 20120002 20130003 20140004 810001a
  //   20110001 20120002 20130003 20140004 810001f 20110001 20120002 20130003 20140004 8100024 20110001
  //   20120002 20130003 20140004 8100029 20110001 20120002 20130003 20140004 2231ffff 1620ffe0 20100001
  //   201200ff 20110001 20130003 12120005 12100004 20110001 20120002 20130003 20140004 16310004 16320003
  //   20110001 20120002 20130003 c10003d 2002000a c 20100000 22100001 102020 20020022 c 3e00008
  //   指令字
  //   流水调试日志用
  //   OP
  //   Func
  //   rs
  //   rt
  //   rd
  //   ID
  //   为方便自动评测，需要输出流水线各段保存的PC值，注意是PC不是PC+4，另外ID段寄存器写入信息，Mem段内存写入信息也要输出
  //   低电平表示冲突
  //   取非高电平表示冲突
  //   执行
  //   EX
  //   MEM
  //   WB
endmodule

module \双预测位状态机  (
  input  [1:0] \原状态位 ,
  input  \分支跳转情况 ,
  output [1:0] \下一状态 
);

  wire [1:0] multiplexer_1_out, multiplexer_2_out, multiplexer_3_out, multiplexer_4_out;

  Multiplexer #(.select(1), .width(2), .disabled("Z"), .enable("false")) multiplexer_1 (
    .in0(2'b00), .in1(2'b01), .out(multiplexer_1_out), .sel(\分支跳转情况 ));
  Multiplexer #(.select(1), .width(2), .disabled("Z"), .enable("false")) multiplexer_2 (
    .in0(2'b00), .in1(2'b10), .out(multiplexer_2_out), .sel(\分支跳转情况 ));
  Multiplexer #(.select(1), .width(2), .disabled("Z"), .enable("false")) multiplexer_3 (
    .in0(2'b11), .in1(2'b10), .out(multiplexer_3_out), .sel(\分支跳转情况 ));
  Multiplexer #(.select(1), .width(2), .disabled("Z"), .enable("false")) multiplexer_4 (
    .in0(2'b00), .in1(2'b10), .out(multiplexer_4_out), .sel(\分支跳转情况 ));
  Multiplexer #(.select(2), .width(2), .disabled("Z"), .enable("false")) multiplexer_5 (
    .in0(multiplexer_1_out), .in1(multiplexer_2_out), .in2(multiplexer_3_out), .in3(multiplexer_4_out),
    .out(\下一状态 ), .sel(\原状态位 ));
endmodule

module \BHT表  (
  input  [31:0] if_PC,
  input  clk,
  input  [31:0] PC,
  input  [31:0] PC_next,
  input  [1:0] fsm_in,
  input  fenzhi_write,
  output [31:0] PC_next_2,
  output hit,
  output [1:0] fsm_out
);

  wire and_1_out, and_2_out, and_3_out, and_4_out, and_5_out, and_6_out, and_7_out, and_8_out, and_9_out,
       and_10_out, and_11_out, and_12_out, and_13_out, and_14_out, and_15_out, and_16_out, and_17_out,
       and_26_out, and_27_out, and_28_out, and_29_out, and_30_out, and_31_out, and_32_out, and_33_out,
       comparator_1_eq, comparator_2_eq, comparator_3_eq, comparator_4_eq, comparator_5_eq, comparator_6_eq,
       comparator_7_eq, comparator_8_eq, comparator_9_eq, comparator_10_eq, comparator_11_eq,
       comparator_12_eq, comparator_13_eq, comparator_14_eq, comparator_15_eq, comparator_16_eq,
       comparator_18_eq, comparator_19_eq, comparator_20_eq, comparator_21_eq, comparator_22_eq,
       comparator_23_eq, comparator_24_eq, comparator_25_eq, d_ff_1_q, d_ff_2_q, d_ff_3_q, d_ff_4_q,
       d_ff_5_q, d_ff_6_q, d_ff_7_q, d_ff_8_q, ex_hit, full, not_1_out, or_1_out, or_2_out, or_3_out,
       or_4_out, or_5_out, or_6_out, or_7_out, or_8_out, V0, V1, V2, V3, V4, V5, V6, V7, w0, w1, w2, w3, w4,
       w5, w6, w7, write0, write1, write2, write3, write4, write5, write6, write7, writeFULL0, writeFULL1,
       writeFULL2, writeFULL3, writeFULL4, writeFULL5, writeFULL6, writeFULL7;
  wire [1:0] fsm0, fsm1, fsm2, fsm3, fsm4, fsm5, fsm6, fsm7;
  wire [2:0] max_1_max_num, max_2_max_num, max_3_max_num, max_4_max_num, max_5_max_num, max_6_max_num,
       max_7_max_num;
  wire [15:0] c0, c1, c2, c3, c4, c5, c6, c7, max_1_max, max_2_max, max_3_max, max_4_max, max_5_max,
       max_6_max;
  wire [31:0] PC0, PC1, PC2, PC3, PC4, PC5, PC6, PC7, PC_next0, PC_next1, PC_next2, PC_next3, PC_next4,
       PC_next5, PC_next6, PC_next7;

  Register #(.width(1), .trigger("rising"), .Select("low")) register_1 (
    .D(1'b1), .en(w0), .Q(V0), .clk(clk));  // open: clr
  Register #(.width(1), .trigger("rising"), .Select("low")) register_2 (
    .D(1'b1), .en(w1), .Q(V1), .clk(clk));  // open: clr
  Register #(.width(1), .trigger("rising"), .Select("low")) register_3 (
    .D(1'b1), .en(w2), .Q(V2), .clk(clk));  // open: clr
  Register #(.width(1), .trigger("rising"), .Select("low")) register_4 (
    .D(1'b1), .en(w3), .Q(V3), .clk(clk));  // open: clr
  Register #(.width(1), .trigger("rising"), .Select("low")) register_5 (
    .D(1'b1), .en(w4), .Q(V4), .clk(clk));  // open: clr
  Register #(.width(1), .trigger("rising"), .Select("low")) register_6 (
    .D(1'b1), .en(w5), .Q(V5), .clk(clk));  // open: clr
  Register #(.width(1), .trigger("rising"), .Select("low")) register_7 (
    .D(1'b1), .en(w6), .Q(V6), .clk(clk));  // open: clr
  Register #(.width(1), .trigger("rising"), .Select("low")) register_8 (
    .D(1'b1), .en(w7), .Q(V7), .clk(clk));  // open: clr
  Register #(.width(32), .trigger("rising"), .Select("low")) \u_分支指令地址  (
    .D(PC), .en(w0), .Q(PC0), .clk(clk));  // open: clr
  Register #(.width(32), .trigger("rising"), .Select("low")) \u_分支指令地址_2  (
    .D(PC), .en(w1), .Q(PC1), .clk(clk));  // open: clr
  Register #(.width(32), .trigger("rising"), .Select("low")) \u_分支指令地址_3  (
    .D(PC), .en(w2), .Q(PC2), .clk(clk));  // open: clr
  Register #(.width(32), .trigger("rising"), .Select("low")) \u_分支指令地址_4  (
    .D(PC), .en(w3), .Q(PC3), .clk(clk));  // open: clr
  Register #(.width(32), .trigger("rising"), .Select("low")) \u_分支指令地址_5  (
    .D(PC), .en(w4), .Q(PC4), .clk(clk));  // open: clr
  Register #(.width(32), .trigger("rising"), .Select("low")) \u_分支指令地址_6  (
    .D(PC), .en(w5), .Q(PC5), .clk(clk));  // open: clr
  Register #(.width(32), .trigger("rising"), .Select("low")) \u_分支指令地址_7  (
    .D(PC), .en(w6), .Q(PC6), .clk(clk));  // open: clr
  Register #(.width(32), .trigger("rising"), .Select("low")) \u_分支指令地址_8  (
    .D(PC), .en(w7), .Q(PC7), .clk(clk));  // open: clr
  Register #(.width(32), .trigger("rising"), .Select("low")) \u_目标地址  (
    .D(PC_next), .en(w0), .Q(PC_next0), .clk(clk));  // open: clr
  Register #(.width(32), .trigger("rising"), .Select("low")) \u_目标地址_2  (
    .D(PC_next), .en(w1), .Q(PC_next1), .clk(clk));  // open: clr
  Register #(.width(32), .trigger("rising"), .Select("low")) \u_目标地址_3  (
    .D(PC_next), .en(w2), .Q(PC_next2), .clk(clk));  // open: clr
  Register #(.width(32), .trigger("rising"), .Select("low")) \u_目标地址_4  (
    .D(PC_next), .en(w3), .Q(PC_next3), .clk(clk));  // open: clr
  Register #(.width(32), .trigger("rising"), .Select("low")) \u_目标地址_5  (
    .D(PC_next), .en(w4), .Q(PC_next4), .clk(clk));  // open: clr
  Register #(.width(32), .trigger("rising"), .Select("low")) \u_目标地址_6  (
    .D(PC_next), .en(w5), .Q(PC_next5), .clk(clk));  // open: clr
  Register #(.width(32), .trigger("rising"), .Select("low")) \u_目标地址_7  (
    .D(PC_next), .en(w6), .Q(PC_next6), .clk(clk));  // open: clr
  Register #(.width(32), .trigger("rising"), .Select("low")) \u_目标地址_8  (
    .D(PC_next), .en(w7), .Q(PC_next7), .clk(clk));  // open: clr
  Register #(.width(2), .trigger("rising"), .Select("low")) \u_分支预测历史  (
    .D(fsm_in), .en(or_3_out), .Q(fsm0), .clk(clk));  // open: clr
  Register #(.width(2), .trigger("rising"), .Select("low")) \u_分支预测历史_2  (
    .D(fsm_in), .en(or_4_out), .Q(fsm1), .clk(clk));  // open: clr
  Register #(.width(2), .trigger("rising"), .Select("low")) \u_分支预测历史_3  (
    .D(fsm_in), .en(or_1_out), .Q(fsm2), .clk(clk));  // open: clr
  Register #(.width(2), .trigger("rising"), .Select("low")) \u_分支预测历史_4  (
    .D(fsm_in), .en(or_2_out), .Q(fsm3), .clk(clk));  // open: clr
  Register #(.width(2), .trigger("rising"), .Select("low")) \u_分支预测历史_5  (
    .D(fsm_in), .en(or_5_out), .Q(fsm4), .clk(clk));  // open: clr
  Register #(.width(2), .trigger("rising"), .Select("low")) \u_分支预测历史_6  (
    .D(fsm_in), .en(or_6_out), .Q(fsm5), .clk(clk));  // open: clr
  Register #(.width(2), .trigger("rising"), .Select("low")) \u_分支预测历史_7  (
    .D(fsm_in), .en(or_7_out), .Q(fsm6), .clk(clk));  // open: clr
  Register #(.width(2), .trigger("rising"), .Select("low")) \u_分支预测历史_8  (
    .D(fsm_in), .en(or_8_out), .Q(fsm7), .clk(clk));  // open: clr
  Counter #(.width(16), .max('hffff), .ongoal("wrap"), .trigger("rising"), .behavior("new")) counter_1 (
    .Q(c0), .clk(clk), .clr(d_ff_1_q));  // open: load, D, count, carry, preset, down
  Counter #(.width(16), .max('hffff), .ongoal("wrap"), .trigger("rising"), .behavior("new")) counter_2 (
    .Q(c1), .clk(clk), .clr(d_ff_2_q));  // open: load, D, count, carry, preset, down
  Counter #(.width(16), .max('hffff), .ongoal("wrap"), .trigger("rising"), .behavior("new")) counter_3 (
    .Q(c2), .clk(clk), .clr(d_ff_3_q));  // open: load, D, count, carry, preset, down
  Counter #(.width(16), .max('hffff), .ongoal("wrap"), .trigger("rising"), .behavior("new")) counter_4 (
    .Q(c3), .clk(clk), .clr(d_ff_4_q));  // open: load, D, count, carry, preset, down
  Counter #(.width(16), .max('hffff), .ongoal("wrap"), .trigger("rising"), .behavior("new")) counter_5 (
    .Q(c4), .clk(clk), .clr(d_ff_5_q));  // open: load, D, count, carry, preset, down
  Counter #(.width(16), .max('hffff), .ongoal("wrap"), .trigger("rising"), .behavior("new")) counter_6 (
    .Q(c5), .clk(clk), .clr(d_ff_6_q));  // open: load, D, count, carry, preset, down
  Counter #(.width(16), .max('hffff), .ongoal("wrap"), .trigger("rising"), .behavior("new")) counter_7 (
    .Q(c6), .clk(clk), .clr(d_ff_7_q));  // open: load, D, count, carry, preset, down
  Counter #(.width(16), .max('hffff), .ongoal("wrap"), .trigger("rising"), .behavior("new")) counter_8 (
    .Q(c7), .clk(clk), .clr(d_ff_8_q));  // open: load, D, count, carry, preset, down
  Comparator #(.width(32), .mode("unsigned")) comparator_1 (.a(PC0), .b(if_PC), .eq(comparator_1_eq));  // open: gt, lt
  Comparator #(.width(32), .mode("unsigned")) comparator_2 (.a(PC1), .b(if_PC), .eq(comparator_2_eq));  // open: gt, lt
  Comparator #(.width(32), .mode("unsigned")) comparator_3 (.a(PC2), .b(if_PC), .eq(comparator_3_eq));  // open: gt, lt
  Comparator #(.width(32), .mode("unsigned")) comparator_4 (.a(PC3), .b(if_PC), .eq(comparator_4_eq));  // open: gt, lt
  Comparator #(.width(32), .mode("unsigned")) comparator_5 (.a(PC4), .b(if_PC), .eq(comparator_5_eq));  // open: gt, lt
  Comparator #(.width(32), .mode("unsigned")) comparator_6 (.a(PC5), .b(if_PC), .eq(comparator_6_eq));  // open: gt, lt
  Comparator #(.width(32), .mode("unsigned")) comparator_7 (.a(PC6), .b(if_PC), .eq(comparator_7_eq));  // open: gt, lt
  Comparator #(.width(32), .mode("unsigned")) comparator_8 (.a(PC7), .b(if_PC), .eq(comparator_8_eq));  // open: gt, lt
  and and_1 (and_1_out, V0, comparator_1_eq);
  assign PC_next_2 = and_1_out ? PC_next0 : 32'bz;  // Controlled_Buffer controlled_buffer_1
  and and_2 (and_2_out, V1, comparator_2_eq);
  assign PC_next_2 = and_2_out ? PC_next1 : 32'bz;  // Controlled_Buffer controlled_buffer_2
  or or_1 (or_1_out, w2, and_3_out);
  and and_3 (and_3_out, V2, comparator_3_eq);
  assign PC_next_2 = and_3_out ? PC_next2 : 32'bz;  // Controlled_Buffer controlled_buffer_3
  or or_2 (or_2_out, w3, and_4_out);
  and and_4 (and_4_out, V3, comparator_4_eq);
  assign PC_next_2 = and_4_out ? PC_next3 : 32'bz;  // Controlled_Buffer controlled_buffer_4
  and and_5 (and_5_out, V4, comparator_5_eq);
  assign PC_next_2 = and_5_out ? PC_next4 : 32'bz;  // Controlled_Buffer controlled_buffer_5
  and and_6 (and_6_out, V5, comparator_6_eq);
  assign PC_next_2 = and_6_out ? PC_next5 : 32'bz;  // Controlled_Buffer controlled_buffer_6
  and and_7 (and_7_out, V6, comparator_7_eq);
  assign PC_next_2 = and_7_out ? PC_next6 : 32'bz;  // Controlled_Buffer controlled_buffer_7
  and and_8 (and_8_out, V7, comparator_8_eq);
  assign PC_next_2 = and_8_out ? PC_next7 : 32'bz;  // Controlled_Buffer controlled_buffer_8
  D_Flip_Flop #(.trigger("rising"), .Pre_Clr_Positions("LEGACY"), .NegatePresetClear("false"), .enable("true"), .NewFFLayout("false")) d_ff_1 (
    .clk(clk), .D(or_3_out), .Q(d_ff_1_q), .reset(d_ff_1_q));  // open: Qn, preset, en
  or or_3 (or_3_out, and_1_out, w0);
  or or_4 (or_4_out, and_2_out, w1);
  or or_5 (or_5_out, w4, and_5_out);
  or or_6 (or_6_out, w5, and_6_out);
  or or_7 (or_7_out, w6, and_7_out);
  or or_8 (or_8_out, w7, and_8_out);
  assign fsm_out = and_1_out ? fsm0 : 2'bz;  // Controlled_Buffer controlled_buffer_9
  D_Flip_Flop #(.trigger("rising"), .Pre_Clr_Positions("LEGACY"), .NegatePresetClear("false"), .enable("true"), .NewFFLayout("false")) d_ff_2 (
    .clk(clk), .D(or_4_out), .Q(d_ff_2_q), .reset(d_ff_2_q));  // open: Qn, preset, en
  assign fsm_out = and_2_out ? fsm1 : 2'bz;  // Controlled_Buffer controlled_buffer_10
  D_Flip_Flop #(.trigger("rising"), .Pre_Clr_Positions("LEGACY"), .NegatePresetClear("false"), .enable("true"), .NewFFLayout("false")) d_ff_3 (
    .clk(clk), .D(or_1_out), .Q(d_ff_3_q), .reset(d_ff_3_q));  // open: Qn, preset, en
  assign fsm_out = and_3_out ? fsm2 : 2'bz;  // Controlled_Buffer controlled_buffer_11
  D_Flip_Flop #(.trigger("rising"), .Pre_Clr_Positions("LEGACY"), .NegatePresetClear("false"), .enable("true"), .NewFFLayout("false")) d_ff_4 (
    .clk(clk), .D(or_2_out), .Q(d_ff_4_q), .reset(d_ff_4_q));  // open: Qn, preset, en
  assign fsm_out = and_4_out ? fsm3 : 2'bz;  // Controlled_Buffer controlled_buffer_12
  assign fsm_out = and_5_out ? fsm4 : 2'bz;  // Controlled_Buffer controlled_buffer_13
  assign fsm_out = and_6_out ? fsm5 : 2'bz;  // Controlled_Buffer controlled_buffer_14
  assign fsm_out = and_7_out ? fsm6 : 2'bz;  // Controlled_Buffer controlled_buffer_15
  assign fsm_out = and_8_out ? fsm7 : 2'bz;  // Controlled_Buffer controlled_buffer_16
  D_Flip_Flop #(.trigger("rising"), .Pre_Clr_Positions("LEGACY"), .NegatePresetClear("false"), .enable("true"), .NewFFLayout("false")) d_ff_5 (
    .clk(clk), .D(or_5_out), .Q(d_ff_5_q), .reset(d_ff_5_q));  // open: Qn, preset, en
  D_Flip_Flop #(.trigger("rising"), .Pre_Clr_Positions("LEGACY"), .NegatePresetClear("false"), .enable("true"), .NewFFLayout("false")) d_ff_6 (
    .clk(clk), .D(or_6_out), .Q(d_ff_6_q), .reset(d_ff_6_q));  // open: Qn, preset, en
  D_Flip_Flop #(.trigger("rising"), .Pre_Clr_Positions("LEGACY"), .NegatePresetClear("false"), .enable("true"), .NewFFLayout("false")) d_ff_7 (
    .clk(clk), .D(or_7_out), .Q(d_ff_7_q), .reset(d_ff_7_q));  // open: Qn, preset, en
  D_Flip_Flop #(.trigger("rising"), .Pre_Clr_Positions("LEGACY"), .NegatePresetClear("false"), .enable("true"), .NewFFLayout("false")) d_ff_8 (
    .clk(clk), .D(or_8_out), .Q(d_ff_8_q), .reset(d_ff_8_q));  // open: Qn, preset, en
  or or_9 (hit, and_1_out, and_2_out, and_3_out, and_4_out, and_5_out, and_6_out, and_7_out, and_8_out);
  and and_9 (and_9_out, fenzhi_write, writeFULL0);
  and and_10 (and_10_out, fenzhi_write, writeFULL1);
  and and_11 (and_11_out, fenzhi_write, writeFULL2);
  and and_12 (and_12_out, fenzhi_write, writeFULL3);
  not not_1 (not_1_out, ex_hit);
  and and_13 (and_13_out, full, not_1_out);
  Multiplexer #(.select(1), .width(1), .disabled("Z"), .enable("false")) multiplexer_1 (
    .in0(write0), .in1(and_9_out), .out(w0), .sel(and_13_out));
  Multiplexer #(.select(1), .width(1), .disabled("Z"), .enable("false")) multiplexer_2 (
    .in0(write1), .in1(and_10_out), .out(w1), .sel(and_13_out));
  Multiplexer #(.select(1), .width(1), .disabled("Z"), .enable("false")) multiplexer_3 (
    .in0(write2), .in1(and_11_out), .out(w2), .sel(and_13_out));
  Multiplexer #(.select(1), .width(1), .disabled("Z"), .enable("false")) multiplexer_4 (
    .in0(write3), .in1(and_12_out), .out(w3), .sel(and_13_out));
  max max_1 (.Y(c1), .X(c0), .Y_num(3'b001), .X_num(3'b000), .MAX(max_1_max), .MAX_num(max_1_max_num));
  max max_2 (.Y(c3), .X(c2), .Y_num(3'b011), .X_num(3'b010), .MAX(max_2_max), .MAX_num(max_2_max_num));
  max max_3 (.Y(c5), .X(c4), .Y_num(3'b101), .X_num(3'b100), .MAX(max_3_max), .MAX_num(max_3_max_num));
  max max_4 (.Y(c7), .X(c6), .Y_num(3'b111), .X_num(3'b110), .MAX(max_4_max), .MAX_num(max_4_max_num));
  max max_5 (
    .Y(max_2_max), .X(max_1_max), .Y_num(max_2_max_num), .X_num(max_1_max_num), .MAX(max_5_max),
    .MAX_num(max_5_max_num));
  max max_6 (
    .Y(max_4_max), .X(max_3_max), .Y_num(max_4_max_num), .X_num(max_3_max_num), .MAX(max_6_max),
    .MAX_num(max_6_max_num));
  and and_14 (and_14_out, fenzhi_write, writeFULL4);
  and and_15 (and_15_out, fenzhi_write, writeFULL5);
  and and_16 (and_16_out, fenzhi_write, writeFULL6);
  and and_17 (and_17_out, fenzhi_write, writeFULL7);
  Multiplexer #(.select(1), .width(1), .disabled("Z"), .enable("false")) multiplexer_5 (
    .in0(write4), .in1(and_14_out), .out(w4), .sel(and_13_out));
  Multiplexer #(.select(1), .width(1), .disabled("Z"), .enable("false")) multiplexer_6 (
    .in0(write5), .in1(and_15_out), .out(w5), .sel(and_13_out));
  Multiplexer #(.select(1), .width(1), .disabled("Z"), .enable("false")) multiplexer_7 (
    .in0(write6), .in1(and_16_out), .out(w6), .sel(and_13_out));
  Multiplexer #(.select(1), .width(1), .disabled("Z"), .enable("false")) multiplexer_8 (
    .in0(write7), .in1(and_17_out), .out(w7), .sel(and_13_out));
  Comparator #(.width(8), .mode("unsigned")) comparator_9 (
    .a({V7, V6, V5, V4, V3, V2, V1, V0}), .b({8{1'b0}}), .eq(comparator_9_eq));  // open: gt, lt
  Comparator #(.width(8), .mode("unsigned")) comparator_10 (
    .a({V7, V6, V5, V4, V3, V2, V1, V0}), .b(8'h1), .eq(comparator_10_eq));  // open: gt, lt
  Comparator #(.width(8), .mode("unsigned")) comparator_11 (
    .a({V7, V6, V5, V4, V3, V2, V1, V0}), .b(8'h3), .eq(comparator_11_eq));  // open: gt, lt
  Comparator #(.width(8), .mode("unsigned")) comparator_12 (
    .a({V7, V6, V5, V4, V3, V2, V1, V0}), .b(8'h7), .eq(comparator_12_eq));  // open: gt, lt
  Comparator #(.width(8), .mode("unsigned")) comparator_13 (
    .a({V7, V6, V5, V4, V3, V2, V1, V0}), .b(8'hf), .eq(comparator_13_eq));  // open: gt, lt
  Comparator #(.width(8), .mode("unsigned")) comparator_14 (
    .a({V7, V6, V5, V4, V3, V2, V1, V0}), .b(8'h1f), .eq(comparator_14_eq));  // open: gt, lt
  Comparator #(.width(8), .mode("unsigned")) comparator_15 (
    .a({V7, V6, V5, V4, V3, V2, V1, V0}), .b(8'h3f), .eq(comparator_15_eq));  // open: gt, lt
  Comparator #(.width(8), .mode("unsigned")) comparator_16 (
    .a({V7, V6, V5, V4, V3, V2, V1, V0}), .b(8'h7f), .eq(comparator_16_eq));  // open: gt, lt
  Comparator #(.width(8), .mode("unsigned")) comparator_17 (
    .a({V7, V6, V5, V4, V3, V2, V1, V0}), .b({8{1'b1}}), .eq(full));  // open: gt, lt
  and and_18 (write0, fenzhi_write, comparator_9_eq);
  and and_19 (write1, fenzhi_write, comparator_10_eq);
  and and_20 (write2, fenzhi_write, comparator_11_eq);
  and and_21 (write3, fenzhi_write, comparator_12_eq);
  and and_22 (write4, fenzhi_write, comparator_13_eq);
  and and_23 (write5, fenzhi_write, comparator_14_eq);
  and and_24 (write6, fenzhi_write, comparator_15_eq);
  and and_25 (write7, fenzhi_write, comparator_16_eq);
  max max_7 (
    .Y(max_6_max), .X(max_5_max), .Y_num(max_6_max_num), .X_num(max_5_max_num), .MAX_num(max_7_max_num));  // open: MAX
  Decoder #(.select(3), .tristate("false"), .disabled("Z"), .enable("false")) decoder_1 (
    .out0(writeFULL0), .out1(writeFULL1), .out2(writeFULL2), .out3(writeFULL3), .out4(writeFULL4),
    .out5(writeFULL5), .out6(writeFULL6), .out7(writeFULL7), .sel(max_7_max_num));
  Comparator #(.width(32), .mode("unsigned")) comparator_18 (.a(PC0), .b(PC), .eq(comparator_18_eq));  // open: gt, lt
  Comparator #(.width(32), .mode("unsigned")) comparator_19 (.a(PC1), .b(PC), .eq(comparator_19_eq));  // open: gt, lt
  Comparator #(.width(32), .mode("unsigned")) comparator_20 (.a(PC2), .b(PC), .eq(comparator_20_eq));  // open: gt, lt
  Comparator #(.width(32), .mode("unsigned")) comparator_21 (.a(PC3), .b(PC), .eq(comparator_21_eq));  // open: gt, lt
  Comparator #(.width(32), .mode("unsigned")) comparator_22 (.a(PC4), .b(PC), .eq(comparator_22_eq));  // open: gt, lt
  Comparator #(.width(32), .mode("unsigned")) comparator_23 (.a(PC5), .b(PC), .eq(comparator_23_eq));  // open: gt, lt
  Comparator #(.width(32), .mode("unsigned")) comparator_24 (.a(PC6), .b(PC), .eq(comparator_24_eq));  // open: gt, lt
  Comparator #(.width(32), .mode("unsigned")) comparator_25 (.a(PC7), .b(PC), .eq(comparator_25_eq));  // open: gt, lt
  and and_26 (and_26_out, V0, comparator_18_eq);
  and and_27 (and_27_out, V1, comparator_19_eq);
  and and_28 (and_28_out, V2, comparator_20_eq);
  and and_29 (and_29_out, V3, comparator_21_eq);
  and and_30 (and_30_out, V4, comparator_22_eq);
  and and_31 (and_31_out, V5, comparator_23_eq);
  and and_32 (and_32_out, V6, comparator_24_eq);
  and and_33 (and_33_out, V7, comparator_25_eq);
  or or_10 (ex_hit, and_26_out, and_27_out, and_28_out, and_29_out, and_30_out, and_31_out, and_32_out, and_33_out);

  // Other names for the same wires on the sheet: fenzhi = fenzhi_write; fsm[1:0] = fsm_out;
  //   PC_next_BHT[31:0] = PC_next_2
endmodule

module max (
  input  [15:0] Y,
  input  [15:0] X,
  input  [2:0] Y_num,
  input  [2:0] X_num,
  output [15:0] MAX,
  output [2:0] MAX_num
);

  wire comparator_1_eq, comparator_1_gt, or_1_out;

  Multiplexer #(.select(1), .width(16), .disabled("Z"), .enable("true")) multiplexer_1 (
    .in0(Y), .in1(X), .out(MAX), .sel(or_1_out), .en(1'b1));
  Comparator #(.width(16), .mode("unsigned")) comparator_1 (
    .a(X), .b(Y), .gt(comparator_1_gt), .eq(comparator_1_eq));  // open: lt
  or or_1 (or_1_out, comparator_1_gt, comparator_1_eq);
  Multiplexer #(.select(1), .width(3), .disabled("Z"), .enable("false")) multiplexer_2 (
    .in0(Y_num), .in1(X_num), .out(MAX_num), .sel(or_1_out));

  // Notes on the sheet:
  //   输出两个输入中的较大值，并输出较大值的2位编号
endmodule
